// Logisim project cMips.circ as structural Verilog: 33 circuits, main circuit main
// 1
module main (
  input  [3:0] in_1,
  input  [2:0] in_2,
  input  [2:0] in_3,
  input  [2:0] in_4,
  input  [2:0] in_5,
  input  in_6,
  input  in_7,
  output [15:0] out_8,
  output [15:0] out_9,
  output [15:0] out_10,
  output [3:0] OP,
  output [2:0] Reg1,
  output [2:0] Reg2,
  output [2:0] Reg_3,
  output [2:0] out_15,
  output [5:0] Imm,
  output [15:0] out_17,
  output [14:0] out_18,
  output [4:0] out_19,
  output [15:0] out_20,
  output [4:0] out_21,
  output [4:0] out_22,
  output [15:0] out_23,
  output [15:0] out_24,
  output [15:0] out_25,
  output [5:0] Imm_2,
  output [15:0] out_27,
  output [15:0] out_28,
  output [3:0] OP_2,
  output [2:0] Reg1_2,
  output [2:0] Reg2_2,
  output [2:0] Reg_3_2,
  output [2:0] out_33,
  output [5:0] Imm_3,
  output [2:0] out_35
);

  wire alu_1_zero, and_2_out, and_3_out, and_4_out, and_5_out, and_6_out, button_1_out, button_2_out,
       button_3_out, button_5_out, button_6_out, clock, clock_1_out, clock_2_out, multi_func_alu_1_overflow,
       multi_func_alu_1_zero, not_1_out, not_2_out, or_3_out, or_4_out, or_5_out, or_6_out, or_7_out,
       or_8_out, reg_write_decode_1_r0, reg_write_decode_1_r1, reg_write_decode_1_r2, reg_write_decode_1_r3,
       reg_write_decode_1_r4, reg_write_decode_1_r5, reg_write_decode_1_r6, reg_write_decode_1_r7, reset,
       SignExtend, SUB_2_add, SUB_2_addi, SUB_2_addiu, SUB_2_addu, SUB_2_and, SUB_2_beq, SUB_2_bne,
       SUB_2_div, SUB_2_divu, SUB_2_j, SUB_2_jal, SUB_2_jr, SUB_2_lhw, SUB_2_mfhi, SUB_2_mflo, SUB_2_multu,
       SUB_2_mutl, SUB_2_nor, SUB_2_or, SUB_2_shw, SUB_2_sll, SUB_2_sllr, SUB_2_slti, SUB_2_sltiu,
       SUB_2_sltu, SUB_2_sra, SUB_2_srl, SUB_2_srlr, SUB_2_stl, SUB_2_sub, SUB_2_subiu, SUB_2_subu,
       SUB_2_syscall, SUB_2_xor, Sys, undriven;
  wire [2:0] WriteReg_num;
  wire [15:0] add_extend_12_16_1_out_2, alu_3_output, multiplexer_2_out, multiplexer_3_out,
       multiplexer_6_out, multiplexer_7_out, multiplexer_10_out, register_1_q, register_2_q, register_3_q,
       register_4_q, register_5_q, register_6_q, register_7_q, register_8_q, signextend_2_out_3;
  wire [23:0] n16bit_display_1_out_3, n16bit_display_1_out_4, n16bit_display_2_out_3, n16bit_display_2_out_4,
       n16bit_display_3_out_3, n16bit_display_3_out_4, n16bit_display_4_out_3, n16bit_display_4_out_4,
       n16bit_display_5_out_3, n16bit_display_5_out_4, n16bit_display_6_out_3, n16bit_display_6_out_4,
       n16bit_display_7_out_3, n16bit_display_7_out_4;
  wire [31:0] matrix_32bit_1_out_7, matrix_32bit_1_out_8, matrix_32bit_1_out_9, matrix_32bit_1_out_10,
       matrix_32bit_1_out_11, matrix_32bit_1_out_12, matrix_32bit_1_out_13, matrix_32bit_1_out_14,
       matrix_32bit_1_out_15, matrix_32bit_1_out_16, matrix_32bit_1_out_17, matrix_32bit_1_out_18,
       matrix_32bit_1_out_19, matrix_32bit_1_out_20, matrix_32bit_1_out_21, matrix_32bit_1_out_22,
       matrix_32bit_1_out_23, matrix_32bit_1_out_24, matrix_32bit_1_out_25, matrix_32bit_1_out_26,
       matrix_32bit_1_out_27, matrix_32bit_1_out_28, matrix_32bit_1_out_29, matrix_32bit_1_out_30,
       matrix_32bit_1_out_31, matrix_32bit_1_out_32, matrix_32bit_1_out_33, matrix_32bit_1_out_34,
       matrix_32bit_1_out_35, matrix_32bit_1_out_36, matrix_32bit_1_out_37, matrix_32bit_1_out_38;

  LED MULT (.in(SUB_2_mutl));
  LED MULTU (.in(SUB_2_multu));
  LED DIV (.in(SUB_2_div));
  LED DIVU (.in(SUB_2_divu));
  LED MFHI (.in(SUB_2_mfhi));
  LED MFLO (.in(SUB_2_mflo));
  LED ADDI (.in(SUB_2_addi));
  LED ADDIU (.in(SUB_2_addiu));
  LED SUBIU (.in(SUB_2_subiu));
  LED SLTI (.in(SUB_2_slti));
  LED SLTIU (.in(SUB_2_sltiu));
  LED LHW (.in(SUB_2_lhw));
  LED SHW (.in(SUB_2_shw));
  LED JUMP (.in(SUB_2_j));
  LED JAL (.in(SUB_2_jal));
  LED BEQ (.in(SUB_2_beq));
  LED BNE (.in(SUB_2_bne));
  LED u_SYS (.in(SUB_2_syscall));
  _7_Segment_Display u_7_segment_display_1 (
    .g(n16bit_display_1_out_3[23]), .f(n16bit_display_1_out_3[22]), .a(n16bit_display_1_out_3[21]),
    .b(n16bit_display_1_out_3[20]), .e(n16bit_display_1_out_4[23]), .d(n16bit_display_1_out_4[22]),
    .c(n16bit_display_1_out_4[21]), .dp(n16bit_display_1_out_4[20]));
  _7_Segment_Display u_7_segment_display_2 (
    .g(n16bit_display_2_out_3[23]), .f(n16bit_display_2_out_3[22]), .a(n16bit_display_2_out_3[21]),
    .b(n16bit_display_2_out_3[20]), .e(n16bit_display_2_out_4[23]), .d(n16bit_display_2_out_4[22]),
    .c(n16bit_display_2_out_4[21]), .dp(n16bit_display_2_out_4[20]));
  _7_Segment_Display u_7_segment_display_3 (
    .g(n16bit_display_3_out_3[23]), .f(n16bit_display_3_out_3[22]), .a(n16bit_display_3_out_3[21]),
    .b(n16bit_display_3_out_3[20]), .e(n16bit_display_3_out_4[23]), .d(n16bit_display_3_out_4[22]),
    .c(n16bit_display_3_out_4[21]), .dp(n16bit_display_3_out_4[20]));
  _7_Segment_Display u_7_segment_display_4 (
    .g(n16bit_display_4_out_3[23]), .f(n16bit_display_4_out_3[22]), .a(n16bit_display_4_out_3[21]),
    .b(n16bit_display_4_out_3[20]), .e(n16bit_display_4_out_4[23]), .d(n16bit_display_4_out_4[22]),
    .c(n16bit_display_4_out_4[21]), .dp(n16bit_display_4_out_4[20]));
  _7_Segment_Display u_7_segment_display_5 (
    .g(n16bit_display_5_out_3[23]), .f(n16bit_display_5_out_3[22]), .a(n16bit_display_5_out_3[21]),
    .b(n16bit_display_5_out_3[20]), .e(n16bit_display_5_out_4[23]), .d(n16bit_display_5_out_4[22]),
    .c(n16bit_display_5_out_4[21]), .dp(n16bit_display_5_out_4[20]));
  _7_Segment_Display u_7_segment_display_6 (
    .g(n16bit_display_6_out_3[23]), .f(n16bit_display_6_out_3[22]), .a(n16bit_display_6_out_3[21]),
    .b(n16bit_display_6_out_3[20]), .e(n16bit_display_6_out_4[23]), .d(n16bit_display_6_out_4[22]),
    .c(n16bit_display_6_out_4[21]), .dp(n16bit_display_6_out_4[20]));
  _7_Segment_Display u_7_segment_display_7 (
    .g(n16bit_display_7_out_3[23]), .f(n16bit_display_7_out_3[22]), .a(n16bit_display_7_out_3[21]),
    .b(n16bit_display_7_out_3[20]), .e(n16bit_display_7_out_4[23]), .d(n16bit_display_7_out_4[22]),
    .c(n16bit_display_7_out_4[21]), .dp(n16bit_display_7_out_4[20]));
  LED ADD (.in(SUB_2_add));
  LED SUB (.in(SUB_2_sub));
  LED ADDU (.in(SUB_2_addu));
  LED SUBU (.in(SUB_2_subu));
  LED AND (.in(SUB_2_and));
  LED OR (.in(SUB_2_or));
  LED NOR (.in(SUB_2_nor));
  LED XOR (.in(SUB_2_xor));
  debug SUB_2 (
    .Add(SUB_2_add), .SLL(SUB_2_sll), .MUTL(SUB_2_mutl), .ADDI(SUB_2_addi), .Sub(SUB_2_sub), .SRL(SUB_2_srl),
    .MULTU(SUB_2_multu), .ADDIU(SUB_2_addiu), .AddU(SUB_2_addu), .SRA(SUB_2_sra), .DIV(SUB_2_div),
    .SUBIU(SUB_2_subiu), .SubU(SUB_2_subu), .SLLR(SUB_2_sllr), .DIVU(SUB_2_divu), .SLTI(SUB_2_slti),
    .AND(SUB_2_and), .SRLR(SUB_2_srlr), .MFHI(SUB_2_mfhi), .SLTIU(SUB_2_sltiu), .OR(SUB_2_or),
    .STL(SUB_2_stl), .MFLO(SUB_2_mflo), .LHW(SUB_2_lhw), .NOR(SUB_2_nor), .SLTU(SUB_2_sltu), .SHW(SUB_2_shw),
    .XOR(SUB_2_xor), .JR(SUB_2_jr), .J(SUB_2_j), .JAL(SUB_2_jal), .BEQ(SUB_2_beq), .BNE(SUB_2_bne),
    .Syscall(SUB_2_syscall), .in_1(out_18));
  LED SLL (.in(SUB_2_sll));
  LED SRL (.in(SUB_2_srl));
  LED SRA (.in(SUB_2_sra));
  LED SLLR (.in(SUB_2_sllr));
  LED SRLR (.in(SUB_2_srlr));
  LED SLT (.in(SUB_2_stl));
  LED SLTU (.in(SUB_2_sltu));
  LED JR (.in(SUB_2_jr));
  _7_Segment_Display u_7_segment_display_8 (
    .g(n16bit_display_1_out_3[15]), .f(n16bit_display_1_out_3[14]), .a(n16bit_display_1_out_3[13]),
    .b(n16bit_display_1_out_3[12]), .e(n16bit_display_1_out_4[15]), .d(n16bit_display_1_out_4[14]),
    .c(n16bit_display_1_out_4[13]), .dp(n16bit_display_1_out_4[12]));
  _7_Segment_Display u_7_segment_display_9 (
    .g(n16bit_display_1_out_3[19]), .f(n16bit_display_1_out_3[18]), .a(n16bit_display_1_out_3[17]),
    .b(n16bit_display_1_out_3[16]), .e(n16bit_display_1_out_4[19]), .d(n16bit_display_1_out_4[18]),
    .c(n16bit_display_1_out_4[17]), .dp(n16bit_display_1_out_4[16]));
  _7_Segment_Display u_7_segment_display_10 (
    .g(n16bit_display_2_out_3[19]), .f(n16bit_display_2_out_3[18]), .a(n16bit_display_2_out_3[17]),
    .b(n16bit_display_2_out_3[16]), .e(n16bit_display_2_out_4[19]), .d(n16bit_display_2_out_4[18]),
    .c(n16bit_display_2_out_4[17]), .dp(n16bit_display_2_out_4[16]));
  _7_Segment_Display u_7_segment_display_11 (
    .g(n16bit_display_2_out_3[15]), .f(n16bit_display_2_out_3[14]), .a(n16bit_display_2_out_3[13]),
    .b(n16bit_display_2_out_3[12]), .e(n16bit_display_2_out_4[15]), .d(n16bit_display_2_out_4[14]),
    .c(n16bit_display_2_out_4[13]), .dp(n16bit_display_2_out_4[12]));
  _7_Segment_Display u_7_segment_display_12 (
    .g(n16bit_display_3_out_3[19]), .f(n16bit_display_3_out_3[18]), .a(n16bit_display_3_out_3[17]),
    .b(n16bit_display_3_out_3[16]), .e(n16bit_display_3_out_4[19]), .d(n16bit_display_3_out_4[18]),
    .c(n16bit_display_3_out_4[17]), .dp(n16bit_display_3_out_4[16]));
  _7_Segment_Display u_7_segment_display_13 (
    .g(n16bit_display_3_out_3[15]), .f(n16bit_display_3_out_3[14]), .a(n16bit_display_3_out_3[13]),
    .b(n16bit_display_3_out_3[12]), .e(n16bit_display_3_out_4[15]), .d(n16bit_display_3_out_4[14]),
    .c(n16bit_display_3_out_4[13]), .dp(n16bit_display_3_out_4[12]));
  _7_Segment_Display u_7_segment_display_14 (
    .g(n16bit_display_4_out_3[19]), .f(n16bit_display_4_out_3[18]), .a(n16bit_display_4_out_3[17]),
    .b(n16bit_display_4_out_3[16]), .e(n16bit_display_4_out_4[19]), .d(n16bit_display_4_out_4[18]),
    .c(n16bit_display_4_out_4[17]), .dp(n16bit_display_4_out_4[16]));
  _7_Segment_Display u_7_segment_display_15 (
    .g(n16bit_display_4_out_3[15]), .f(n16bit_display_4_out_3[14]), .a(n16bit_display_4_out_3[13]),
    .b(n16bit_display_4_out_3[12]), .e(n16bit_display_4_out_4[15]), .d(n16bit_display_4_out_4[14]),
    .c(n16bit_display_4_out_4[13]), .dp(n16bit_display_4_out_4[12]));
  _7_Segment_Display u_7_segment_display_16 (
    .g(n16bit_display_5_out_3[19]), .f(n16bit_display_5_out_3[18]), .a(n16bit_display_5_out_3[17]),
    .b(n16bit_display_5_out_3[16]), .e(n16bit_display_5_out_4[19]), .d(n16bit_display_5_out_4[18]),
    .c(n16bit_display_5_out_4[17]), .dp(n16bit_display_5_out_4[16]));
  _7_Segment_Display u_7_segment_display_17 (
    .g(n16bit_display_5_out_3[15]), .f(n16bit_display_5_out_3[14]), .a(n16bit_display_5_out_3[13]),
    .b(n16bit_display_5_out_3[12]), .e(n16bit_display_5_out_4[15]), .d(n16bit_display_5_out_4[14]),
    .c(n16bit_display_5_out_4[13]), .dp(n16bit_display_5_out_4[12]));
  _7_Segment_Display u_7_segment_display_18 (
    .g(n16bit_display_6_out_3[19]), .f(n16bit_display_6_out_3[18]), .a(n16bit_display_6_out_3[17]),
    .b(n16bit_display_6_out_3[16]), .e(n16bit_display_6_out_4[19]), .d(n16bit_display_6_out_4[18]),
    .c(n16bit_display_6_out_4[17]), .dp(n16bit_display_6_out_4[16]));
  _7_Segment_Display u_7_segment_display_19 (
    .g(n16bit_display_6_out_3[15]), .f(n16bit_display_6_out_3[14]), .a(n16bit_display_6_out_3[13]),
    .b(n16bit_display_6_out_3[12]), .e(n16bit_display_6_out_4[15]), .d(n16bit_display_6_out_4[14]),
    .c(n16bit_display_6_out_4[13]), .dp(n16bit_display_6_out_4[12]));
  _7_Segment_Display u_7_segment_display_20 (
    .g(n16bit_display_7_out_3[15]), .f(n16bit_display_7_out_3[14]), .a(n16bit_display_7_out_3[13]),
    .b(n16bit_display_7_out_3[12]), .e(n16bit_display_7_out_4[15]), .d(n16bit_display_7_out_4[14]),
    .c(n16bit_display_7_out_4[13]), .dp(n16bit_display_7_out_4[12]));
  _7_Segment_Display u_7_segment_display_21 (
    .g(n16bit_display_7_out_3[19]), .f(n16bit_display_7_out_3[18]), .a(n16bit_display_7_out_3[17]),
    .b(n16bit_display_7_out_3[16]), .e(n16bit_display_7_out_4[19]), .d(n16bit_display_7_out_4[18]),
    .c(n16bit_display_7_out_4[17]), .dp(n16bit_display_7_out_4[16]));
  ALU alu_1 (.add_sub(1'b1), .B(16'h1f), .A(out_9), .zero(alu_1_zero));  // open: overflow, output
  Button button_1 (.out(button_1_out));
  _7_Segment_Display u_7_segment_display_22 (
    .g(n16bit_display_1_out_3[11]), .f(n16bit_display_1_out_3[10]), .a(n16bit_display_1_out_3[9]),
    .b(n16bit_display_1_out_3[8]), .e(n16bit_display_1_out_4[11]), .d(n16bit_display_1_out_4[10]),
    .c(n16bit_display_1_out_4[9]), .dp(n16bit_display_1_out_4[8]));
  _7_Segment_Display u_7_segment_display_23 (
    .g(n16bit_display_1_out_3[7]), .f(n16bit_display_1_out_3[6]), .a(n16bit_display_1_out_3[5]),
    .b(n16bit_display_1_out_3[4]), .e(n16bit_display_1_out_4[7]), .d(n16bit_display_1_out_4[6]),
    .c(n16bit_display_1_out_4[5]), .dp(n16bit_display_1_out_4[4]));
  _7_Segment_Display u_7_segment_display_24 (
    .g(n16bit_display_2_out_3[11]), .f(n16bit_display_2_out_3[10]), .a(n16bit_display_2_out_3[9]),
    .b(n16bit_display_2_out_3[8]), .e(n16bit_display_2_out_4[11]), .d(n16bit_display_2_out_4[10]),
    .c(n16bit_display_2_out_4[9]), .dp(n16bit_display_2_out_4[8]));
  _7_Segment_Display u_7_segment_display_25 (
    .g(n16bit_display_2_out_3[7]), .f(n16bit_display_2_out_3[6]), .a(n16bit_display_2_out_3[5]),
    .b(n16bit_display_2_out_3[4]), .e(n16bit_display_2_out_4[7]), .d(n16bit_display_2_out_4[6]),
    .c(n16bit_display_2_out_4[5]), .dp(n16bit_display_2_out_4[4]));
  _7_Segment_Display u_7_segment_display_26 (
    .g(n16bit_display_3_out_3[11]), .f(n16bit_display_3_out_3[10]), .a(n16bit_display_3_out_3[9]),
    .b(n16bit_display_3_out_3[8]), .e(n16bit_display_3_out_4[11]), .d(n16bit_display_3_out_4[10]),
    .c(n16bit_display_3_out_4[9]), .dp(n16bit_display_3_out_4[8]));
  _7_Segment_Display u_7_segment_display_27 (
    .g(n16bit_display_3_out_3[7]), .f(n16bit_display_3_out_3[6]), .a(n16bit_display_3_out_3[5]),
    .b(n16bit_display_3_out_3[4]), .e(n16bit_display_3_out_4[7]), .d(n16bit_display_3_out_4[6]),
    .c(n16bit_display_3_out_4[5]), .dp(n16bit_display_3_out_4[4]));
  _7_Segment_Display u_7_segment_display_28 (
    .g(n16bit_display_4_out_3[7]), .f(n16bit_display_4_out_3[6]), .a(n16bit_display_4_out_3[5]),
    .b(n16bit_display_4_out_3[4]), .e(n16bit_display_4_out_4[7]), .d(n16bit_display_4_out_4[6]),
    .c(n16bit_display_4_out_4[5]), .dp(n16bit_display_4_out_4[4]));
  _7_Segment_Display u_7_segment_display_29 (
    .g(n16bit_display_4_out_3[11]), .f(n16bit_display_4_out_3[10]), .a(n16bit_display_4_out_3[9]),
    .b(n16bit_display_4_out_3[8]), .e(n16bit_display_4_out_4[11]), .d(n16bit_display_4_out_4[10]),
    .c(n16bit_display_4_out_4[9]), .dp(n16bit_display_4_out_4[8]));
  _7_Segment_Display u_7_segment_display_30 (
    .g(n16bit_display_5_out_3[11]), .f(n16bit_display_5_out_3[10]), .a(n16bit_display_5_out_3[9]),
    .b(n16bit_display_5_out_3[8]), .e(n16bit_display_5_out_4[11]), .d(n16bit_display_5_out_4[10]),
    .c(n16bit_display_5_out_4[9]), .dp(n16bit_display_5_out_4[8]));
  _7_Segment_Display u_7_segment_display_31 (
    .g(n16bit_display_5_out_3[7]), .f(n16bit_display_5_out_3[6]), .a(n16bit_display_5_out_3[5]),
    .b(n16bit_display_5_out_3[4]), .e(n16bit_display_5_out_4[7]), .d(n16bit_display_5_out_4[6]),
    .c(n16bit_display_5_out_4[5]), .dp(n16bit_display_5_out_4[4]));
  _7_Segment_Display u_7_segment_display_32 (
    .g(n16bit_display_6_out_3[7]), .f(n16bit_display_6_out_3[6]), .a(n16bit_display_6_out_3[5]),
    .b(n16bit_display_6_out_3[4]), .e(n16bit_display_6_out_4[7]), .d(n16bit_display_6_out_4[6]),
    .c(n16bit_display_6_out_4[5]), .dp(n16bit_display_6_out_4[4]));
  _7_Segment_Display u_7_segment_display_33 (
    .g(n16bit_display_6_out_3[11]), .f(n16bit_display_6_out_3[10]), .a(n16bit_display_6_out_3[9]),
    .b(n16bit_display_6_out_3[8]), .e(n16bit_display_6_out_4[11]), .d(n16bit_display_6_out_4[10]),
    .c(n16bit_display_6_out_4[9]), .dp(n16bit_display_6_out_4[8]));
  _7_Segment_Display u_7_segment_display_34 (
    .g(n16bit_display_7_out_3[11]), .f(n16bit_display_7_out_3[10]), .a(n16bit_display_7_out_3[9]),
    .b(n16bit_display_7_out_3[8]), .e(n16bit_display_7_out_4[11]), .d(n16bit_display_7_out_4[10]),
    .c(n16bit_display_7_out_4[9]), .dp(n16bit_display_7_out_4[8]));
  _7_Segment_Display u_7_segment_display_35 (
    .g(n16bit_display_7_out_3[7]), .f(n16bit_display_7_out_3[6]), .a(n16bit_display_7_out_3[5]),
    .b(n16bit_display_7_out_3[4]), .e(n16bit_display_7_out_4[7]), .d(n16bit_display_7_out_4[6]),
    .c(n16bit_display_7_out_4[5]), .dp(n16bit_display_7_out_4[4]));
  Clock clock_1 (.out(clock_1_out));
  or or_2 (clock, clock_1_out, or_4_out, button_2_out);
  PC pc_1 (.Input(out_9), .Output(out_17), .CLOCK(clock), .preset_0(or_3_out), .A_Reset(or_4_out));
  or or_3 (or_3_out, alu_1_zero, button_1_out);
  _7_Segment_Display u_7_segment_display_36 (
    .g(n16bit_display_1_out_3[3]), .f(n16bit_display_1_out_3[2]), .a(n16bit_display_1_out_3[1]),
    .b(n16bit_display_1_out_3[0]), .e(n16bit_display_1_out_4[3]), .d(n16bit_display_1_out_4[2]),
    .c(n16bit_display_1_out_4[1]), .dp(n16bit_display_1_out_4[0]));
  _7_Segment_Display u_7_segment_display_37 (
    .g(n16bit_display_2_out_3[3]), .f(n16bit_display_2_out_3[2]), .a(n16bit_display_2_out_3[1]),
    .b(n16bit_display_2_out_3[0]), .e(n16bit_display_2_out_4[3]), .d(n16bit_display_2_out_4[2]),
    .c(n16bit_display_2_out_4[1]), .dp(n16bit_display_2_out_4[0]));
  _7_Segment_Display u_7_segment_display_38 (
    .g(n16bit_display_3_out_3[3]), .f(n16bit_display_3_out_3[2]), .a(n16bit_display_3_out_3[1]),
    .b(n16bit_display_3_out_3[0]), .e(n16bit_display_3_out_4[3]), .d(n16bit_display_3_out_4[2]),
    .c(n16bit_display_3_out_4[1]), .dp(n16bit_display_3_out_4[0]));
  _7_Segment_Display u_7_segment_display_39 (
    .g(n16bit_display_4_out_3[3]), .f(n16bit_display_4_out_3[2]), .a(n16bit_display_4_out_3[1]),
    .b(n16bit_display_4_out_3[0]), .e(n16bit_display_4_out_4[3]), .d(n16bit_display_4_out_4[2]),
    .c(n16bit_display_4_out_4[1]), .dp(n16bit_display_4_out_4[0]));
  _7_Segment_Display u_7_segment_display_40 (
    .g(n16bit_display_5_out_3[3]), .f(n16bit_display_5_out_3[2]), .a(n16bit_display_5_out_3[1]),
    .b(n16bit_display_5_out_3[0]), .e(n16bit_display_5_out_4[3]), .d(n16bit_display_5_out_4[2]),
    .c(n16bit_display_5_out_4[1]), .dp(n16bit_display_5_out_4[0]));
  _7_Segment_Display u_7_segment_display_41 (
    .g(n16bit_display_6_out_3[3]), .f(n16bit_display_6_out_3[2]), .a(n16bit_display_6_out_3[1]),
    .b(n16bit_display_6_out_3[0]), .e(n16bit_display_6_out_4[3]), .d(n16bit_display_6_out_4[2]),
    .c(n16bit_display_6_out_4[1]), .dp(n16bit_display_6_out_4[0]));
  _7_Segment_Display u_7_segment_display_42 (
    .g(n16bit_display_7_out_3[3]), .f(n16bit_display_7_out_3[2]), .a(n16bit_display_7_out_3[1]),
    .b(n16bit_display_7_out_3[0]), .e(n16bit_display_7_out_4[3]), .d(n16bit_display_7_out_4[2]),
    .c(n16bit_display_7_out_4[1]), .dp(n16bit_display_7_out_4[0]));
  Button button_2 (.out(button_2_out));
  _16bit_display u_16bit_display_1 (
    .out_3(n16bit_display_1_out_3), .out_4(n16bit_display_1_out_4), .in_2(register_3_q), .\signed (in_7));
  _16bit_display u_16bit_display_2 (
    .out_3(n16bit_display_2_out_3), .out_4(n16bit_display_2_out_4), .in_2(register_2_q), .\signed (in_7));
  _16bit_display u_16bit_display_3 (
    .out_3(n16bit_display_3_out_3), .out_4(n16bit_display_3_out_4), .in_2(register_4_q), .\signed (in_7));
  _16bit_display u_16bit_display_4 (
    .out_3(n16bit_display_4_out_3), .out_4(n16bit_display_4_out_4), .in_2(register_5_q), .\signed (in_7));
  _16bit_display u_16bit_display_5 (
    .out_3(n16bit_display_5_out_3), .out_4(n16bit_display_5_out_4), .in_2(register_7_q), .\signed (in_7));
  _16bit_display u_16bit_display_6 (
    .out_3(n16bit_display_6_out_3), .out_4(n16bit_display_6_out_4), .in_2(register_6_q), .\signed (in_7));
  _16bit_display u_16bit_display_7 (
    .out_3(n16bit_display_7_out_3), .out_4(n16bit_display_7_out_4), .in_2(register_8_q), .\signed (in_7));
  ALU alu_2 (.add_sub(1'b0), .B(out_17), .A(16'h1), .\output (out_8));  // open: overflow, zero
  or or_4 (or_4_out, button_3_out, reset);
  Button button_3 (.out(button_3_out));
  RAM #(.addrWidth(16), .dataWidth(16)) ram_1 (
    .addr(out_17), .data({OP_2, Reg1_2, Reg2_2, Imm_3}));  // open: sel, clk, ld, clr
  add_extend_12_16 add_extend_12_16_1 (.in_1({Reg1, Reg2, Imm}), .out_2(add_extend_12_16_1_out_2));
  Transistor #(.\type ("n"), .width(16)) transistor_1 (
    .in({in_1, in_2, in_3, in_4, in_5}), .out({OP, Reg1, Reg2, Imm}), .gate(in_6));
  Transistor #(.width(16)) transistor_2 (.in({OP_2, Reg1_2, Reg2_2, Imm_3}), .out({OP, Reg1, Reg2, Imm}), .gate(in_6));
  // Probe on Reg1
  // Probe on Reg2
  Multiplexer #(.width(3), .enable("false")) multiplexer_1 (
    .in0(Reg2), .in1(Imm[5:3]), .out(WriteReg_num), .sel(out_18[14]));
  // Probe on Imm[5:3]
  // Probe on multiplexer_2_out
  // Probe on Reg1
  Register #(.width(16)) register_1 (
    .D(out_28), .en(reg_write_decode_1_r0), .Q(register_1_q), .clk(clock), .clr(or_4_out));
  ALU alu_3 (.add_sub(1'b1), .B(out_10), .A(out_8), .\output (alu_3_output));  // open: overflow, zero
  // Probe on WriteReg_num
  signExtend signextend_1 (.in_1(Imm), .out_3(out_10), .in_2(SignExtend));
  Multiplexer #(.select(3), .width(16), .enable("false")) multiplexer_2 (
    .in0(register_1_q), .in1(register_3_q), .in2(register_2_q), .in3(register_4_q), .in4(register_5_q),
    .in5(register_7_q), .in6(register_6_q), .in7(register_8_q), .out(multiplexer_2_out), .sel(Reg1));
  Register #(.width(16)) register_2 (
    .D(out_28), .en(reg_write_decode_1_r2), .Q(register_2_q), .clk(clock), .clr(or_4_out));
  Register #(.width(16)) register_3 (
    .D(out_28), .en(reg_write_decode_1_r1), .Q(register_3_q), .clk(clock), .clr(or_4_out));
  Register #(.width(16)) register_4 (
    .D(out_28), .en(reg_write_decode_1_r3), .Q(register_4_q), .clk(clock), .clr(or_4_out));
  reg_Write_Decode reg_write_decode_1 (
    .in_2(out_35), .R0(reg_write_decode_1_r0), .R1(reg_write_decode_1_r1), .R2(reg_write_decode_1_r2),
    .R3(reg_write_decode_1_r3), .R4(reg_write_decode_1_r4), .R5(reg_write_decode_1_r5),
    .R6(reg_write_decode_1_r6), .R7(reg_write_decode_1_r7), .in_1(out_18[6]));
  signExtend signextend_2 (.in_1({3'b000, Reg1}), .out_3(signextend_2_out_3), .in_2(SignExtend));
  // Probe on multiplexer_6_out
  // Probe on Reg2
  Register #(.width(16)) register_5 (
    .D(out_28), .en(reg_write_decode_1_r4), .Q(register_5_q), .clk(clock), .clr(or_4_out));
  Multiplexer #(.width(16), .enable("false")) multiplexer_3 (
    .in0(out_8), .in1(alu_3_output), .out(multiplexer_3_out), .sel(or_5_out));
  or or_5 (or_5_out, and_2_out, and_3_out);
  and and_2 (and_2_out, out_18[10], not_1_out);
  not not_1 (not_1_out, multi_func_alu_1_zero);
  Multiplexer #(.width(16), .enable("false")) multiplexer_4 (
    .in0(multiplexer_2_out), .in1(signextend_2_out_3), .out(out_20), .sel(out_18[13]));
  Multiplexer #(.width(16), .enable("false")) multiplexer_5 (
    .in0(multiplexer_6_out), .in1(out_10), .out({out_23[15:5], out_22}), .sel(out_18[5]));
  Multiplexer #(.select(3), .width(16), .enable("false")) multiplexer_6 (
    .in0(register_1_q), .in1(register_3_q), .in2(register_2_q), .in3(register_4_q), .in4(register_5_q),
    .in5(register_7_q), .in6(register_6_q), .in7(register_8_q), .out(multiplexer_6_out), .sel(Reg2));
  Register #(.width(16)) register_6 (
    .D(out_28), .en(reg_write_decode_1_r6), .Q(register_6_q), .clk(clock), .clr(or_4_out));
  Register #(.width(16)) register_7 (
    .D(out_28), .en(reg_write_decode_1_r5), .Q(register_7_q), .clk(clock), .clr(or_4_out));
  Multiplexer #(.width(16), .enable("false")) multiplexer_7 (
    .in0(multiplexer_3_out), .in1(add_extend_12_16_1_out_2), .out(multiplexer_7_out), .sel(out_18[11]));
  and and_3 (and_3_out, out_18[9], multi_func_alu_1_zero);
  Register #(.width(16)) register_8 (
    .D(out_28), .en(reg_write_decode_1_r7), .Q(register_8_q), .clk(clock), .clr(or_4_out));
  Multiplexer #(.width(3), .enable("false")) multiplexer_8 (
    .in0(WriteReg_num), .in1(3'b111), .out(out_35), .sel(and_4_out));
  Multiplexer #(.width(16), .enable("false")) multiplexer_9 (
    .in0(multiplexer_7_out), .in1(out_20), .out(out_9), .sel(out_18[12]));
  Multi_Func_ALU multi_func_alu_1 (
    .B({out_23[15:5], out_22}), .A(out_20), .overflow(multi_func_alu_1_overflow),
    .zero(multi_func_alu_1_zero), .output_2(out_25), .add_sub(out_18[4:0]));  // open: output
  LED led_1 (.in(multi_func_alu_1_overflow));
  Multiplexer #(.width(16), .enable("false")) multiplexer_10 (
    .in0(out_25), .in1(out_27), .out(multiplexer_10_out), .sel(out_18[8]));
  Multiplexer #(.width(16), .enable("false")) multiplexer_11 (
    .in0(multiplexer_10_out), .in1(out_8), .out(out_28), .sel(and_4_out));
  and and_4 (and_4_out, out_18[6], out_18[11]);
  or or_6 (or_6_out, out_18[7], out_18[8]);
  Button button_4 (.out(reset));
  control_final control_final_1 (
    .a(OP[3]), .c(OP[1]), .b(OP[2]), .d(OP[0]), .x(Imm[2]), .y(Imm[1]), .z(Imm[0]), .jump(out_18[11]),
    .branch(out_18[10:9]), .MemRead(out_18[8]), .Reg2Imm(out_18[13]), .MemWrite(out_18[7]),
    .Jump2Ra(out_18[12]), .AluSrc(out_18[5]), .AluOp4(out_18[3]), .AluOp3(out_18[2]), .AluOp1(out_18[0]),
    .AluOp5(out_18[4]), .RegWrite(out_18[6]), .AluOp2(out_18[1]), .RegD(out_18[14]), .SignExtend(SignExtend),
    .out_8(Sys));
  RAM #(.addrWidth(16), .dataWidth(16)) ram_2 (
    .addr(out_25), .data(out_27), .sel(or_6_out), .clk(clock), .ld(out_18[8]), .clr(undriven));
  Transistor #(.gate("br"), .width(16)) transistor_3 (.in(multiplexer_6_out), .out(out_27), .gate(out_18[8]));
  or or_7 (or_7_out, button_5_out, clock);
  Button button_5 (.out(button_5_out));
  Clock clock_2 (.out(clock_2_out));
  DotMatrix #(.matrixcols(32), .matrixrows(32)) dotmatrix_1 (
    .col0(matrix_32bit_1_out_11), .col1(matrix_32bit_1_out_12), .col2(matrix_32bit_1_out_13),
    .col3(matrix_32bit_1_out_14), .col4(matrix_32bit_1_out_7), .col5(matrix_32bit_1_out_8),
    .col6(matrix_32bit_1_out_9), .col7(matrix_32bit_1_out_10), .col8(matrix_32bit_1_out_15),
    .col9(matrix_32bit_1_out_16), .col10(matrix_32bit_1_out_17), .col11(matrix_32bit_1_out_18),
    .col12(matrix_32bit_1_out_19), .col13(matrix_32bit_1_out_20), .col14(matrix_32bit_1_out_21),
    .col15(matrix_32bit_1_out_22), .col16(matrix_32bit_1_out_23), .col17(matrix_32bit_1_out_24),
    .col18(matrix_32bit_1_out_25), .col19(matrix_32bit_1_out_26), .col20(matrix_32bit_1_out_27),
    .col21(matrix_32bit_1_out_28), .col22(matrix_32bit_1_out_29), .col23(matrix_32bit_1_out_30),
    .col24(matrix_32bit_1_out_31), .col25(matrix_32bit_1_out_32), .col26(matrix_32bit_1_out_33),
    .col27(matrix_32bit_1_out_34), .col28(matrix_32bit_1_out_35), .col29(matrix_32bit_1_out_36),
    .col30(matrix_32bit_1_out_37), .col31(matrix_32bit_1_out_38));
  or or_8 (or_8_out, or_4_out, and_5_out, button_6_out);
  and and_5 (and_5_out, out_10[1], and_6_out, Sys);
  Button button_6 (.out(button_6_out));
  and and_6 (and_6_out, clock, not_2_out);
  not not_2 (not_2_out, clock);
  matrix_32bit matrix_32bit_1 (
    .in_1(out_20[4:0]), .Reset(or_8_out), .Write(Sys), .in_2(out_22), .Data(out_10[0]),
    .out_11(matrix_32bit_1_out_11), .out_12(matrix_32bit_1_out_12), .out_13(matrix_32bit_1_out_13),
    .out_14(matrix_32bit_1_out_14), .out_7(matrix_32bit_1_out_7), .out_8(matrix_32bit_1_out_8),
    .out_9(matrix_32bit_1_out_9), .out_10(matrix_32bit_1_out_10), .out_15(matrix_32bit_1_out_15),
    .out_16(matrix_32bit_1_out_16), .out_17(matrix_32bit_1_out_17), .out_18(matrix_32bit_1_out_18),
    .Clock(or_7_out), .out_19(matrix_32bit_1_out_19), .out_20(matrix_32bit_1_out_20),
    .out_21(matrix_32bit_1_out_21), .out_22(matrix_32bit_1_out_22), .out_23(matrix_32bit_1_out_23),
    .out_24(matrix_32bit_1_out_24), .out_25(matrix_32bit_1_out_25), .out_26(matrix_32bit_1_out_26),
    .out_27(matrix_32bit_1_out_27), .out_28(matrix_32bit_1_out_28), .out_29(matrix_32bit_1_out_29),
    .out_30(matrix_32bit_1_out_30), .out_31(matrix_32bit_1_out_31), .out_32(matrix_32bit_1_out_32),
    .out_33(matrix_32bit_1_out_33), .out_34(matrix_32bit_1_out_34), .out_35(matrix_32bit_1_out_35),
    .out_36(matrix_32bit_1_out_36), .out_37(matrix_32bit_1_out_37), .out_38(matrix_32bit_1_out_38));

  assign Imm_2 = Imm;
  assign out_15 = Imm[2:0];
  assign out_19 = out_18[4:0];
  assign out_21 = out_20[4:0];
  assign out_23[4:0] = out_22;
  assign out_24 = out_10;
  assign out_33 = Imm_3[2:0];
  assign Reg_3 = Imm[5:3];
  assign Reg_3_2 = Imm_3[5:3];

  // Other names for the same wires on the sheet: ReadReg1[2:0] = Reg1; cmd[15:0] = {OP_2, Reg1_2, Reg2_2, Imm_3};
  //   ALUcodes[4:0] = out_18[4:0]; Controls[14:0] = out_18; AluSrc = out_18[5]; regWrite = out_18[6];
  //   memWrite = out_18[7]; memRead = out_18[8]; branch[1:0] = out_18[10:9]; jump = out_18[11]; jump2reg = out_18[12];
  //   reg2imm = out_18[13]; regD = out_18[14]; ReadReg2[2:0] = Reg2

  // Notes on the sheet:
  //   1
  //   2
  //   3
  //   4
  //   5
  //   6
  //   7
  //   reset oc
  //   reset
  //   Going A
  //   reset
endmodule

module PC (
  input  [15:0] Input,
  input  CLOCK,
  input  preset_0,
  input  A_Reset,
  output [15:0] Output
);

  D_Latch_w_R_and_Set d_latch_w_r_and_set_1 (
    .Clock(CLOCK), .Data(Input[0]), .A_Reset(A_Reset), .Preset0(preset_0), .Data_Out(Output[0]));  // open: out_6
  D_Latch_w_R_and_Set d_latch_w_r_and_set_2 (
    .Clock(CLOCK), .Data(Input[1]), .A_Reset(A_Reset), .Preset0(preset_0), .Data_Out(Output[1]));  // open: out_6
  D_Latch_w_R_and_Set d_latch_w_r_and_set_3 (
    .Clock(CLOCK), .Data(Input[2]), .A_Reset(A_Reset), .Preset0(preset_0), .Data_Out(Output[2]));  // open: out_6
  D_Latch_w_R_and_Set d_latch_w_r_and_set_4 (
    .Clock(CLOCK), .Data(Input[3]), .A_Reset(A_Reset), .Preset0(preset_0), .Data_Out(Output[3]));  // open: out_6
  D_Latch_w_R_and_Set d_latch_w_r_and_set_5 (
    .Clock(CLOCK), .Data(Input[4]), .A_Reset(A_Reset), .Preset0(preset_0), .Data_Out(Output[4]));  // open: out_6
  D_Latch_w_R_and_Set d_latch_w_r_and_set_6 (
    .Clock(CLOCK), .Data(Input[5]), .A_Reset(A_Reset), .Preset0(preset_0), .Data_Out(Output[5]));  // open: out_6
  D_Latch_w_R_and_Set d_latch_w_r_and_set_7 (
    .Clock(CLOCK), .Data(Input[6]), .A_Reset(A_Reset), .Preset0(preset_0), .Data_Out(Output[6]));  // open: out_6
  D_Latch_w_R_and_Set d_latch_w_r_and_set_8 (
    .Clock(CLOCK), .Data(Input[7]), .A_Reset(A_Reset), .Preset0(preset_0), .Data_Out(Output[7]));  // open: out_6
  D_Latch_w_R_and_Set d_latch_w_r_and_set_9 (
    .Clock(CLOCK), .Data(Input[8]), .A_Reset(A_Reset), .Preset0(preset_0), .Data_Out(Output[8]));  // open: out_6
  D_Latch_w_R_and_Set d_latch_w_r_and_set_10 (
    .Clock(CLOCK), .Data(Input[9]), .A_Reset(A_Reset), .Preset0(preset_0), .Data_Out(Output[9]));  // open: out_6
  D_Latch_w_R_and_Set d_latch_w_r_and_set_11 (
    .Clock(CLOCK), .Data(Input[10]), .A_Reset(A_Reset), .Preset0(preset_0), .Data_Out(Output[10]));  // open: out_6
  D_Latch_w_R_and_Set d_latch_w_r_and_set_12 (
    .Clock(CLOCK), .Data(Input[11]), .A_Reset(A_Reset), .Preset0(preset_0), .Data_Out(Output[11]));  // open: out_6
  D_Latch_w_R_and_Set d_latch_w_r_and_set_13 (
    .Clock(CLOCK), .Data(Input[12]), .A_Reset(A_Reset), .Preset0(preset_0), .Data_Out(Output[12]));  // open: out_6
  D_Latch_w_R_and_Set d_latch_w_r_and_set_14 (
    .Clock(CLOCK), .Data(Input[13]), .A_Reset(A_Reset), .Preset0(preset_0), .Data_Out(Output[13]));  // open: out_6
  D_Latch_w_R_and_Set d_latch_w_r_and_set_15 (
    .Clock(CLOCK), .Data(Input[14]), .A_Reset(A_Reset), .Preset0(preset_0), .Data_Out(Output[14]));  // open: out_6
  D_Latch_w_R_and_Set d_latch_w_r_and_set_16 (
    .Clock(CLOCK), .Data(Input[15]), .A_Reset(A_Reset), .Preset0(preset_0), .Data_Out(Output[15]));  // open: out_6
endmodule

module miniadder (
  input  in_1,
  input  in_2,
  input  in_3,
  input  in_4,
  input  in_5,
  input  in_6,
  input  in_7,
  input  in_8,
  input  in_9,
  input  in_10,
  input  in_11,
  input  in_12,
  input  in_13,
  input  in_14,
  input  in_15,
  input  in_16,
  input  in_17,
  input  in_18,
  input  in_19,
  input  in_20,
  input  in_21,
  input  in_22,
  input  in_23,
  input  in_24
);

  wire adder_sub_1_c_out, adder_sub_1_data, adder_sub_2_c_out, adder_sub_2_data, adder_sub_3_c_out,
       adder_sub_3_data, adder_sub_4_c_out, adder_sub_4_data, adder_sub_5_c_out, adder_sub_5_data,
       adder_sub_6_c_out, adder_sub_6_data, adder_sub_7_c_out, adder_sub_7_data, adder_sub_8_c_out,
       adder_sub_8_data, bcd_8bit_1_out_9, bcd_8bit_1_out_10, bcd_8bit_1_out_11, bcd_8bit_1_out_12,
       bcd_8bit_1_out_13, bcd_8bit_1_out_14, bcd_8bit_1_out_15, bcd_8bit_1_out_16, bcd_8bit_1_out_17,
       bcd_8bit_1_out_18, bcd_8bit_2_out_9, bcd_8bit_2_out_10, bcd_8bit_2_out_11, bcd_8bit_2_out_12,
       bcd_8bit_2_out_13, bcd_8bit_2_out_14, bcd_8bit_2_out_15, bcd_8bit_2_out_16, bcd_8bit_2_out_17,
       bcd_8bit_2_out_18, bcd_8bit_3_out_9, bcd_8bit_3_out_10, bcd_8bit_3_out_11, bcd_8bit_3_out_12,
       bcd_8bit_3_out_13, bcd_8bit_3_out_14, bcd_8bit_3_out_15, bcd_8bit_3_out_16, bcd_8bit_3_out_17,
       bcd_8bit_3_out_18;
  wire [2:0] bcd_to_7segment_display_1_bl, bcd_to_7segment_display_2_bl, bcd_to_7segment_display_3_bl,
       bcd_to_7segment_display_4_bl, bcd_to_7segment_display_5_bl, bcd_to_7segment_display_6_bl,
       bcd_to_7segment_display_7_bl, bcd_to_7segment_display_8_bl, bcd_to_7segment_display_9_bl;
  wire [3:0] bcd_to_7segment_display_1_tr, bcd_to_7segment_display_2_tr, bcd_to_7segment_display_3_tr,
       bcd_to_7segment_display_4_tr, bcd_to_7segment_display_5_tr, bcd_to_7segment_display_6_tr,
       bcd_to_7segment_display_7_tr, bcd_to_7segment_display_8_tr, bcd_to_7segment_display_9_tr;

  BCD_to_7segment_display bcd_to_7segment_display_1 (
    .a(in_17), .b(in_18), .c(bcd_8bit_1_out_9), .m(bcd_to_7segment_display_1_tr[3]), .d(bcd_8bit_1_out_10),
    .tl(bcd_to_7segment_display_1_tr[2]), .t(bcd_to_7segment_display_1_tr[1]),
    .tr(bcd_to_7segment_display_1_tr[0]), .bl(bcd_to_7segment_display_1_bl[0]),
    .b2(bcd_to_7segment_display_1_bl[1]), .br(bcd_to_7segment_display_1_bl[2]));
  bcd_8bit bcd_8bit_1 (
    .in_1(in_1), .in_2(in_2), .in_3(in_3), .in_4(in_4), .in_5(in_5), .in_6(in_6), .in_7(in_7),
    .out_17(bcd_8bit_1_out_17), .out_16(bcd_8bit_1_out_16), .out_15(bcd_8bit_1_out_15),
    .out_14(bcd_8bit_1_out_14), .out_13(bcd_8bit_1_out_13), .out_12(bcd_8bit_1_out_12),
    .out_11(bcd_8bit_1_out_11), .out_10(bcd_8bit_1_out_10), .out_9(bcd_8bit_1_out_9), .in_8(in_8),
    .out_18(bcd_8bit_1_out_18));
  BCD_to_7segment_display bcd_to_7segment_display_2 (
    .a(bcd_8bit_1_out_11), .b(bcd_8bit_1_out_12), .c(bcd_8bit_1_out_13), .m(bcd_to_7segment_display_2_tr[3]),
    .d(bcd_8bit_1_out_14), .tl(bcd_to_7segment_display_2_tr[2]), .t(bcd_to_7segment_display_2_tr[1]),
    .tr(bcd_to_7segment_display_2_tr[0]), .bl(bcd_to_7segment_display_2_bl[0]),
    .b2(bcd_to_7segment_display_2_bl[1]), .br(bcd_to_7segment_display_2_bl[2]));
  _7_Segment_Display u_7_segment_display_1 (
    .g(bcd_to_7segment_display_2_tr[3]), .f(bcd_to_7segment_display_2_tr[2]),
    .a(bcd_to_7segment_display_2_tr[1]), .b(bcd_to_7segment_display_2_tr[0]),
    .e(bcd_to_7segment_display_2_bl[0]), .d(bcd_to_7segment_display_2_bl[1]),
    .c(bcd_to_7segment_display_2_bl[2]));  // open: dp
  _7_Segment_Display u_7_segment_display_2 (
    .g(bcd_to_7segment_display_1_tr[3]), .f(bcd_to_7segment_display_1_tr[2]),
    .a(bcd_to_7segment_display_1_tr[1]), .b(bcd_to_7segment_display_1_tr[0]),
    .e(bcd_to_7segment_display_1_bl[0]), .d(bcd_to_7segment_display_1_bl[1]),
    .c(bcd_to_7segment_display_1_bl[2]));  // open: dp
  LED led_1 (.in(adder_sub_1_c_out));
  BCD_to_7segment_display bcd_to_7segment_display_3 (
    .a(bcd_8bit_1_out_15), .b(bcd_8bit_1_out_16), .c(bcd_8bit_1_out_17), .m(bcd_to_7segment_display_3_tr[3]),
    .d(bcd_8bit_1_out_18), .tl(bcd_to_7segment_display_3_tr[2]), .t(bcd_to_7segment_display_3_tr[1]),
    .tr(bcd_to_7segment_display_3_tr[0]), .bl(bcd_to_7segment_display_3_bl[0]),
    .b2(bcd_to_7segment_display_3_bl[1]), .br(bcd_to_7segment_display_3_bl[2]));
  _7_Segment_Display u_7_segment_display_3 (
    .g(bcd_to_7segment_display_3_tr[3]), .f(bcd_to_7segment_display_3_tr[2]),
    .a(bcd_to_7segment_display_3_tr[1]), .b(bcd_to_7segment_display_3_tr[0]),
    .e(bcd_to_7segment_display_3_bl[0]), .d(bcd_to_7segment_display_3_bl[1]),
    .c(bcd_to_7segment_display_3_bl[2]));  // open: dp
  adder_sub adder_sub_1 (
    .a(in_1), .b(in_9), .c(adder_sub_2_c_out), .c_out(adder_sub_1_c_out), .data(adder_sub_1_data),
    .add_sub(in_21));
  adder_sub adder_sub_2 (
    .a(in_2), .b(in_10), .c(adder_sub_3_c_out), .c_out(adder_sub_2_c_out), .data(adder_sub_2_data),
    .add_sub(in_21));
  adder_sub adder_sub_3 (
    .a(in_3), .b(in_11), .c(adder_sub_4_c_out), .c_out(adder_sub_3_c_out), .data(adder_sub_3_data),
    .add_sub(in_21));
  BCD_to_7segment_display bcd_to_7segment_display_4 (
    .a(in_23), .b(in_24), .c(bcd_8bit_2_out_9), .m(bcd_to_7segment_display_4_tr[3]), .d(bcd_8bit_2_out_10),
    .tl(bcd_to_7segment_display_4_tr[2]), .t(bcd_to_7segment_display_4_tr[1]),
    .tr(bcd_to_7segment_display_4_tr[0]), .bl(bcd_to_7segment_display_4_bl[0]),
    .b2(bcd_to_7segment_display_4_bl[1]), .br(bcd_to_7segment_display_4_bl[2]));
  adder_sub adder_sub_4 (
    .a(in_4), .b(in_12), .c(adder_sub_5_c_out), .c_out(adder_sub_4_c_out), .data(adder_sub_4_data),
    .add_sub(in_21));
  bcd_8bit bcd_8bit_2 (
    .in_1(adder_sub_1_data), .in_2(adder_sub_2_data), .in_3(adder_sub_3_data), .in_4(adder_sub_4_data),
    .in_5(adder_sub_5_data), .in_6(adder_sub_6_data), .in_7(adder_sub_7_data), .out_17(bcd_8bit_2_out_17),
    .out_16(bcd_8bit_2_out_16), .out_15(bcd_8bit_2_out_15), .out_14(bcd_8bit_2_out_14),
    .out_13(bcd_8bit_2_out_13), .out_12(bcd_8bit_2_out_12), .out_11(bcd_8bit_2_out_11),
    .out_10(bcd_8bit_2_out_10), .out_9(bcd_8bit_2_out_9), .in_8(adder_sub_8_data), .out_18(bcd_8bit_2_out_18));
  BCD_to_7segment_display bcd_to_7segment_display_5 (
    .a(bcd_8bit_2_out_11), .b(bcd_8bit_2_out_12), .c(bcd_8bit_2_out_13), .m(bcd_to_7segment_display_5_tr[3]),
    .d(bcd_8bit_2_out_14), .tl(bcd_to_7segment_display_5_tr[2]), .t(bcd_to_7segment_display_5_tr[1]),
    .tr(bcd_to_7segment_display_5_tr[0]), .bl(bcd_to_7segment_display_5_bl[0]),
    .b2(bcd_to_7segment_display_5_bl[1]), .br(bcd_to_7segment_display_5_bl[2]));
  BCD_to_7segment_display bcd_to_7segment_display_6 (
    .a(in_19), .b(in_20), .c(bcd_8bit_3_out_9), .m(bcd_to_7segment_display_6_tr[3]), .d(bcd_8bit_3_out_10),
    .tl(bcd_to_7segment_display_6_tr[2]), .t(bcd_to_7segment_display_6_tr[1]),
    .tr(bcd_to_7segment_display_6_tr[0]), .bl(bcd_to_7segment_display_6_bl[0]),
    .b2(bcd_to_7segment_display_6_bl[1]), .br(bcd_to_7segment_display_6_bl[2]));
  adder_sub adder_sub_5 (
    .a(in_5), .b(in_13), .c(adder_sub_6_c_out), .c_out(adder_sub_5_c_out), .data(adder_sub_5_data),
    .add_sub(in_21));
  adder_sub adder_sub_6 (
    .a(in_6), .b(in_14), .c(adder_sub_7_c_out), .c_out(adder_sub_6_c_out), .data(adder_sub_6_data),
    .add_sub(in_21));
  BCD_to_7segment_display bcd_to_7segment_display_7 (
    .a(bcd_8bit_2_out_15), .b(bcd_8bit_2_out_16), .c(bcd_8bit_2_out_17), .m(bcd_to_7segment_display_7_tr[3]),
    .d(bcd_8bit_2_out_18), .tl(bcd_to_7segment_display_7_tr[2]), .t(bcd_to_7segment_display_7_tr[1]),
    .tr(bcd_to_7segment_display_7_tr[0]), .bl(bcd_to_7segment_display_7_bl[0]),
    .b2(bcd_to_7segment_display_7_bl[1]), .br(bcd_to_7segment_display_7_bl[2]));
  bcd_8bit bcd_8bit_3 (
    .in_1(in_9), .in_2(in_10), .in_3(in_11), .in_4(in_12), .in_5(in_13), .in_6(in_14), .in_7(in_15),
    .out_17(bcd_8bit_3_out_17), .out_16(bcd_8bit_3_out_16), .out_15(bcd_8bit_3_out_15),
    .out_14(bcd_8bit_3_out_14), .out_13(bcd_8bit_3_out_13), .out_12(bcd_8bit_3_out_12),
    .out_11(bcd_8bit_3_out_11), .out_10(bcd_8bit_3_out_10), .out_9(bcd_8bit_3_out_9), .in_8(in_16),
    .out_18(bcd_8bit_3_out_18));
  BCD_to_7segment_display bcd_to_7segment_display_8 (
    .a(bcd_8bit_3_out_11), .b(bcd_8bit_3_out_12), .c(bcd_8bit_3_out_13), .m(bcd_to_7segment_display_8_tr[3]),
    .d(bcd_8bit_3_out_14), .tl(bcd_to_7segment_display_8_tr[2]), .t(bcd_to_7segment_display_8_tr[1]),
    .tr(bcd_to_7segment_display_8_tr[0]), .bl(bcd_to_7segment_display_8_bl[0]),
    .b2(bcd_to_7segment_display_8_bl[1]), .br(bcd_to_7segment_display_8_bl[2]));
  _7_Segment_Display u_7_segment_display_4 (
    .g(bcd_to_7segment_display_6_tr[3]), .f(bcd_to_7segment_display_6_tr[2]),
    .a(bcd_to_7segment_display_6_tr[1]), .b(bcd_to_7segment_display_6_tr[0]),
    .e(bcd_to_7segment_display_6_bl[0]), .d(bcd_to_7segment_display_6_bl[1]),
    .c(bcd_to_7segment_display_6_bl[2]));  // open: dp
  _7_Segment_Display u_7_segment_display_5 (
    .g(bcd_to_7segment_display_8_tr[3]), .f(bcd_to_7segment_display_8_tr[2]),
    .a(bcd_to_7segment_display_8_tr[1]), .b(bcd_to_7segment_display_8_tr[0]),
    .e(bcd_to_7segment_display_8_bl[0]), .d(bcd_to_7segment_display_8_bl[1]),
    .c(bcd_to_7segment_display_8_bl[2]));  // open: dp
  adder_sub adder_sub_7 (
    .a(in_7), .b(in_15), .c(adder_sub_8_c_out), .c_out(adder_sub_7_c_out), .data(adder_sub_7_data),
    .add_sub(in_21));
  BCD_to_7segment_display bcd_to_7segment_display_9 (
    .a(bcd_8bit_3_out_15), .b(bcd_8bit_3_out_16), .c(bcd_8bit_3_out_17), .m(bcd_to_7segment_display_9_tr[3]),
    .d(bcd_8bit_3_out_18), .tl(bcd_to_7segment_display_9_tr[2]), .t(bcd_to_7segment_display_9_tr[1]),
    .tr(bcd_to_7segment_display_9_tr[0]), .bl(bcd_to_7segment_display_9_bl[0]),
    .b2(bcd_to_7segment_display_9_bl[1]), .br(bcd_to_7segment_display_9_bl[2]));
  _7_Segment_Display u_7_segment_display_6 (
    .g(bcd_to_7segment_display_9_tr[3]), .f(bcd_to_7segment_display_9_tr[2]),
    .a(bcd_to_7segment_display_9_tr[1]), .b(bcd_to_7segment_display_9_tr[0]),
    .e(bcd_to_7segment_display_9_bl[0]), .d(bcd_to_7segment_display_9_bl[1]),
    .c(bcd_to_7segment_display_9_bl[2]));  // open: dp
  adder_sub adder_sub_8 (
    .a(in_8), .b(in_16), .c(in_22), .c_out(adder_sub_8_c_out), .data(adder_sub_8_data), .add_sub(in_21));
  _7_Segment_Display u_7_segment_display_7 (
    .g(bcd_to_7segment_display_5_tr[3]), .f(bcd_to_7segment_display_5_tr[2]),
    .a(bcd_to_7segment_display_5_tr[1]), .b(bcd_to_7segment_display_5_tr[0]),
    .e(bcd_to_7segment_display_5_bl[0]), .d(bcd_to_7segment_display_5_bl[1]),
    .c(bcd_to_7segment_display_5_bl[2]));  // open: dp
  _7_Segment_Display u_7_segment_display_8 (
    .g(bcd_to_7segment_display_4_tr[3]), .f(bcd_to_7segment_display_4_tr[2]),
    .a(bcd_to_7segment_display_4_tr[1]), .b(bcd_to_7segment_display_4_tr[0]),
    .e(bcd_to_7segment_display_4_bl[0]), .d(bcd_to_7segment_display_4_bl[1]),
    .c(bcd_to_7segment_display_4_bl[2]));  // open: dp
  _7_Segment_Display u_7_segment_display_9 (
    .g(bcd_to_7segment_display_7_tr[3]), .f(bcd_to_7segment_display_7_tr[2]),
    .a(bcd_to_7segment_display_7_tr[1]), .b(bcd_to_7segment_display_7_tr[0]),
    .e(bcd_to_7segment_display_7_bl[0]), .d(bcd_to_7segment_display_7_bl[1]),
    .c(bcd_to_7segment_display_7_bl[2]));  // open: dp

  // Notes on the sheet:
  //   0=a 1=s
endmodule

module adder_sub (
  input  a,
  input  b,
  input  c,
  input  add_sub,
  output data,
  output c_out
);

  wire and_1_out, and_2_out, and_3_out, and_4_out, and_5_out, and_6_out, nand_1_out, nand_2_out, or_1_out,
       or_2_out, or_3_out, xor_1_out, xor_2_out, xor_3_out;

  or or_1 (or_1_out, a, b);
  nand nand_1 (nand_1_out, a, b);
  and and_1 (and_1_out, b, a);
  xor xor_1 (xor_1_out, a, b);
  and and_2 (and_2_out, b, xor_2_out);
  xor xor_2 (xor_2_out, a, add_sub);
  and and_3 (and_3_out, or_1_out, nand_1_out);
  xor xor_3 (xor_3_out, xor_1_out, add_sub);
  or or_2 (or_2_out, and_3_out, c);
  and and_4 (and_4_out, or_2_out, nand_2_out);
  nand nand_2 (nand_2_out, and_3_out, c);
  or or_3 (or_3_out, and_1_out, and_5_out);
  and and_5 (and_5_out, and_3_out, c);
  xor xor_4 (data, xor_1_out, c);
  or or_4 (c_out, and_2_out, and_6_out);
  and and_6 (and_6_out, xor_3_out, c);
endmodule

module BCD_to_7segment_display (
  input  a,
  input  b,
  input  c,
  input  d,
  output m,
  output tl,
  output t,
  output tr,
  output bl,
  output b2,
  output br
);

  wire and_1_out, and_2_out, and_3_out, and_4_out, and_5_out, and_6_out, and_7_out, and_8_out, and_9_out,
       and_10_out, and_11_out, and_12_out, and_13_out, and_14_out, and_15_out, and_16_out, and_17_out,
       and_18_out, and_19_out, and_20_out, and_21_out, and_22_out, and_23_out, and_24_out, and_25_out,
       and_26_out, and_27_out, and_28_out, and_29_out, and_30_out, not_1_out, not_2_out, not_3_out,
       not_4_out, not_5_out, not_6_out, not_7_out, not_8_out, not_9_out, not_10_out, not_11_out, not_12_out,
       not_13_out, not_14_out, not_15_out, not_16_out, not_17_out, not_18_out, not_19_out, not_20_out,
       not_21_out, not_22_out, not_23_out, not_24_out, not_25_out, not_26_out, not_27_out, not_28_out,
       not_29_out, not_30_out, not_31_out, not_32_out, not_33_out, not_34_out, not_35_out, not_36_out,
       not_37_out, not_38_out, not_39_out, not_40_out;

  not not_1 (not_1_out, a);
  not not_2 (not_2_out, b);
  and and_1 (and_1_out, not_1_out, not_2_out, c);
  and and_2 (and_2_out, b, not_3_out);
  not not_3 (not_3_out, c);
  and and_3 (and_3_out, b, not_4_out);
  not not_4 (not_4_out, d);
  and and_4 (and_4_out, a, not_5_out);
  not not_5 (not_5_out, c);
  and and_5 (and_5_out, a, d);
  not not_6 (not_6_out, c);
  and and_6 (and_6_out, not_6_out, not_7_out);
  not not_7 (not_7_out, d);
  and and_7 (and_7_out, b, not_8_out);
  not not_8 (not_8_out, c);
  and and_8 (and_8_out, b, not_9_out);
  not not_9 (not_9_out, d);
  and and_9 (and_9_out, a, not_10_out);
  not not_10 (not_10_out, c);
  and and_10 (and_10_out, a, b);
  not not_11 (not_11_out, a);
  not not_12 (not_12_out, b);
  and and_11 (and_11_out, not_11_out, not_12_out, not_13_out);
  not not_13 (not_13_out, d);
  not not_14 (not_14_out, a);
  and and_12 (and_12_out, not_14_out, c);
  and and_13 (and_13_out, b, d);
  and and_14 (and_14_out, a, not_15_out);
  not not_15 (not_15_out, c);
  and and_15 (and_15_out, a, b);
  not not_16 (not_16_out, a);
  and and_16 (and_16_out, not_16_out, not_17_out);
  not not_17 (not_17_out, b);
  not not_18 (not_18_out, b);
  and and_17 (and_17_out, not_18_out, not_19_out);
  not not_19 (not_19_out, c);
  not not_20 (not_20_out, c);
  and and_18 (and_18_out, not_20_out, not_21_out);
  not not_21 (not_21_out, d);
  not not_22 (not_22_out, a);
  and and_19 (and_19_out, not_22_out, c, d);
  and and_20 (and_20_out, a, b);
  not not_23 (not_23_out, a);
  and and_21 (and_21_out, not_23_out, not_24_out, not_25_out);
  not not_24 (not_24_out, b);
  not not_25 (not_25_out, d);
  not not_26 (not_26_out, b);
  not not_27 (not_27_out, c);
  and and_22 (and_22_out, not_26_out, not_27_out, not_28_out);
  not not_28 (not_28_out, d);
  not not_29 (not_29_out, a);
  and and_23 (and_23_out, not_29_out, c, not_30_out);
  not not_30 (not_30_out, d);
  and and_24 (and_24_out, a, b);
  not not_31 (not_31_out, b);
  not not_32 (not_32_out, c);
  and and_25 (and_25_out, not_31_out, not_32_out, not_33_out);
  not not_33 (not_33_out, d);
  not not_34 (not_34_out, a);
  not not_35 (not_35_out, b);
  and and_26 (and_26_out, not_34_out, not_35_out, c);
  not not_36 (not_36_out, a);
  and and_27 (and_27_out, not_36_out, c, not_37_out);
  not not_37 (not_37_out, d);
  and and_28 (and_28_out, b, not_38_out, d);
  not not_38 (not_38_out, c);
  and and_29 (and_29_out, a, b);
  not not_39 (not_39_out, c);
  not not_40 (not_40_out, a);
  and and_30 (and_30_out, not_40_out, d);
  or or_1 (m, and_1_out, and_2_out, and_3_out, and_4_out, and_5_out);
  or or_2 (tl, and_6_out, and_7_out, and_8_out, and_9_out, and_10_out);
  or or_3 (t, and_11_out, and_12_out, and_13_out, and_14_out, and_15_out);
  or or_4 (tr, and_16_out, and_17_out, and_18_out, and_19_out, and_20_out);
  or or_5 (bl, and_21_out, and_22_out, and_23_out, and_24_out);
  or or_6 (b2, and_25_out, and_26_out, and_27_out, and_28_out, and_29_out);
  or or_7 (br, not_39_out, and_30_out, b);
endmodule

module RS_LATCH (
  input  L,
  input  I,
  input  in_3,
  output Q
);

  wire and_1_out, and_2_out, nand_1_out, nand_2_out, nand_4_out, not_1_out, not_2_out, or_1_out;

  and and_1 (and_1_out, Q, not_1_out);
  not not_1 (not_1_out, L);
  and and_2 (and_2_out, L, I);
  or or_1 (or_1_out, and_1_out, and_2_out);
  not not_2 (not_2_out, or_1_out);
  nand nand_1 (nand_1_out, or_1_out, in_3);
  nand nand_2 (nand_2_out, in_3, not_2_out);
  nand nand_3 (Q, nand_1_out, nand_4_out);
  nand nand_4 (nand_4_out, Q, nand_2_out);

  // Notes on the sheet:
  //   D
  //   Q'
endmodule

module ram_matrix (
  input  in_1,
  input  in_2,
  input  in_3,
  input  in_4,
  input  in_5,
  input  in_6,
  input  in_7,
  input  in_8,
  input  in_9
);

  wire and_2_out, and_4_out, and_6_out, and_8_out, and_10_out, and_12_out, and_14_out, and_16_out,
       and_26_out, and_28_out, and_30_out, and_32_out, and_34_out, and_36_out, and_38_out, and_40_out,
       and_50_out, and_52_out, and_54_out, and_56_out, and_58_out, and_60_out, and_62_out, and_64_out,
       and_74_out, and_76_out, and_78_out, and_80_out, and_82_out, and_84_out, and_86_out, and_88_out,
       and_92_out, and_98_out, and_99_out, and_101_out, and_103_out, and_105_out, and_107_out, and_109_out,
       and_111_out, and_113_out, and_116_out, and_122_out, and_123_out, and_125_out, and_126_out,
       and_128_out, and_129_out, and_131_out, and_132_out, and_134_out, and_135_out, and_137_out,
       and_138_out, and_140_out, and_141_out, and_143_out, and_144_out, and_146_out, and_147_out,
       and_149_out, and_150_out, and_152_out, and_153_out, and_155_out, and_156_out, and_158_out,
       and_159_out, and_161_out, and_162_out, and_164_out, and_165_out, and_167_out, and_168_out,
       and_170_out, and_173_out, and_176_out, and_179_out, and_182_out, and_185_out, and_188_out,
       and_191_out, clock_1_out, decoder_1_out0, decoder_1_out1, decoder_1_out2, decoder_1_out3,
       decoder_1_out4, decoder_1_out5, decoder_1_out6, decoder_1_out7, decoder_2_out0, decoder_2_out1,
       decoder_2_out2, decoder_2_out3, decoder_2_out6, decoder_2_out7, rs_latch_1_q, rs_latch_2_q,
       rs_latch_3_q, rs_latch_4_q, rs_latch_5_q, rs_latch_6_q, rs_latch_7_q, rs_latch_8_q, rs_latch_9_q,
       rs_latch_10_q, rs_latch_11_q, rs_latch_12_q, rs_latch_13_q, rs_latch_14_q, rs_latch_15_q,
       rs_latch_16_q, rs_latch_17_q, rs_latch_18_q, rs_latch_19_q, rs_latch_20_q, rs_latch_21_q,
       rs_latch_22_q, rs_latch_23_q, rs_latch_24_q, rs_latch_25_q, rs_latch_26_q, rs_latch_27_q,
       rs_latch_29_q, rs_latch_30_q, rs_latch_31_q, rs_latch_32_q, rs_latch_33_q, rs_latch_34_q,
       rs_latch_35_q, rs_latch_37_q, rs_latch_38_q, rs_latch_39_q, rs_latch_40_q, rs_latch_41_q,
       rs_latch_42_q, rs_latch_43_q, rs_latch_44_q, rs_latch_45_q, rs_latch_46_q, rs_latch_47_q,
       rs_latch_48_q, rs_latch_49_q, rs_latch_50_q, rs_latch_51_q, rs_latch_52_q, rs_latch_53_q,
       rs_latch_54_q, rs_latch_55_q, rs_latch_56_q, rs_latch_57_q, rs_latch_58_q, rs_latch_59_q,
       rs_latch_60_q, rs_latch_61_q, rs_latch_62_q, rs_latch_63_q, rs_latch_64_q, transistor_1_out,
       transistor_2_out, transistor_3_out, transistor_4_out, transistor_5_out, transistor_6_out,
       transistor_7_out, transistor_8_out, transistor_9_out, transistor_10_out, transistor_11_out,
       transistor_12_out, transistor_13_out, transistor_14_out, transistor_15_out, transistor_16_out,
       transistor_17_out, transistor_18_out, transistor_19_out, transistor_20_out, transistor_21_out,
       transistor_22_out, transistor_23_out, transistor_24_out, transistor_25_out, transistor_26_out,
       transistor_27_out, transistor_28_out, transistor_29_out, transistor_30_out, transistor_31_out,
       transistor_32_out, transistor_33_out, transistor_35_out, transistor_36_out, transistor_37_out,
       transistor_38_out, transistor_39_out, transistor_40_out, transistor_57_out, transistor_58_out,
       transistor_59_out, transistor_60_out, transistor_61_out, transistor_62_out, transistor_63_out,
       transistor_64_out;

  Decoder #(.select(3)) decoder_1 (
    .out0(decoder_1_out0), .out1(decoder_1_out1), .out2(decoder_1_out2), .out3(decoder_1_out3),
    .out4(decoder_1_out4), .out5(decoder_1_out5), .out6(decoder_1_out6), .out7(decoder_1_out7),
    .sel({in_1, in_2, in_3}));  // open: en
  and and_1 (in_7, in_9, and_2_out);
  and and_2 (and_2_out, decoder_1_out0, decoder_2_out0);
  and and_3 (in_7, in_9, and_4_out);
  and and_4 (and_4_out, decoder_1_out1, decoder_2_out0);
  and and_5 (in_7, in_9, and_6_out);
  and and_6 (and_6_out, decoder_1_out2, decoder_2_out0);
  and and_7 (in_7, in_9, and_8_out);
  and and_8 (and_8_out, decoder_1_out3, decoder_2_out0);
  and and_9 (in_7, in_9, and_10_out);
  and and_10 (and_10_out, decoder_1_out4, decoder_2_out0);
  and and_11 (in_7, in_9, and_12_out);
  and and_12 (and_12_out, decoder_1_out5, decoder_2_out0);
  and and_13 (in_7, in_9, and_14_out);
  and and_14 (and_14_out, decoder_1_out6, decoder_2_out0);
  and and_15 (in_7, in_9, and_16_out);
  and and_16 (and_16_out, decoder_1_out7, decoder_2_out0);
  Transistor transistor_1 (.in(rs_latch_1_q), .out(transistor_1_out), .gate(in_7));
  LED led_1 (.in(rs_latch_1_q));
  RS_LATCH rs_latch_1 (.L(in_7), .I(in_7), .in_3(clock_1_out), .Q(rs_latch_1_q));
  and and_17 (transistor_1_out, and_2_out, in_8);
  Transistor transistor_2 (.in(rs_latch_2_q), .out(transistor_2_out), .gate(in_7));
  RS_LATCH rs_latch_2 (.L(in_7), .I(in_7), .in_3(clock_1_out), .Q(rs_latch_2_q));
  LED led_2 (.in(rs_latch_2_q));
  and and_18 (transistor_2_out, and_4_out, in_8);
  Transistor transistor_3 (.in(rs_latch_3_q), .out(transistor_3_out), .gate(in_7));
  LED led_3 (.in(rs_latch_3_q));
  RS_LATCH rs_latch_3 (.L(in_7), .I(in_7), .in_3(clock_1_out), .Q(rs_latch_3_q));
  and and_19 (transistor_3_out, and_6_out, in_8);
  Transistor transistor_4 (.in(rs_latch_4_q), .out(transistor_4_out), .gate(in_7));
  RS_LATCH rs_latch_4 (.L(in_7), .I(in_7), .in_3(clock_1_out), .Q(rs_latch_4_q));
  LED led_4 (.in(rs_latch_4_q));
  and and_20 (transistor_4_out, and_8_out, in_8);
  Transistor transistor_5 (.in(rs_latch_5_q), .out(transistor_5_out), .gate(in_7));
  LED led_5 (.in(rs_latch_5_q));
  RS_LATCH rs_latch_5 (.L(in_7), .I(in_7), .in_3(clock_1_out), .Q(rs_latch_5_q));
  and and_21 (transistor_5_out, and_10_out, in_8);
  Transistor transistor_6 (.in(rs_latch_6_q), .out(transistor_6_out), .gate(in_7));
  RS_LATCH rs_latch_6 (.L(in_7), .I(in_7), .in_3(clock_1_out), .Q(rs_latch_6_q));
  LED led_6 (.in(rs_latch_6_q));
  and and_22 (transistor_6_out, and_12_out, in_8);
  Transistor transistor_7 (.in(rs_latch_7_q), .out(transistor_7_out), .gate(in_7));
  LED led_7 (.in(rs_latch_7_q));
  RS_LATCH rs_latch_7 (.L(in_7), .I(in_7), .in_3(clock_1_out), .Q(rs_latch_7_q));
  and and_23 (transistor_7_out, and_14_out, in_8);
  Transistor transistor_8 (.in(rs_latch_8_q), .out(transistor_8_out), .gate(in_7));
  RS_LATCH rs_latch_8 (.L(in_7), .I(in_7), .in_3(clock_1_out), .Q(rs_latch_8_q));
  LED led_8 (.in(rs_latch_8_q));
  and and_24 (transistor_8_out, and_16_out, in_8);
  and and_25 (in_7, in_9, and_26_out);
  and and_26 (and_26_out, decoder_1_out0, decoder_2_out1);
  and and_27 (in_7, in_9, and_28_out);
  and and_28 (and_28_out, decoder_1_out1, decoder_2_out1);
  and and_29 (in_7, in_9, and_30_out);
  and and_30 (and_30_out, decoder_1_out2, decoder_2_out1);
  and and_31 (in_7, in_9, and_32_out);
  and and_32 (and_32_out, decoder_1_out3, decoder_2_out1);
  and and_33 (in_7, in_9, and_34_out);
  and and_34 (and_34_out, decoder_1_out4, decoder_2_out1);
  and and_35 (in_7, in_9, and_36_out);
  and and_36 (and_36_out, decoder_1_out5, decoder_2_out1);
  and and_37 (in_7, in_9, and_38_out);
  and and_38 (and_38_out, decoder_1_out6, decoder_2_out1);
  and and_39 (in_7, in_9, and_40_out);
  and and_40 (and_40_out, decoder_1_out7, decoder_2_out1);
  LED led_9 (.in(in_7));
  Transistor transistor_9 (.in(rs_latch_9_q), .out(transistor_9_out), .gate(in_7));
  RS_LATCH rs_latch_9 (.L(in_7), .I(in_7), .in_3(clock_1_out), .Q(rs_latch_9_q));
  LED led_10 (.in(rs_latch_9_q));
  and and_41 (transistor_9_out, and_26_out, in_8);
  Transistor transistor_10 (.in(rs_latch_10_q), .out(transistor_10_out), .gate(in_7));
  RS_LATCH rs_latch_10 (.L(in_7), .I(in_7), .in_3(clock_1_out), .Q(rs_latch_10_q));
  LED led_11 (.in(rs_latch_10_q));
  and and_42 (transistor_10_out, and_28_out, in_8);
  Transistor transistor_11 (.in(rs_latch_11_q), .out(transistor_11_out), .gate(in_7));
  LED led_12 (.in(rs_latch_11_q));
  RS_LATCH rs_latch_11 (.L(in_7), .I(in_7), .in_3(clock_1_out), .Q(rs_latch_11_q));
  and and_43 (transistor_11_out, and_30_out, in_8);
  Transistor transistor_12 (.in(rs_latch_12_q), .out(transistor_12_out), .gate(in_7));
  LED led_13 (.in(rs_latch_12_q));
  RS_LATCH rs_latch_12 (.L(in_7), .I(in_7), .in_3(clock_1_out), .Q(rs_latch_12_q));
  and and_44 (transistor_12_out, and_32_out, in_8);
  Transistor transistor_13 (.in(rs_latch_13_q), .out(transistor_13_out), .gate(in_7));
  LED led_14 (.in(rs_latch_13_q));
  RS_LATCH rs_latch_13 (.L(in_7), .I(in_7), .in_3(clock_1_out), .Q(rs_latch_13_q));
  and and_45 (transistor_13_out, and_34_out, in_8);
  Transistor transistor_14 (.in(rs_latch_14_q), .out(transistor_14_out), .gate(in_7));
  RS_LATCH rs_latch_14 (.L(in_7), .I(in_7), .in_3(clock_1_out), .Q(rs_latch_14_q));
  LED led_15 (.in(rs_latch_14_q));
  and and_46 (transistor_14_out, and_36_out, in_8);
  Transistor transistor_15 (.in(rs_latch_15_q), .out(transistor_15_out), .gate(in_7));
  RS_LATCH rs_latch_15 (.L(in_7), .I(in_7), .in_3(clock_1_out), .Q(rs_latch_15_q));
  LED led_16 (.in(rs_latch_15_q));
  and and_47 (transistor_15_out, and_38_out, in_8);
  Transistor transistor_16 (.in(rs_latch_16_q), .out(transistor_16_out), .gate(in_7));
  LED led_17 (.in(rs_latch_16_q));
  RS_LATCH rs_latch_16 (.L(in_7), .I(in_7), .in_3(clock_1_out), .Q(rs_latch_16_q));
  and and_48 (transistor_16_out, and_40_out, in_8);
  and and_49 (in_7, in_9, and_50_out);
  and and_50 (and_50_out, decoder_1_out0, decoder_2_out2);
  and and_51 (in_7, in_9, and_52_out);
  and and_52 (and_52_out, decoder_1_out1, decoder_2_out2);
  and and_53 (in_7, in_9, and_54_out);
  and and_54 (and_54_out, decoder_1_out2, decoder_2_out2);
  and and_55 (in_7, in_9, and_56_out);
  and and_56 (and_56_out, decoder_1_out3, decoder_2_out2);
  and and_57 (in_7, in_9, and_58_out);
  and and_58 (and_58_out, decoder_1_out4, decoder_2_out2);
  and and_59 (in_7, in_9, and_60_out);
  and and_60 (and_60_out, decoder_1_out5, decoder_2_out2);
  and and_61 (in_7, in_9, and_62_out);
  and and_62 (and_62_out, decoder_1_out6, decoder_2_out2);
  and and_63 (in_7, in_9, and_64_out);
  and and_64 (and_64_out, decoder_1_out7, decoder_2_out2);
  Transistor transistor_17 (.in(rs_latch_17_q), .out(transistor_17_out), .gate(in_7));
  RS_LATCH rs_latch_17 (.L(in_7), .I(in_7), .in_3(clock_1_out), .Q(rs_latch_17_q));
  LED led_18 (.in(rs_latch_17_q));
  and and_65 (transistor_17_out, and_50_out, in_8);
  Transistor transistor_18 (.in(rs_latch_18_q), .out(transistor_18_out), .gate(in_7));
  RS_LATCH rs_latch_18 (.L(in_7), .I(in_7), .in_3(clock_1_out), .Q(rs_latch_18_q));
  LED led_19 (.in(rs_latch_18_q));
  and and_66 (transistor_18_out, and_52_out, in_8);
  Transistor transistor_19 (.in(rs_latch_19_q), .out(transistor_19_out), .gate(in_7));
  LED led_20 (.in(rs_latch_19_q));
  RS_LATCH rs_latch_19 (.L(in_7), .I(in_7), .in_3(clock_1_out), .Q(rs_latch_19_q));
  and and_67 (transistor_19_out, and_54_out, in_8);
  Transistor transistor_20 (.in(rs_latch_20_q), .out(transistor_20_out), .gate(in_7));
  RS_LATCH rs_latch_20 (.L(in_7), .I(in_7), .in_3(clock_1_out), .Q(rs_latch_20_q));
  LED led_21 (.in(rs_latch_20_q));
  and and_68 (transistor_20_out, and_56_out, in_8);
  Transistor transistor_21 (.in(rs_latch_21_q), .out(transistor_21_out), .gate(in_7));
  LED led_22 (.in(rs_latch_21_q));
  RS_LATCH rs_latch_21 (.L(in_7), .I(in_7), .in_3(clock_1_out), .Q(rs_latch_21_q));
  and and_69 (transistor_21_out, and_58_out, in_8);
  Transistor transistor_22 (.in(rs_latch_22_q), .out(transistor_22_out), .gate(in_7));
  RS_LATCH rs_latch_22 (.L(in_7), .I(in_7), .in_3(clock_1_out), .Q(rs_latch_22_q));
  LED led_23 (.in(rs_latch_22_q));
  and and_70 (transistor_22_out, and_60_out, in_8);
  Transistor transistor_23 (.in(rs_latch_23_q), .out(transistor_23_out), .gate(in_7));
  LED led_24 (.in(rs_latch_23_q));
  RS_LATCH rs_latch_23 (.L(in_7), .I(in_7), .in_3(clock_1_out), .Q(rs_latch_23_q));
  and and_71 (transistor_23_out, and_62_out, in_8);
  Transistor transistor_24 (.in(rs_latch_24_q), .out(transistor_24_out), .gate(in_7));
  LED led_25 (.in(rs_latch_24_q));
  RS_LATCH rs_latch_24 (.L(in_7), .I(in_7), .in_3(clock_1_out), .Q(rs_latch_24_q));
  and and_72 (transistor_24_out, and_64_out, in_8);
  Decoder #(.select(3)) decoder_2 (
    .out0(decoder_2_out0), .out1(decoder_2_out1), .out2(decoder_2_out2), .out3(decoder_2_out3), .out4(in_7),
    .out5(in_7), .out6(decoder_2_out6), .out7(decoder_2_out7), .sel({in_4, in_5, in_6}));  // open: en
  and and_73 (in_7, in_9, and_74_out);
  and and_74 (and_74_out, decoder_1_out0, decoder_2_out3);
  and and_75 (in_7, in_9, and_76_out);
  and and_76 (and_76_out, decoder_1_out1, decoder_2_out3);
  and and_77 (in_7, in_9, and_78_out);
  and and_78 (and_78_out, decoder_1_out2, decoder_2_out3);
  and and_79 (in_7, in_9, and_80_out);
  Transistor transistor_25 (.in(and_92_out), .out(transistor_25_out), .gate(in_7));
  and and_80 (and_80_out, decoder_1_out3, decoder_2_out3);
  and and_81 (in_7, in_9, and_82_out);
  and and_82 (and_82_out, decoder_1_out4, decoder_2_out3);
  and and_83 (in_7, in_9, and_84_out);
  and and_84 (and_84_out, decoder_1_out5, decoder_2_out3);
  and and_85 (in_7, in_9, and_86_out);
  and and_86 (and_86_out, decoder_1_out6, decoder_2_out3);
  and and_87 (in_7, in_9, and_88_out);
  and and_88 (and_88_out, decoder_1_out7, decoder_2_out3);
  Transistor transistor_26 (.in(rs_latch_25_q), .out(transistor_26_out), .gate(in_7));
  LED led_26 (.in(rs_latch_25_q));
  RS_LATCH rs_latch_25 (.L(in_7), .I(in_7), .in_3(clock_1_out), .Q(rs_latch_25_q));
  and and_89 (transistor_26_out, and_74_out, in_8);
  Transistor transistor_27 (.in(rs_latch_26_q), .out(transistor_27_out), .gate(in_7));
  LED led_27 (.in(rs_latch_26_q));
  RS_LATCH rs_latch_26 (.L(in_7), .I(in_7), .in_3(clock_1_out), .Q(rs_latch_26_q));
  and and_90 (transistor_27_out, and_76_out, in_8);
  Transistor transistor_28 (.in(rs_latch_27_q), .out(transistor_28_out), .gate(in_7));
  RS_LATCH rs_latch_27 (.L(in_7), .I(in_7), .in_3(clock_1_out), .Q(rs_latch_27_q));
  LED led_28 (.in(rs_latch_27_q));
  and and_91 (transistor_28_out, and_78_out, in_8);
  RS_LATCH rs_latch_28 (.L(in_7), .I(in_7), .in_3(clock_1_out), .Q(transistor_25_out));
  LED led_29 (.in(transistor_25_out));
  and and_92 (and_92_out, and_80_out, in_8);
  Transistor transistor_29 (.in(rs_latch_29_q), .out(transistor_29_out), .gate(in_7));
  LED led_30 (.in(rs_latch_29_q));
  RS_LATCH rs_latch_29 (.L(in_7), .I(in_7), .in_3(clock_1_out), .Q(rs_latch_29_q));
  and and_93 (transistor_29_out, and_82_out, in_8);
  Transistor transistor_30 (.in(rs_latch_30_q), .out(transistor_30_out), .gate(in_7));
  LED led_31 (.in(rs_latch_30_q));
  RS_LATCH rs_latch_30 (.L(in_7), .I(in_7), .in_3(clock_1_out), .Q(rs_latch_30_q));
  and and_94 (transistor_30_out, and_84_out, in_8);
  Transistor transistor_31 (.in(rs_latch_31_q), .out(transistor_31_out), .gate(in_7));
  RS_LATCH rs_latch_31 (.L(in_7), .I(in_7), .in_3(clock_1_out), .Q(rs_latch_31_q));
  LED led_32 (.in(rs_latch_31_q));
  and and_95 (transistor_31_out, and_86_out, in_8);
  Transistor transistor_32 (.in(rs_latch_32_q), .out(transistor_32_out), .gate(in_7));
  RS_LATCH rs_latch_32 (.L(in_7), .I(in_7), .in_3(clock_1_out), .Q(rs_latch_32_q));
  LED led_33 (.in(rs_latch_32_q));
  and and_96 (transistor_32_out, and_88_out, in_8);
  and and_97 (in_7, in_9, and_98_out);
  and and_98 (and_98_out, decoder_1_out0, in_7);
  and and_99 (and_99_out, and_98_out, in_8);
  and and_100 (in_7, in_9, and_101_out);
  and and_101 (and_101_out, decoder_1_out1, in_7);
  and and_102 (in_7, in_9, and_103_out);
  and and_103 (and_103_out, decoder_1_out2, in_7);
  and and_104 (in_7, in_9, and_105_out);
  Transistor transistor_33 (.in(and_116_out), .out(transistor_33_out), .gate(in_7));
  and and_105 (and_105_out, decoder_1_out3, in_7);
  and and_106 (in_7, in_9, and_107_out);
  and and_107 (and_107_out, decoder_1_out4, in_7);
  and and_108 (in_7, in_9, and_109_out);
  and and_109 (and_109_out, decoder_1_out5, in_7);
  and and_110 (in_7, in_9, and_111_out);
  and and_111 (and_111_out, decoder_1_out6, in_7);
  and and_112 (in_7, in_9, and_113_out);
  and and_113 (and_113_out, decoder_1_out7, in_7);
  Transistor transistor_34 (.in(rs_latch_33_q), .out(and_99_out), .gate(in_7));
  RS_LATCH rs_latch_33 (.L(in_7), .I(in_7), .in_3(clock_1_out), .Q(rs_latch_33_q));
  LED led_34 (.in(rs_latch_33_q));
  Transistor transistor_35 (.in(rs_latch_34_q), .out(transistor_35_out), .gate(in_7));
  RS_LATCH rs_latch_34 (.L(in_7), .I(in_7), .in_3(clock_1_out), .Q(rs_latch_34_q));
  LED led_35 (.in(rs_latch_34_q));
  and and_114 (transistor_35_out, and_101_out, in_8);
  Transistor transistor_36 (.in(rs_latch_35_q), .out(transistor_36_out), .gate(in_7));
  RS_LATCH rs_latch_35 (.L(in_7), .I(in_7), .in_3(clock_1_out), .Q(rs_latch_35_q));
  LED led_36 (.in(rs_latch_35_q));
  and and_115 (transistor_36_out, and_103_out, in_8);
  RS_LATCH rs_latch_36 (.L(in_7), .I(in_7), .in_3(clock_1_out), .Q(transistor_33_out));
  LED led_37 (.in(transistor_33_out));
  and and_116 (and_116_out, and_105_out, in_8);
  Transistor transistor_37 (.in(rs_latch_37_q), .out(transistor_37_out), .gate(in_7));
  RS_LATCH rs_latch_37 (.L(in_7), .I(in_7), .in_3(clock_1_out), .Q(rs_latch_37_q));
  LED led_38 (.in(rs_latch_37_q));
  and and_117 (transistor_37_out, and_107_out, in_8);
  Transistor transistor_38 (.in(rs_latch_38_q), .out(transistor_38_out), .gate(in_7));
  LED led_39 (.in(rs_latch_38_q));
  RS_LATCH rs_latch_38 (.L(in_7), .I(in_7), .in_3(clock_1_out), .Q(rs_latch_38_q));
  and and_118 (transistor_38_out, and_109_out, in_8);
  Transistor transistor_39 (.in(rs_latch_39_q), .out(transistor_39_out), .gate(in_7));
  RS_LATCH rs_latch_39 (.L(in_7), .I(in_7), .in_3(clock_1_out), .Q(rs_latch_39_q));
  LED led_40 (.in(rs_latch_39_q));
  and and_119 (transistor_39_out, and_111_out, in_8);
  Transistor transistor_40 (.in(rs_latch_40_q), .out(transistor_40_out), .gate(in_7));
  LED led_41 (.in(rs_latch_40_q));
  RS_LATCH rs_latch_40 (.L(in_7), .I(in_7), .in_3(clock_1_out), .Q(rs_latch_40_q));
  and and_120 (transistor_40_out, and_113_out, in_8);
  and and_121 (in_7, in_9, and_122_out);
  and and_122 (and_122_out, decoder_1_out0, in_7);
  and and_123 (and_123_out, and_122_out, in_8);
  and and_124 (in_7, in_9, and_125_out);
  and and_125 (and_125_out, decoder_1_out1, in_7);
  and and_126 (and_126_out, and_125_out, in_8);
  and and_127 (in_7, in_9, and_128_out);
  and and_128 (and_128_out, decoder_1_out2, in_7);
  and and_129 (and_129_out, and_128_out, in_8);
  and and_130 (in_7, in_9, and_131_out);
  and and_131 (and_131_out, decoder_1_out3, in_7);
  and and_132 (and_132_out, and_131_out, in_8);
  and and_133 (in_7, in_9, and_134_out);
  and and_134 (and_134_out, decoder_1_out4, in_7);
  and and_135 (and_135_out, and_134_out, in_8);
  and and_136 (in_7, in_9, and_137_out);
  and and_137 (and_137_out, decoder_1_out5, in_7);
  and and_138 (and_138_out, and_137_out, in_8);
  and and_139 (in_7, in_9, and_140_out);
  and and_140 (and_140_out, decoder_1_out6, in_7);
  and and_141 (and_141_out, and_140_out, in_8);
  and and_142 (in_7, in_9, and_143_out);
  and and_143 (and_143_out, decoder_1_out7, in_7);
  and and_144 (and_144_out, and_143_out, in_8);
  Transistor transistor_41 (.in(rs_latch_41_q), .out(and_123_out), .gate(in_7));
  RS_LATCH rs_latch_41 (.L(in_7), .I(in_7), .in_3(clock_1_out), .Q(rs_latch_41_q));
  LED led_42 (.in(rs_latch_41_q));
  Transistor transistor_42 (.in(rs_latch_42_q), .out(and_126_out), .gate(in_7));
  RS_LATCH rs_latch_42 (.L(in_7), .I(in_7), .in_3(clock_1_out), .Q(rs_latch_42_q));
  LED led_43 (.in(rs_latch_42_q));
  Transistor transistor_43 (.in(rs_latch_43_q), .out(and_129_out), .gate(in_7));
  LED led_44 (.in(rs_latch_43_q));
  RS_LATCH rs_latch_43 (.L(in_7), .I(in_7), .in_3(clock_1_out), .Q(rs_latch_43_q));
  Transistor transistor_44 (.in(rs_latch_44_q), .out(and_132_out), .gate(in_7));
  RS_LATCH rs_latch_44 (.L(in_7), .I(in_7), .in_3(clock_1_out), .Q(rs_latch_44_q));
  LED led_45 (.in(rs_latch_44_q));
  Transistor transistor_45 (.in(rs_latch_45_q), .out(and_135_out), .gate(in_7));
  LED led_46 (.in(rs_latch_45_q));
  RS_LATCH rs_latch_45 (.L(in_7), .I(in_7), .in_3(clock_1_out), .Q(rs_latch_45_q));
  Transistor transistor_46 (.in(rs_latch_46_q), .out(and_138_out), .gate(in_7));
  LED led_47 (.in(rs_latch_46_q));
  RS_LATCH rs_latch_46 (.L(in_7), .I(in_7), .in_3(clock_1_out), .Q(rs_latch_46_q));
  Transistor transistor_47 (.in(rs_latch_47_q), .out(and_141_out), .gate(in_7));
  RS_LATCH rs_latch_47 (.L(in_7), .I(in_7), .in_3(clock_1_out), .Q(rs_latch_47_q));
  LED led_48 (.in(rs_latch_47_q));
  Transistor transistor_48 (.in(rs_latch_48_q), .out(and_144_out), .gate(in_7));
  RS_LATCH rs_latch_48 (.L(in_7), .I(in_7), .in_3(clock_1_out), .Q(rs_latch_48_q));
  LED led_49 (.in(rs_latch_48_q));
  and and_145 (in_7, in_9, and_146_out);
  RS_LATCH rs_latch_49 (.L(in_7), .I(in_7), .in_3(clock_1_out), .Q(rs_latch_49_q));
  LED led_50 (.in(rs_latch_49_q));
  and and_146 (and_146_out, decoder_1_out0, decoder_2_out6);
  and and_147 (and_147_out, and_146_out, in_8);
  and and_148 (in_7, in_9, and_149_out);
  RS_LATCH rs_latch_50 (.L(in_7), .I(in_7), .in_3(clock_1_out), .Q(rs_latch_50_q));
  LED led_51 (.in(rs_latch_50_q));
  and and_149 (and_149_out, decoder_1_out1, decoder_2_out6);
  and and_150 (and_150_out, and_149_out, in_8);
  and and_151 (in_7, in_9, and_152_out);
  LED led_52 (.in(rs_latch_51_q));
  RS_LATCH rs_latch_51 (.L(in_7), .I(in_7), .in_3(clock_1_out), .Q(rs_latch_51_q));
  and and_152 (and_152_out, decoder_1_out2, decoder_2_out6);
  and and_153 (and_153_out, and_152_out, in_8);
  and and_154 (in_7, in_9, and_155_out);
  RS_LATCH rs_latch_52 (.L(in_7), .I(in_7), .in_3(clock_1_out), .Q(rs_latch_52_q));
  LED led_53 (.in(rs_latch_52_q));
  and and_155 (and_155_out, decoder_1_out3, decoder_2_out6);
  and and_156 (and_156_out, and_155_out, in_8);
  and and_157 (in_7, in_9, and_158_out);
  RS_LATCH rs_latch_53 (.L(in_7), .I(in_7), .in_3(clock_1_out), .Q(rs_latch_53_q));
  LED led_54 (.in(rs_latch_53_q));
  and and_158 (and_158_out, decoder_1_out4, decoder_2_out6);
  and and_159 (and_159_out, and_158_out, in_8);
  and and_160 (in_7, in_9, and_161_out);
  RS_LATCH rs_latch_54 (.L(in_7), .I(in_7), .in_3(clock_1_out), .Q(rs_latch_54_q));
  LED led_55 (.in(rs_latch_54_q));
  and and_161 (and_161_out, decoder_1_out5, decoder_2_out6);
  and and_162 (and_162_out, and_161_out, in_8);
  and and_163 (in_7, in_9, and_164_out);
  LED led_56 (.in(rs_latch_55_q));
  RS_LATCH rs_latch_55 (.L(in_7), .I(in_7), .in_3(clock_1_out), .Q(rs_latch_55_q));
  and and_164 (and_164_out, decoder_1_out6, decoder_2_out6);
  and and_165 (and_165_out, and_164_out, in_8);
  and and_166 (in_7, in_9, and_167_out);
  LED led_57 (.in(rs_latch_56_q));
  RS_LATCH rs_latch_56 (.L(in_7), .I(in_7), .in_3(clock_1_out), .Q(rs_latch_56_q));
  and and_167 (and_167_out, decoder_1_out7, decoder_2_out6);
  and and_168 (and_168_out, and_167_out, in_8);
  Transistor transistor_49 (.in(rs_latch_49_q), .out(and_147_out), .gate(in_7));
  Transistor transistor_50 (.in(rs_latch_50_q), .out(and_150_out), .gate(in_7));
  Transistor transistor_51 (.in(rs_latch_51_q), .out(and_153_out), .gate(in_7));
  Transistor transistor_52 (.in(rs_latch_52_q), .out(and_156_out), .gate(in_7));
  Transistor transistor_53 (.in(rs_latch_53_q), .out(and_159_out), .gate(in_7));
  Transistor transistor_54 (.in(rs_latch_54_q), .out(and_162_out), .gate(in_7));
  Transistor transistor_55 (.in(rs_latch_55_q), .out(and_165_out), .gate(in_7));
  Transistor transistor_56 (.in(rs_latch_56_q), .out(and_168_out), .gate(in_7));
  Clock clock_1 (.out(clock_1_out));
  Transistor transistor_57 (.in(rs_latch_57_q), .out(transistor_57_out), .gate(in_7));
  and and_169 (in_7, in_9, and_170_out);
  RS_LATCH rs_latch_57 (.L(in_7), .I(in_7), .in_3(clock_1_out), .Q(rs_latch_57_q));
  LED led_58 (.in(rs_latch_57_q));
  and and_170 (and_170_out, decoder_1_out0, decoder_2_out7);
  and and_171 (transistor_57_out, and_170_out, in_8);
  Transistor transistor_58 (.in(rs_latch_58_q), .out(transistor_58_out), .gate(in_7));
  and and_172 (in_7, in_9, and_173_out);
  LED led_59 (.in(rs_latch_58_q));
  RS_LATCH rs_latch_58 (.L(in_7), .I(in_7), .in_3(clock_1_out), .Q(rs_latch_58_q));
  and and_173 (and_173_out, decoder_1_out1, decoder_2_out7);
  and and_174 (transistor_58_out, and_173_out, in_8);
  Transistor transistor_59 (.in(rs_latch_59_q), .out(transistor_59_out), .gate(in_7));
  and and_175 (in_7, in_9, and_176_out);
  RS_LATCH rs_latch_59 (.L(in_7), .I(in_7), .in_3(clock_1_out), .Q(rs_latch_59_q));
  LED led_60 (.in(rs_latch_59_q));
  and and_176 (and_176_out, decoder_1_out2, decoder_2_out7);
  and and_177 (transistor_59_out, and_176_out, in_8);
  and and_178 (in_7, in_9, and_179_out);
  Transistor transistor_60 (.in(rs_latch_60_q), .out(transistor_60_out), .gate(in_7));
  RS_LATCH rs_latch_60 (.L(in_7), .I(in_7), .in_3(clock_1_out), .Q(rs_latch_60_q));
  LED led_61 (.in(rs_latch_60_q));
  and and_179 (and_179_out, decoder_1_out3, decoder_2_out7);
  and and_180 (transistor_60_out, and_179_out, in_8);
  and and_181 (in_7, in_9, and_182_out);
  Transistor transistor_61 (.in(rs_latch_61_q), .out(transistor_61_out), .gate(in_7));
  RS_LATCH rs_latch_61 (.L(in_7), .I(in_7), .in_3(clock_1_out), .Q(rs_latch_61_q));
  LED led_62 (.in(rs_latch_61_q));
  and and_182 (and_182_out, decoder_1_out4, decoder_2_out7);
  and and_183 (transistor_61_out, and_182_out, in_8);
  and and_184 (in_7, in_9, and_185_out);
  Transistor transistor_62 (.in(rs_latch_62_q), .out(transistor_62_out), .gate(in_7));
  LED led_63 (.in(rs_latch_62_q));
  RS_LATCH rs_latch_62 (.L(in_7), .I(in_7), .in_3(clock_1_out), .Q(rs_latch_62_q));
  and and_185 (and_185_out, decoder_1_out5, decoder_2_out7);
  and and_186 (transistor_62_out, and_185_out, in_8);
  and and_187 (in_7, in_9, and_188_out);
  Transistor transistor_63 (.in(rs_latch_63_q), .out(transistor_63_out), .gate(in_7));
  LED led_64 (.in(rs_latch_63_q));
  RS_LATCH rs_latch_63 (.L(in_7), .I(in_7), .in_3(clock_1_out), .Q(rs_latch_63_q));
  and and_188 (and_188_out, decoder_1_out6, decoder_2_out7);
  and and_189 (transistor_63_out, and_188_out, in_8);
  and and_190 (in_7, in_9, and_191_out);
  Transistor transistor_64 (.in(rs_latch_64_q), .out(transistor_64_out), .gate(in_7));
  LED led_65 (.in(rs_latch_64_q));
  RS_LATCH rs_latch_64 (.L(in_7), .I(in_7), .in_3(clock_1_out), .Q(rs_latch_64_q));
  and and_191 (and_191_out, decoder_1_out7, decoder_2_out7);
  and and_192 (transistor_64_out, and_191_out, in_8);

  // Notes on the sheet:
  //   3x4
  //   R
  //   C
  //   r
  //   w
endmodule

module ram_matrix_64bits (
  input  in_1,
  input  in_2,
  input  in_3,
  input  in_4,
  input  in_5,
  input  in_6,
  input  in_7,
  input  R,
  input  W,
  input  in_10
);

  wire clock_1_out, decoder_1_out0, decoder_1_out1, decoder_1_out2, decoder_1_out3, decoder_1_out4,
       decoder_1_out5, decoder_1_out6, decoder_1_out7, decoder_2_out0, decoder_2_out1, decoder_2_out2,
       decoder_2_out3, decoder_2_out4, decoder_2_out5, decoder_2_out6, decoder_2_out7, mem_bit_1_out_7,
       mem_bit_2_out_7, mem_bit_3_out_7, mem_bit_4_out_7, mem_bit_5_out_7, mem_bit_6_out_7, mem_bit_7_out_7,
       mem_bit_8_out_7, mem_bit_9_out_7, mem_bit_10_out_7, mem_bit_11_out_7, transistor_8_out,
       transistor_9_out, transistor_10_out, transistor_11_out, undriven, undriven_2, undriven_3, undriven_4,
       undriven_5, undriven_6, undriven_7, undriven_8, undriven_9, undriven_10, undriven_11;

  Decoder #(.select(3)) decoder_1 (
    .out0(decoder_1_out0), .out1(decoder_1_out1), .out2(decoder_1_out2), .out3(decoder_1_out3),
    .out4(decoder_1_out4), .out5(decoder_1_out5), .out6(decoder_1_out6), .out7(decoder_1_out7),
    .sel({in_1, in_2, in_3}));  // open: en
  Transistor #(.\type ("n")) transistor_1 (.in(mem_bit_1_out_7), .out(in_7), .gate(R));
  Transistor #(.\type ("n")) transistor_2 (.in(mem_bit_2_out_7), .out(in_7), .gate(R));
  mem_bit mem_bit_1 (
    .Write(W), .X(decoder_2_out0), .reset(in_10), .out_7(mem_bit_1_out_7), .Y(decoder_1_out0),
    .Clock(clock_1_out), .Data(in_7));
  LED led_1 (.in(mem_bit_1_out_7));
  LED led_2 (.in(mem_bit_2_out_7));
  mem_bit mem_bit_2 (
    .Write(W), .X(decoder_2_out0), .reset(in_10), .out_7(mem_bit_2_out_7), .Y(decoder_1_out1),
    .Clock(clock_1_out), .Data(in_7));
  Transistor #(.\type ("n")) transistor_3 (.in(mem_bit_3_out_7), .out(in_7), .gate(R));
  mem_bit mem_bit_3 (
    .Write(W), .X(decoder_2_out1), .reset(in_10), .out_7(mem_bit_3_out_7), .Y(decoder_1_out0),
    .Clock(clock_1_out), .Data(in_7));
  LED led_3 (.in(mem_bit_3_out_7));
  Transistor #(.\type ("n")) transistor_4 (.in(mem_bit_4_out_7), .out(in_7), .gate(R));
  LED led_4 (.in(mem_bit_4_out_7));
  mem_bit mem_bit_4 (
    .Write(W), .X(decoder_2_out1), .reset(in_10), .out_7(mem_bit_4_out_7), .Y(decoder_1_out1), .Clock(W),
    .Data(in_7));
  LED led_5 (.in(in_7));
  Transistor #(.\type ("n")) transistor_5 (.in(mem_bit_5_out_7), .out(in_7), .gate(R));
  mem_bit mem_bit_5 (
    .Write(W), .X(decoder_2_out2), .reset(in_10), .out_7(mem_bit_5_out_7), .Data(in_7));  // open: Y, Clock
  LED led_6 (.in(mem_bit_5_out_7));
  Transistor #(.\type ("n")) transistor_6 (.in(mem_bit_6_out_7), .out(in_7), .gate(R));
  LED led_7 (.in(mem_bit_6_out_7));
  mem_bit mem_bit_6 (
    .Write(W), .X(decoder_2_out2), .reset(in_10), .out_7(mem_bit_6_out_7), .Y(decoder_1_out1),
    .Clock(clock_1_out), .Data(in_7));
  Clock clock_1 (.out(clock_1_out));
  Decoder #(.select(3)) decoder_2 (
    .out0(decoder_2_out0), .out1(decoder_2_out1), .out2(decoder_2_out2), .out3(decoder_2_out3),
    .out4(decoder_2_out4), .out5(decoder_2_out5), .out6(decoder_2_out6), .out7(decoder_2_out7),
    .sel({in_4, in_5, in_6}));  // open: en
  Transistor #(.\type ("n")) transistor_7 (.in(mem_bit_7_out_7), .out(in_7), .gate(R));
  LED led_8 (.in(mem_bit_7_out_7));
  mem_bit mem_bit_7 (
    .Write(W), .X(decoder_2_out3), .reset(in_10), .out_7(mem_bit_7_out_7), .Y(decoder_1_out0),
    .Clock(clock_1_out), .Data(in_7));
  Transistor #(.\type ("n")) transistor_8 (.in(mem_bit_8_out_7), .out(transistor_8_out), .gate(mem_bit_8_out_7));
  mem_bit mem_bit_8 (
    .Write(undriven_2), .X(undriven), .reset(in_10), .out_7(mem_bit_8_out_7), .Data(transistor_8_out));  // open: Y, Clock
  LED led_9 (.in(mem_bit_8_out_7));
  Transistor #(.\type ("n")) transistor_9 (.in(mem_bit_9_out_7), .out(transistor_9_out), .gate(mem_bit_9_out_7));
  LED led_10 (.in(mem_bit_9_out_7));
  mem_bit mem_bit_9 (
    .Write(undriven_5), .X(undriven_4), .reset(undriven_3), .out_7(mem_bit_9_out_7), .Data(transistor_9_out));  // open: Y, Clock
  Transistor #(.\type ("n")) transistor_10 (.in(mem_bit_10_out_7), .out(transistor_10_out), .gate(mem_bit_10_out_7));
  mem_bit mem_bit_10 (
    .Write(undriven_8), .X(undriven_7), .reset(undriven_6), .out_7(mem_bit_10_out_7), .Data(transistor_10_out));  // open: Y, Clock
  LED led_11 (.in(mem_bit_10_out_7));
  Transistor #(.\type ("n")) transistor_11 (.in(mem_bit_11_out_7), .out(transistor_11_out), .gate(mem_bit_11_out_7));
  mem_bit mem_bit_11 (
    .Write(undriven_11), .X(undriven_10), .reset(undriven_9), .out_7(mem_bit_11_out_7),
    .Data(transistor_11_out));  // open: Y, Clock
  LED led_12 (.in(mem_bit_11_out_7));

  // Notes on the sheet:
  //   3x4
  //   R
  //   C
endmodule

module bcd_8bit (
  input  in_1,
  input  in_2,
  input  in_3,
  input  in_4,
  input  in_5,
  input  in_6,
  input  in_7,
  input  in_8,
  output out_9,
  output out_10,
  output out_11,
  output out_12,
  output out_13,
  output out_14,
  output out_15,
  output out_16,
  output out_17,
  output out_18
);

  wire add3_bcd_1_a_2, add3_bcd_1_b_2, add3_bcd_1_c_2, add3_bcd_1_d_2, add3_bcd_2_a_2, add3_bcd_2_b_2,
       add3_bcd_2_c_2, add3_bcd_2_d_2, add3_bcd_3_a_2, add3_bcd_3_b_2, add3_bcd_3_c_2, add3_bcd_5_a_2,
       add3_bcd_5_b_2, add3_bcd_5_c_2, add3_bcd_5_d_2, add3_bcd_6_a_2, add3_bcd_6_b_2, add3_bcd_6_c_2,
       add3_bcd_6_d_2;

  add3_bcd add3_bcd_1 (
    .d(1'b0), .c(in_1), .b(in_2), .a(in_3), .d_2(add3_bcd_1_d_2), .c_2(add3_bcd_1_c_2), .b_2(add3_bcd_1_b_2),
    .a_2(add3_bcd_1_a_2));
  add3_bcd add3_bcd_2 (
    .d(add3_bcd_1_c_2), .c(add3_bcd_1_b_2), .b(add3_bcd_1_a_2), .a(in_4), .d_2(add3_bcd_2_d_2),
    .c_2(add3_bcd_2_c_2), .b_2(add3_bcd_2_b_2), .a_2(add3_bcd_2_a_2));
  add3_bcd add3_bcd_3 (
    .d(1'b0), .c(add3_bcd_1_d_2), .b(add3_bcd_2_d_2), .a(add3_bcd_5_d_2), .d_2(out_9), .c_2(add3_bcd_3_c_2),
    .b_2(add3_bcd_3_b_2), .a_2(add3_bcd_3_a_2));
  add3_bcd add3_bcd_4 (
    .d(add3_bcd_3_c_2), .c(add3_bcd_3_b_2), .b(add3_bcd_3_a_2), .a(add3_bcd_6_d_2), .d_2(out_10),
    .c_2(out_11), .b_2(out_12), .a_2(out_13));
  add3_bcd add3_bcd_5 (
    .d(add3_bcd_2_c_2), .c(add3_bcd_2_b_2), .b(add3_bcd_2_a_2), .a(in_5), .d_2(add3_bcd_5_d_2),
    .c_2(add3_bcd_5_c_2), .b_2(add3_bcd_5_b_2), .a_2(add3_bcd_5_a_2));
  add3_bcd add3_bcd_6 (
    .d(add3_bcd_5_c_2), .c(add3_bcd_5_b_2), .b(add3_bcd_5_a_2), .a(in_6), .d_2(add3_bcd_6_d_2),
    .c_2(add3_bcd_6_c_2), .b_2(add3_bcd_6_b_2), .a_2(add3_bcd_6_a_2));
  add3_bcd add3_bcd_7 (
    .d(add3_bcd_6_c_2), .c(add3_bcd_6_b_2), .b(add3_bcd_6_a_2), .a(in_7), .d_2(out_14), .c_2(out_15),
    .b_2(out_16), .a_2(out_17));

  assign out_18 = in_8;
endmodule

module _16b_bcd (
  input  [15:0] in_1,
  input  in_2,
  output out_3,
  output out_4,
  output out_5,
  output out_6,
  output out_7,
  output out_8,
  output out_9,
  output out_10,
  output out_11,
  output out_12,
  output out_13,
  output out_14,
  output out_15,
  output out_16,
  output out_17,
  output out_18,
  output out_19,
  output out_20,
  output out_21,
  output out_22,
  output out_23,
  output out_24,
  output out_25,
  output out_26
);

  wire add3_bcd_1_a_2, add3_bcd_1_b_2, add3_bcd_1_c_2, add3_bcd_1_d_2, add3_bcd_2_a_2, add3_bcd_2_b_2,
       add3_bcd_2_c_2, add3_bcd_2_d_2, add3_bcd_3_a_2, add3_bcd_3_b_2, add3_bcd_3_c_2, add3_bcd_3_d_2,
       add3_bcd_4_a_2, add3_bcd_4_b_2, add3_bcd_4_c_2, add3_bcd_5_a_2, add3_bcd_5_b_2, add3_bcd_5_c_2,
       add3_bcd_6_a_2, add3_bcd_6_b_2, add3_bcd_6_c_2, add3_bcd_7_a_2, add3_bcd_7_b_2, add3_bcd_7_c_2,
       add3_bcd_7_d_2, add3_bcd_8_a_2, add3_bcd_8_b_2, add3_bcd_8_c_2, add3_bcd_8_d_2, add3_bcd_9_a_2,
       add3_bcd_9_b_2, add3_bcd_9_c_2, add3_bcd_9_d_2, add3_bcd_10_a_2, add3_bcd_10_b_2, add3_bcd_10_c_2,
       add3_bcd_10_d_2, add3_bcd_11_a_2, add3_bcd_11_b_2, add3_bcd_11_c_2, add3_bcd_11_d_2, add3_bcd_12_a_2,
       add3_bcd_12_b_2, add3_bcd_12_c_2, add3_bcd_12_d_2, add3_bcd_13_a_2, add3_bcd_13_b_2, add3_bcd_13_c_2,
       add3_bcd_13_d_2, add3_bcd_14_a_2, add3_bcd_14_b_2, add3_bcd_14_c_2, add3_bcd_14_d_2, add3_bcd_15_a_2,
       add3_bcd_15_b_2, add3_bcd_15_c_2, add3_bcd_15_d_2, add3_bcd_16_a_2, add3_bcd_16_b_2, add3_bcd_16_c_2,
       add3_bcd_16_d_2, add3_bcd_17_a_2, add3_bcd_17_b_2, add3_bcd_17_c_2, add3_bcd_17_d_2, add3_bcd_18_a_2,
       add3_bcd_18_b_2, add3_bcd_18_c_2, add3_bcd_18_d_2, add3_bcd_20_a_2, add3_bcd_20_b_2, add3_bcd_20_c_2,
       add3_bcd_20_d_2, add3_bcd_21_a_2, add3_bcd_21_b_2, add3_bcd_21_c_2, add3_bcd_21_d_2, add3_bcd_22_a_2,
       add3_bcd_22_b_2, add3_bcd_22_c_2, add3_bcd_22_d_2, add3_bcd_23_a_2, add3_bcd_23_b_2, add3_bcd_23_c_2,
       add3_bcd_23_d_2, add3_bcd_24_a_2, add3_bcd_24_b_2, add3_bcd_24_c_2, add3_bcd_24_d_2, add3_bcd_25_a_2,
       add3_bcd_25_b_2, add3_bcd_25_c_2, add3_bcd_25_d_2, add3_bcd_26_a_2, add3_bcd_26_b_2, add3_bcd_26_c_2,
       add3_bcd_26_d_2, add3_bcd_27_a_2, add3_bcd_27_b_2, add3_bcd_27_c_2, add3_bcd_27_d_2, add3_bcd_29_a_2,
       add3_bcd_29_b_2, add3_bcd_29_c_2, add3_bcd_29_d_2, add3_bcd_30_a_2, add3_bcd_30_b_2, add3_bcd_30_c_2,
       add3_bcd_30_d_2, add3_bcd_31_a_2, add3_bcd_31_b_2, add3_bcd_31_c_2, add3_bcd_31_d_2, add3_bcd_32_a_2,
       add3_bcd_32_b_2, add3_bcd_32_c_2, add3_bcd_32_d_2, and_1_out, and_2_out, not_1_out;

  and and_1 (and_1_out, in_1[15], in_2);
  Multiplexer #(.width(4), .enable("false")) multiplexer_1 (
    .in0(4'b1010), .in1(4'b1011), .out({out_3, out_4, out_5, out_6}), .sel(and_1_out));
  not not_1 (not_1_out, in_2);
  and and_2 (and_2_out, not_1_out, in_1[15]);
  add3_bcd add3_bcd_1 (
    .d(1'b0), .c(add3_bcd_7_d_2), .b(add3_bcd_8_d_2), .a(add3_bcd_9_d_2), .d_2(add3_bcd_1_d_2),
    .c_2(add3_bcd_1_c_2), .b_2(add3_bcd_1_b_2), .a_2(add3_bcd_1_a_2));
  add3_bcd add3_bcd_2 (
    .d(1'b0), .c(add3_bcd_1_d_2), .b(add3_bcd_11_d_2), .a(add3_bcd_12_d_2), .d_2(add3_bcd_2_d_2),
    .c_2(add3_bcd_2_c_2), .b_2(add3_bcd_2_b_2), .a_2(add3_bcd_2_a_2));
  add3_bcd add3_bcd_3 (
    .d(add3_bcd_2_c_2), .c(add3_bcd_2_b_2), .b(add3_bcd_2_a_2), .a(add3_bcd_13_d_2), .d_2(add3_bcd_3_d_2),
    .c_2(add3_bcd_3_c_2), .b_2(add3_bcd_3_b_2), .a_2(add3_bcd_3_a_2));
  add3_bcd add3_bcd_4 (
    .d(1'b0), .c(add3_bcd_2_d_2), .b(add3_bcd_3_d_2), .a(add3_bcd_15_d_2), .d_2(out_7), .c_2(add3_bcd_4_c_2),
    .b_2(add3_bcd_4_b_2), .a_2(add3_bcd_4_a_2));
  add3_bcd add3_bcd_5 (
    .d(add3_bcd_4_c_2), .c(add3_bcd_4_b_2), .b(add3_bcd_4_a_2), .a(add3_bcd_16_d_2), .d_2(out_8),
    .c_2(add3_bcd_5_c_2), .b_2(add3_bcd_5_b_2), .a_2(add3_bcd_5_a_2));
  add3_bcd add3_bcd_6 (
    .d(add3_bcd_5_c_2), .c(add3_bcd_5_b_2), .b(add3_bcd_5_a_2), .a(add3_bcd_17_d_2), .d_2(out_9),
    .c_2(add3_bcd_6_c_2), .b_2(add3_bcd_6_b_2), .a_2(add3_bcd_6_a_2));
  add3_bcd add3_bcd_7 (
    .d(1'b0), .c(and_2_out), .b(in_1[14]), .a(in_1[13]), .d_2(add3_bcd_7_d_2), .c_2(add3_bcd_7_c_2),
    .b_2(add3_bcd_7_b_2), .a_2(add3_bcd_7_a_2));
  add3_bcd add3_bcd_8 (
    .d(add3_bcd_7_c_2), .c(add3_bcd_7_b_2), .b(add3_bcd_7_a_2), .a(in_1[12]), .d_2(add3_bcd_8_d_2),
    .c_2(add3_bcd_8_c_2), .b_2(add3_bcd_8_b_2), .a_2(add3_bcd_8_a_2));
  add3_bcd add3_bcd_9 (
    .d(add3_bcd_8_c_2), .c(add3_bcd_8_b_2), .b(add3_bcd_8_a_2), .a(in_1[11]), .d_2(add3_bcd_9_d_2),
    .c_2(add3_bcd_9_c_2), .b_2(add3_bcd_9_b_2), .a_2(add3_bcd_9_a_2));
  add3_bcd add3_bcd_10 (
    .d(add3_bcd_9_c_2), .c(add3_bcd_9_b_2), .b(add3_bcd_9_a_2), .a(in_1[10]), .d_2(add3_bcd_10_d_2),
    .c_2(add3_bcd_10_c_2), .b_2(add3_bcd_10_b_2), .a_2(add3_bcd_10_a_2));
  add3_bcd add3_bcd_11 (
    .d(add3_bcd_1_c_2), .c(add3_bcd_1_b_2), .b(add3_bcd_1_a_2), .a(add3_bcd_10_d_2), .d_2(add3_bcd_11_d_2),
    .c_2(add3_bcd_11_c_2), .b_2(add3_bcd_11_b_2), .a_2(add3_bcd_11_a_2));
  add3_bcd add3_bcd_12 (
    .d(add3_bcd_11_c_2), .c(add3_bcd_11_b_2), .b(add3_bcd_11_a_2), .a(add3_bcd_20_d_2),
    .d_2(add3_bcd_12_d_2), .c_2(add3_bcd_12_c_2), .b_2(add3_bcd_12_b_2), .a_2(add3_bcd_12_a_2));
  add3_bcd add3_bcd_13 (
    .d(add3_bcd_12_c_2), .c(add3_bcd_12_b_2), .b(add3_bcd_12_a_2), .a(add3_bcd_21_d_2),
    .d_2(add3_bcd_13_d_2), .c_2(add3_bcd_13_c_2), .b_2(add3_bcd_13_b_2), .a_2(add3_bcd_13_a_2));
  add3_bcd add3_bcd_14 (
    .d(add3_bcd_13_c_2), .c(add3_bcd_13_b_2), .b(add3_bcd_13_a_2), .a(add3_bcd_22_d_2),
    .d_2(add3_bcd_14_d_2), .c_2(add3_bcd_14_c_2), .b_2(add3_bcd_14_b_2), .a_2(add3_bcd_14_a_2));
  add3_bcd add3_bcd_15 (
    .d(add3_bcd_3_c_2), .c(add3_bcd_3_b_2), .b(add3_bcd_3_a_2), .a(add3_bcd_14_d_2), .d_2(add3_bcd_15_d_2),
    .c_2(add3_bcd_15_c_2), .b_2(add3_bcd_15_b_2), .a_2(add3_bcd_15_a_2));
  add3_bcd add3_bcd_16 (
    .d(add3_bcd_15_c_2), .c(add3_bcd_15_b_2), .b(add3_bcd_15_a_2), .a(add3_bcd_24_d_2),
    .d_2(add3_bcd_16_d_2), .c_2(add3_bcd_16_c_2), .b_2(add3_bcd_16_b_2), .a_2(add3_bcd_16_a_2));
  add3_bcd add3_bcd_17 (
    .d(add3_bcd_16_c_2), .c(add3_bcd_16_b_2), .b(add3_bcd_16_a_2), .a(add3_bcd_25_d_2),
    .d_2(add3_bcd_17_d_2), .c_2(add3_bcd_17_c_2), .b_2(add3_bcd_17_b_2), .a_2(add3_bcd_17_a_2));
  add3_bcd add3_bcd_18 (
    .d(add3_bcd_17_c_2), .c(add3_bcd_17_b_2), .b(add3_bcd_17_a_2), .a(add3_bcd_26_d_2),
    .d_2(add3_bcd_18_d_2), .c_2(add3_bcd_18_c_2), .b_2(add3_bcd_18_b_2), .a_2(add3_bcd_18_a_2));
  add3_bcd add3_bcd_19 (
    .d(add3_bcd_6_c_2), .c(add3_bcd_6_b_2), .b(add3_bcd_6_a_2), .a(add3_bcd_18_d_2), .d_2(out_10),
    .c_2(out_11), .b_2(out_12), .a_2(out_13));
  add3_bcd add3_bcd_20 (
    .d(add3_bcd_10_c_2), .c(add3_bcd_10_b_2), .b(add3_bcd_10_a_2), .a(in_1[9]), .d_2(add3_bcd_20_d_2),
    .c_2(add3_bcd_20_c_2), .b_2(add3_bcd_20_b_2), .a_2(add3_bcd_20_a_2));
  add3_bcd add3_bcd_21 (
    .d(add3_bcd_20_c_2), .c(add3_bcd_20_b_2), .b(add3_bcd_20_a_2), .a(in_1[8]), .d_2(add3_bcd_21_d_2),
    .c_2(add3_bcd_21_c_2), .b_2(add3_bcd_21_b_2), .a_2(add3_bcd_21_a_2));
  add3_bcd add3_bcd_22 (
    .d(add3_bcd_21_c_2), .c(add3_bcd_21_b_2), .b(add3_bcd_21_a_2), .a(in_1[7]), .d_2(add3_bcd_22_d_2),
    .c_2(add3_bcd_22_c_2), .b_2(add3_bcd_22_b_2), .a_2(add3_bcd_22_a_2));
  add3_bcd add3_bcd_23 (
    .d(add3_bcd_22_c_2), .c(add3_bcd_22_b_2), .b(add3_bcd_22_a_2), .a(in_1[6]), .d_2(add3_bcd_23_d_2),
    .c_2(add3_bcd_23_c_2), .b_2(add3_bcd_23_b_2), .a_2(add3_bcd_23_a_2));
  add3_bcd add3_bcd_24 (
    .d(add3_bcd_14_c_2), .c(add3_bcd_14_b_2), .b(add3_bcd_14_a_2), .a(add3_bcd_23_d_2),
    .d_2(add3_bcd_24_d_2), .c_2(add3_bcd_24_c_2), .b_2(add3_bcd_24_b_2), .a_2(add3_bcd_24_a_2));
  add3_bcd add3_bcd_25 (
    .d(add3_bcd_24_c_2), .c(add3_bcd_24_b_2), .b(add3_bcd_24_a_2), .a(add3_bcd_29_d_2),
    .d_2(add3_bcd_25_d_2), .c_2(add3_bcd_25_c_2), .b_2(add3_bcd_25_b_2), .a_2(add3_bcd_25_a_2));
  add3_bcd add3_bcd_26 (
    .d(add3_bcd_25_c_2), .c(add3_bcd_25_b_2), .b(add3_bcd_25_a_2), .a(add3_bcd_30_d_2),
    .d_2(add3_bcd_26_d_2), .c_2(add3_bcd_26_c_2), .b_2(add3_bcd_26_b_2), .a_2(add3_bcd_26_a_2));
  add3_bcd add3_bcd_27 (
    .d(add3_bcd_26_c_2), .c(add3_bcd_26_b_2), .b(add3_bcd_26_a_2), .a(add3_bcd_31_d_2),
    .d_2(add3_bcd_27_d_2), .c_2(add3_bcd_27_c_2), .b_2(add3_bcd_27_b_2), .a_2(add3_bcd_27_a_2));
  add3_bcd add3_bcd_28 (
    .d(add3_bcd_18_c_2), .c(add3_bcd_18_b_2), .b(add3_bcd_18_a_2), .a(add3_bcd_27_d_2), .d_2(out_14),
    .c_2(out_15), .b_2(out_16), .a_2(out_17));
  add3_bcd add3_bcd_29 (
    .d(add3_bcd_23_c_2), .c(add3_bcd_23_b_2), .b(add3_bcd_23_a_2), .a(in_1[5]), .d_2(add3_bcd_29_d_2),
    .c_2(add3_bcd_29_c_2), .b_2(add3_bcd_29_b_2), .a_2(add3_bcd_29_a_2));
  add3_bcd add3_bcd_30 (
    .d(add3_bcd_29_c_2), .c(add3_bcd_29_b_2), .b(add3_bcd_29_a_2), .a(in_1[4]), .d_2(add3_bcd_30_d_2),
    .c_2(add3_bcd_30_c_2), .b_2(add3_bcd_30_b_2), .a_2(add3_bcd_30_a_2));
  add3_bcd add3_bcd_31 (
    .d(add3_bcd_30_c_2), .c(add3_bcd_30_b_2), .b(add3_bcd_30_a_2), .a(in_1[3]), .d_2(add3_bcd_31_d_2),
    .c_2(add3_bcd_31_c_2), .b_2(add3_bcd_31_b_2), .a_2(add3_bcd_31_a_2));
  add3_bcd add3_bcd_32 (
    .d(add3_bcd_31_c_2), .c(add3_bcd_31_b_2), .b(add3_bcd_31_a_2), .a(in_1[2]), .d_2(add3_bcd_32_d_2),
    .c_2(add3_bcd_32_c_2), .b_2(add3_bcd_32_b_2), .a_2(add3_bcd_32_a_2));
  add3_bcd add3_bcd_33 (
    .d(add3_bcd_27_c_2), .c(add3_bcd_27_b_2), .b(add3_bcd_27_a_2), .a(add3_bcd_32_d_2), .d_2(out_18),
    .c_2(out_19), .b_2(out_20), .a_2(out_21));
  add3_bcd add3_bcd_34 (
    .d(add3_bcd_32_c_2), .c(add3_bcd_32_b_2), .b(add3_bcd_32_a_2), .a(in_1[1]), .d_2(out_22), .c_2(out_23),
    .b_2(out_24), .a_2(out_25));

  assign out_26 = in_1[0];
endmodule

module add3_bcd (
  input  d,
  input  c,
  input  b,
  input  a,
  output d_2,
  output c_2,
  output b_2,
  output a_2
);

  wire and_1_out, and_2_out, and_3_out, and_4_out, and_5_out, and_6_out, and_7_out, and_8_out, and_9_out,
       and_10_out, and_11_out, and_12_out, and_13_out, not_1_out, not_2_out, not_3_out, not_4_out, not_5_out,
       not_6_out, not_7_out, not_8_out, or_1_out, or_3_out, or_6_out;

  and and_1 (and_1_out, c, a);
  and and_2 (and_2_out, c, b);
  and and_3 (and_3_out, c, not_1_out);
  not not_1 (not_1_out, b);
  not not_2 (not_2_out, a);
  not not_3 (not_3_out, c);
  and and_4 (and_4_out, not_3_out, b);
  and and_5 (and_5_out, b, a);
  not not_4 (not_4_out, a);
  not not_5 (not_5_out, d);
  and and_6 (and_6_out, not_5_out, not_6_out);
  not not_6 (not_6_out, c);
  and and_7 (and_7_out, c, b);
  not not_7 (not_7_out, a);
  or or_1 (or_1_out, and_1_out, and_2_out);
  or or_2 (d_2, or_1_out, d);
  and and_8 (and_8_out, and_3_out, not_2_out);
  and and_9 (and_9_out, d, a);
  or or_3 (or_3_out, and_4_out, and_5_out);
  and and_10 (and_10_out, d, not_4_out);
  and and_11 (and_11_out, and_6_out, a);
  and and_12 (and_12_out, and_7_out, not_7_out);
  not not_8 (not_8_out, a);
  or or_4 (c_2, and_8_out, and_9_out);
  or or_5 (b_2, or_3_out, and_10_out);
  or or_6 (or_6_out, and_11_out, and_12_out);
  and and_13 (and_13_out, d, not_8_out);
  or or_7 (a_2, or_6_out, and_13_out);
endmodule

module _16bit_display (
  input  \signed ,
  input  [15:0] in_2,
  output [23:0] out_3,
  output [23:0] out_4
);

  wire n16b_bcd_1_out_3, n16b_bcd_1_out_4, n16b_bcd_1_out_5, n16b_bcd_1_out_6, n16b_bcd_1_out_7,
       n16b_bcd_1_out_8, n16b_bcd_1_out_9, n16b_bcd_1_out_10, n16b_bcd_1_out_11, n16b_bcd_1_out_12,
       n16b_bcd_1_out_13, n16b_bcd_1_out_14, n16b_bcd_1_out_15, n16b_bcd_1_out_16, n16b_bcd_1_out_17,
       n16b_bcd_1_out_18, n16b_bcd_1_out_19, n16b_bcd_1_out_20, n16b_bcd_1_out_21, n16b_bcd_1_out_22,
       n16b_bcd_1_out_23, n16b_bcd_1_out_24, n16b_bcd_1_out_25, n16b_bcd_1_out_26;

  BCD_to_7segment_display bcd_to_7segment_display_1 (
    .a(n16b_bcd_1_out_3), .b(n16b_bcd_1_out_4), .c(n16b_bcd_1_out_5), .m(out_3[23]), .d(n16b_bcd_1_out_6),
    .tl(out_3[22]), .t(out_3[21]), .tr(out_3[20]), .bl(out_4[23]), .b2(out_4[22]), .br(out_4[21]));
  BCD_to_7segment_display bcd_to_7segment_display_2 (
    .a(n16b_bcd_1_out_7), .b(n16b_bcd_1_out_8), .c(n16b_bcd_1_out_9), .m(out_3[19]), .d(n16b_bcd_1_out_10),
    .tl(out_3[18]), .t(out_3[17]), .tr(out_3[16]), .bl(out_4[19]), .b2(out_4[18]), .br(out_4[17]));
  _16b_bcd u_16b_bcd_1 (
    .out_11(n16b_bcd_1_out_11), .out_12(n16b_bcd_1_out_12), .out_13(n16b_bcd_1_out_13),
    .out_14(n16b_bcd_1_out_14), .out_15(n16b_bcd_1_out_15), .out_16(n16b_bcd_1_out_16),
    .out_17(n16b_bcd_1_out_17), .out_18(n16b_bcd_1_out_18), .out_19(n16b_bcd_1_out_19),
    .out_20(n16b_bcd_1_out_20), .out_21(n16b_bcd_1_out_21), .out_22(n16b_bcd_1_out_22),
    .out_23(n16b_bcd_1_out_23), .out_24(n16b_bcd_1_out_24), .out_25(n16b_bcd_1_out_25),
    .out_26(n16b_bcd_1_out_26), .in_1(in_2), .in_2(\signed ), .out_7(n16b_bcd_1_out_7),
    .out_8(n16b_bcd_1_out_8), .out_9(n16b_bcd_1_out_9), .out_10(n16b_bcd_1_out_10), .out_3(n16b_bcd_1_out_3),
    .out_4(n16b_bcd_1_out_4), .out_5(n16b_bcd_1_out_5), .out_6(n16b_bcd_1_out_6));
  BCD_to_7segment_display bcd_to_7segment_display_3 (
    .a(n16b_bcd_1_out_11), .b(n16b_bcd_1_out_12), .c(n16b_bcd_1_out_13), .m(out_3[15]),
    .d(n16b_bcd_1_out_14), .tl(out_3[14]), .t(out_3[13]), .tr(out_3[12]), .bl(out_4[15]), .b2(out_4[14]),
    .br(out_4[13]));
  BCD_to_7segment_display bcd_to_7segment_display_4 (
    .a(n16b_bcd_1_out_15), .b(n16b_bcd_1_out_16), .c(n16b_bcd_1_out_17), .m(out_3[11]),
    .d(n16b_bcd_1_out_18), .tl(out_3[10]), .t(out_3[9]), .tr(out_3[8]), .bl(out_4[11]), .b2(out_4[10]),
    .br(out_4[9]));
  BCD_to_7segment_display bcd_to_7segment_display_5 (
    .a(n16b_bcd_1_out_19), .b(n16b_bcd_1_out_20), .c(n16b_bcd_1_out_21), .m(out_3[7]), .d(n16b_bcd_1_out_22),
    .tl(out_3[6]), .t(out_3[5]), .tr(out_3[4]), .bl(out_4[7]), .b2(out_4[6]), .br(out_4[5]));
  BCD_to_7segment_display bcd_to_7segment_display_6 (
    .a(n16b_bcd_1_out_23), .b(n16b_bcd_1_out_24), .c(n16b_bcd_1_out_25), .m(out_3[3]), .d(n16b_bcd_1_out_26),
    .tl(out_3[2]), .t(out_3[1]), .tr(out_3[0]), .bl(out_4[3]), .b2(out_4[2]), .br(out_4[1]));
endmodule

module ALU (
  input  [15:0] B,
  input  [15:0] A,
  input  add_sub,
  output overflow,
  output [15:0] \output ,
  output zero
);

  wire adder_sub_2_c_out, adder_sub_3_c_out, adder_sub_4_c_out, adder_sub_5_c_out, adder_sub_6_c_out,
       adder_sub_7_c_out, adder_sub_8_c_out, adder_sub_9_c_out, adder_sub_10_c_out, adder_sub_11_c_out,
       adder_sub_12_c_out, adder_sub_13_c_out, adder_sub_14_c_out, adder_sub_15_c_out, adder_sub_16_c_out,
       or_1_out;

  adder_sub adder_sub_1 (
    .a(A[15]), .b(B[15]), .c(adder_sub_3_c_out), .c_out(overflow), .data(\output [15]), .add_sub(add_sub));
  adder_sub adder_sub_2 (
    .a(A[13]), .b(B[13]), .c(adder_sub_4_c_out), .c_out(adder_sub_2_c_out), .data(\output [13]),
    .add_sub(add_sub));
  adder_sub adder_sub_3 (
    .a(A[14]), .b(B[14]), .c(adder_sub_2_c_out), .c_out(adder_sub_3_c_out), .data(\output [14]),
    .add_sub(add_sub));
  adder_sub adder_sub_4 (
    .a(A[12]), .b(B[12]), .c(adder_sub_5_c_out), .c_out(adder_sub_4_c_out), .data(\output [12]),
    .add_sub(add_sub));
  adder_sub adder_sub_5 (
    .a(A[11]), .b(B[11]), .c(adder_sub_6_c_out), .c_out(adder_sub_5_c_out), .data(\output [11]),
    .add_sub(add_sub));
  adder_sub adder_sub_6 (
    .a(A[10]), .b(B[10]), .c(adder_sub_7_c_out), .c_out(adder_sub_6_c_out), .data(\output [10]),
    .add_sub(add_sub));
  adder_sub adder_sub_7 (
    .a(A[9]), .b(B[9]), .c(adder_sub_8_c_out), .c_out(adder_sub_7_c_out), .data(\output [9]),
    .add_sub(add_sub));
  adder_sub adder_sub_8 (
    .a(A[8]), .b(B[8]), .c(adder_sub_9_c_out), .c_out(adder_sub_8_c_out), .data(\output [8]),
    .add_sub(add_sub));
  adder_sub adder_sub_9 (
    .a(A[7]), .b(B[7]), .c(adder_sub_10_c_out), .c_out(adder_sub_9_c_out), .data(\output [7]),
    .add_sub(add_sub));
  or or_1 (or_1_out, \output [15], \output [14], \output [13], \output [12], \output [11], \output [10], \output [9], \output [8], \output [7], \output [6], \output [5], \output [4], \output [3], \output [2], \output [1], \output [0]);
  not not_1 (zero, or_1_out);
  adder_sub adder_sub_10 (
    .a(A[6]), .b(B[6]), .c(adder_sub_11_c_out), .c_out(adder_sub_10_c_out), .data(\output [6]),
    .add_sub(add_sub));
  adder_sub adder_sub_11 (
    .a(A[5]), .b(B[5]), .c(adder_sub_12_c_out), .c_out(adder_sub_11_c_out), .data(\output [5]),
    .add_sub(add_sub));
  adder_sub adder_sub_12 (
    .a(A[4]), .b(B[4]), .c(adder_sub_13_c_out), .c_out(adder_sub_12_c_out), .data(\output [4]),
    .add_sub(add_sub));
  adder_sub adder_sub_13 (
    .a(A[3]), .b(B[3]), .c(adder_sub_14_c_out), .c_out(adder_sub_13_c_out), .data(\output [3]),
    .add_sub(add_sub));
  adder_sub adder_sub_14 (
    .a(A[2]), .b(B[2]), .c(adder_sub_16_c_out), .c_out(adder_sub_14_c_out), .data(\output [2]),
    .add_sub(add_sub));
  adder_sub adder_sub_15 (
    .a(A[0]), .b(B[0]), .c(1'b0), .c_out(adder_sub_15_c_out), .data(\output [0]), .add_sub(add_sub));
  adder_sub adder_sub_16 (
    .a(A[1]), .b(B[1]), .c(adder_sub_15_c_out), .c_out(adder_sub_16_c_out), .data(\output [1]),
    .add_sub(add_sub));
endmodule

module onebit_ALU (
  input  [2:0] ALUop,
  input  Cin,
  input  a,
  input  b,
  output Carry_Out,
  output data_out
);

  wire adder_sub_1_data, and_1_out, nor_1_out, or_1_out, xor_1_out;

  adder_sub adder_sub_1 (.a(a), .b(b), .c(Cin), .c_out(Carry_Out), .data(adder_sub_1_data), .add_sub(ALUop[0]));
  and and_1 (and_1_out, a, b);
  or or_1 (or_1_out, a, b);
  nor nor_1 (nor_1_out, a, b);
  xor xor_1 (xor_1_out, a, b);
  Multiplexer #(.select(3), .enable("false")) multiplexer_1 (
    .in0(adder_sub_1_data), .in1(adder_sub_1_data), .in2(adder_sub_1_data), .in3(adder_sub_1_data),
    .in4(and_1_out), .in5(or_1_out), .in6(nor_1_out), .in7(xor_1_out), .out(data_out), .sel(ALUop));
endmodule
module shiftright (
  input  [15:0] \input ,
  input  SLL,
  input  sign,
  input  [2:0] shiftammt,
  output [15:0] \output 
);

  wire and_1_out, and_2_out, and_3_out, multiplexer_1_out, multiplexer_2_out, multiplexer_3_out,
       multiplexer_4_out, multiplexer_5_out, multiplexer_6_out, multiplexer_7_out, multiplexer_8_out,
       multiplexer_9_out, multiplexer_10_out, multiplexer_11_out, multiplexer_12_out, multiplexer_13_out,
       multiplexer_14_out, multiplexer_15_out, multiplexer_16_out, multiplexer_17_out, multiplexer_18_out,
       multiplexer_19_out, multiplexer_20_out, multiplexer_21_out, multiplexer_22_out, multiplexer_23_out,
       multiplexer_24_out, multiplexer_25_out, multiplexer_26_out, multiplexer_27_out, multiplexer_28_out,
       multiplexer_29_out, multiplexer_30_out, multiplexer_31_out, multiplexer_32_out;
  wire [15:0] multiplexer_33_out, reverse_binary_1_output;

  reverse_binary reverse_binary_1 (
    .reverse(SLL), .\input (\input ), .\output (reverse_binary_1_output), .inverse(1'b0));
  and and_1 (and_1_out, reverse_binary_1_output[15], sign);
  Multiplexer #(.enable("false")) multiplexer_1 (
    .in0(reverse_binary_1_output[0]), .in1(reverse_binary_1_output[1]), .out(multiplexer_1_out),
    .sel(shiftammt[0]));
  Multiplexer #(.enable("false")) multiplexer_2 (
    .in0(reverse_binary_1_output[1]), .in1(reverse_binary_1_output[2]), .out(multiplexer_2_out),
    .sel(shiftammt[0]));
  Multiplexer #(.enable("false")) multiplexer_3 (
    .in0(reverse_binary_1_output[2]), .in1(reverse_binary_1_output[3]), .out(multiplexer_3_out),
    .sel(shiftammt[0]));
  Multiplexer #(.enable("false")) multiplexer_4 (
    .in0(reverse_binary_1_output[3]), .in1(reverse_binary_1_output[4]), .out(multiplexer_4_out),
    .sel(shiftammt[0]));
  Multiplexer #(.enable("false")) multiplexer_5 (
    .in0(reverse_binary_1_output[4]), .in1(reverse_binary_1_output[5]), .out(multiplexer_5_out),
    .sel(shiftammt[0]));
  Multiplexer #(.enable("false")) multiplexer_6 (
    .in0(reverse_binary_1_output[5]), .in1(reverse_binary_1_output[6]), .out(multiplexer_6_out),
    .sel(shiftammt[0]));
  Multiplexer #(.enable("false")) multiplexer_7 (
    .in0(reverse_binary_1_output[6]), .in1(reverse_binary_1_output[7]), .out(multiplexer_7_out),
    .sel(shiftammt[0]));
  Multiplexer #(.enable("false")) multiplexer_8 (
    .in0(reverse_binary_1_output[7]), .in1(reverse_binary_1_output[8]), .out(multiplexer_8_out),
    .sel(shiftammt[0]));
  Multiplexer #(.enable("false")) multiplexer_9 (
    .in0(reverse_binary_1_output[8]), .in1(reverse_binary_1_output[9]), .out(multiplexer_9_out),
    .sel(shiftammt[0]));
  Multiplexer #(.enable("false")) multiplexer_10 (
    .in0(reverse_binary_1_output[9]), .in1(reverse_binary_1_output[10]), .out(multiplexer_10_out),
    .sel(shiftammt[0]));
  Multiplexer #(.enable("false")) multiplexer_11 (
    .in0(reverse_binary_1_output[10]), .in1(reverse_binary_1_output[11]), .out(multiplexer_11_out),
    .sel(shiftammt[0]));
  Multiplexer #(.enable("false")) multiplexer_12 (
    .in0(reverse_binary_1_output[11]), .in1(reverse_binary_1_output[12]), .out(multiplexer_12_out),
    .sel(shiftammt[0]));
  Multiplexer #(.enable("false")) multiplexer_13 (
    .in0(reverse_binary_1_output[12]), .in1(reverse_binary_1_output[13]), .out(multiplexer_13_out),
    .sel(shiftammt[0]));
  Multiplexer #(.enable("false")) multiplexer_14 (
    .in0(reverse_binary_1_output[13]), .in1(reverse_binary_1_output[14]), .out(multiplexer_14_out),
    .sel(shiftammt[0]));
  Multiplexer #(.enable("false")) multiplexer_15 (
    .in0(reverse_binary_1_output[14]), .in1(reverse_binary_1_output[15]), .out(multiplexer_15_out),
    .sel(shiftammt[0]));
  Multiplexer #(.enable("false")) multiplexer_16 (
    .in0(reverse_binary_1_output[15]), .in1(and_1_out), .out(multiplexer_16_out), .sel(shiftammt[0]));
  and and_2 (and_2_out, multiplexer_16_out, sign);
  Multiplexer #(.enable("false")) multiplexer_17 (
    .in0(multiplexer_1_out), .in1(multiplexer_3_out), .out(multiplexer_17_out), .sel(shiftammt[1]));
  Multiplexer #(.enable("false")) multiplexer_18 (
    .in0(multiplexer_2_out), .in1(multiplexer_4_out), .out(multiplexer_18_out), .sel(shiftammt[1]));
  Multiplexer #(.enable("false")) multiplexer_19 (
    .in0(multiplexer_3_out), .in1(multiplexer_5_out), .out(multiplexer_19_out), .sel(shiftammt[1]));
  Multiplexer #(.enable("false")) multiplexer_20 (
    .in0(multiplexer_4_out), .in1(multiplexer_6_out), .out(multiplexer_20_out), .sel(shiftammt[1]));
  Multiplexer #(.enable("false")) multiplexer_21 (
    .in0(multiplexer_5_out), .in1(multiplexer_7_out), .out(multiplexer_21_out), .sel(shiftammt[1]));
  Multiplexer #(.enable("false")) multiplexer_22 (
    .in0(multiplexer_6_out), .in1(multiplexer_8_out), .out(multiplexer_22_out), .sel(shiftammt[1]));
  Multiplexer #(.enable("false")) multiplexer_23 (
    .in0(multiplexer_7_out), .in1(multiplexer_9_out), .out(multiplexer_23_out), .sel(shiftammt[1]));
  Multiplexer #(.enable("false")) multiplexer_24 (
    .in0(multiplexer_8_out), .in1(multiplexer_10_out), .out(multiplexer_24_out), .sel(shiftammt[1]));
  Multiplexer #(.enable("false")) multiplexer_25 (
    .in0(multiplexer_9_out), .in1(multiplexer_11_out), .out(multiplexer_25_out), .sel(shiftammt[1]));
  Multiplexer #(.enable("false")) multiplexer_26 (
    .in0(multiplexer_10_out), .in1(multiplexer_12_out), .out(multiplexer_26_out), .sel(shiftammt[1]));
  Multiplexer #(.enable("false")) multiplexer_27 (
    .in0(multiplexer_11_out), .in1(multiplexer_13_out), .out(multiplexer_27_out), .sel(shiftammt[1]));
  Multiplexer #(.enable("false")) multiplexer_28 (
    .in0(multiplexer_12_out), .in1(multiplexer_14_out), .out(multiplexer_28_out), .sel(shiftammt[1]));
  Multiplexer #(.enable("false")) multiplexer_29 (
    .in0(multiplexer_13_out), .in1(multiplexer_15_out), .out(multiplexer_29_out), .sel(shiftammt[1]));
  Multiplexer #(.enable("false")) multiplexer_30 (
    .in0(multiplexer_14_out), .in1(multiplexer_16_out), .out(multiplexer_30_out), .sel(shiftammt[1]));
  Multiplexer #(.enable("false")) multiplexer_31 (
    .in0(multiplexer_15_out), .in1(and_2_out), .out(multiplexer_31_out), .sel(shiftammt[1]));
  Multiplexer #(.enable("false")) multiplexer_32 (
    .in0(multiplexer_16_out), .in1(and_2_out), .out(multiplexer_32_out), .sel(shiftammt[1]));
  Multiplexer #(.enable("false")) multiplexer_33 (
    .in0(multiplexer_17_out), .in1(multiplexer_21_out), .out(multiplexer_33_out[0]), .sel(shiftammt[2]));
  Multiplexer #(.enable("false")) multiplexer_34 (
    .in0(multiplexer_18_out), .in1(multiplexer_22_out), .out(multiplexer_33_out[1]), .sel(shiftammt[2]));
  Multiplexer #(.enable("false")) multiplexer_35 (
    .in0(multiplexer_19_out), .in1(multiplexer_23_out), .out(multiplexer_33_out[2]), .sel(shiftammt[2]));
  Multiplexer #(.enable("false")) multiplexer_36 (
    .in0(multiplexer_20_out), .in1(multiplexer_24_out), .out(multiplexer_33_out[3]), .sel(shiftammt[2]));
  Multiplexer #(.enable("false")) multiplexer_37 (
    .in0(multiplexer_21_out), .in1(multiplexer_25_out), .out(multiplexer_33_out[4]), .sel(shiftammt[2]));
  Multiplexer #(.enable("false")) multiplexer_38 (
    .in0(multiplexer_22_out), .in1(multiplexer_26_out), .out(multiplexer_33_out[5]), .sel(shiftammt[2]));
  Multiplexer #(.enable("false")) multiplexer_39 (
    .in0(multiplexer_23_out), .in1(multiplexer_27_out), .out(multiplexer_33_out[6]), .sel(shiftammt[2]));
  Multiplexer #(.enable("false")) multiplexer_40 (
    .in0(multiplexer_24_out), .in1(multiplexer_28_out), .out(multiplexer_33_out[7]), .sel(shiftammt[2]));
  Multiplexer #(.enable("false")) multiplexer_41 (
    .in0(multiplexer_25_out), .in1(multiplexer_29_out), .out(multiplexer_33_out[8]), .sel(shiftammt[2]));
  Multiplexer #(.enable("false")) multiplexer_42 (
    .in0(multiplexer_26_out), .in1(multiplexer_30_out), .out(multiplexer_33_out[9]), .sel(shiftammt[2]));
  Multiplexer #(.enable("false")) multiplexer_43 (
    .in0(multiplexer_27_out), .in1(multiplexer_31_out), .out(multiplexer_33_out[10]), .sel(shiftammt[2]));
  Multiplexer #(.enable("false")) multiplexer_44 (
    .in0(multiplexer_28_out), .in1(multiplexer_32_out), .out(multiplexer_33_out[11]), .sel(shiftammt[2]));
  Multiplexer #(.enable("false")) multiplexer_45 (
    .in0(multiplexer_29_out), .in1(and_3_out), .out(multiplexer_33_out[12]), .sel(shiftammt[2]));
  Multiplexer #(.enable("false")) multiplexer_46 (
    .in0(multiplexer_30_out), .in1(and_3_out), .out(multiplexer_33_out[13]), .sel(shiftammt[2]));
  Multiplexer #(.enable("false")) multiplexer_47 (
    .in0(multiplexer_31_out), .in1(and_3_out), .out(multiplexer_33_out[14]), .sel(shiftammt[2]));
  Multiplexer #(.enable("false")) multiplexer_48 (
    .in0(multiplexer_32_out), .in1(and_3_out), .out(multiplexer_33_out[15]), .sel(shiftammt[2]));
  and and_3 (and_3_out, multiplexer_32_out, sign);
  reverse_binary reverse_binary_2 (.reverse(SLL), .\input (multiplexer_33_out), .\output (\output ), .inverse(1'b0));

  // Other names for the same wires on the sheet: SLLflag = SLL
endmodule

module reverse_binary (
  input  [15:0] \input ,
  input  reverse,
  input  inverse,
  output [15:0] \output 
);

  wire [15:0] xor_16_out;

  xor xor_1 (xor_16_out[0], \input [0], inverse);
  xor xor_2 (xor_16_out[1], \input [1], inverse);
  xor xor_3 (xor_16_out[2], \input [2], inverse);
  xor xor_4 (xor_16_out[3], \input [3], inverse);
  xor xor_5 (xor_16_out[4], \input [4], inverse);
  xor xor_6 (xor_16_out[5], \input [5], inverse);
  xor xor_7 (xor_16_out[6], \input [6], inverse);
  xor xor_8 (xor_16_out[7], \input [7], inverse);
  xor xor_9 (xor_16_out[8], \input [8], inverse);
  xor xor_10 (xor_16_out[9], \input [9], inverse);
  xor xor_11 (xor_16_out[10], \input [10], inverse);
  xor xor_12 (xor_16_out[11], \input [11], inverse);
  xor xor_13 (xor_16_out[12], \input [12], inverse);
  xor xor_14 (xor_16_out[13], \input [13], inverse);
  xor xor_15 (xor_16_out[14], \input [14], inverse);
  xor xor_16 (xor_16_out[15], \input [15], inverse);
  Multiplexer #(.width(16), .enable("false")) multiplexer_1 (
    .in0(xor_16_out),
    .in1({xor_16_out[0], xor_16_out[1], xor_16_out[2], xor_16_out[3], xor_16_out[4], xor_16_out[5], xor_16_out[6], xor_16_out[7], xor_16_out[8], xor_16_out[9], xor_16_out[10], xor_16_out[11], xor_16_out[12], xor_16_out[13], xor_16_out[14], xor_16_out[15]}),
    .out(\output ), .sel(reverse));
endmodule

module Multi_Func_ALU (
  input  [15:0] B,
  input  [15:0] A,
  input  [4:0] add_sub,
  output [15:0] \output ,
  output [15:0] output_2,
  output overflow,
  output zero
);

  wire and_1_out, and_2_out, nor_1_out, not_1_out, not_3_out, not_4_out, not_5_out, not_6_out, not_7_out,
       not_8_out, not_9_out, not_10_out, not_11_out, not_12_out, not_13_out, not_14_out, not_15_out,
       not_16_out, not_17_out, onebit_alu_1_carry_out, onebit_alu_2_carry_out, onebit_alu_3_carry_out,
       onebit_alu_4_carry_out, onebit_alu_5_carry_out, onebit_alu_6_carry_out, onebit_alu_7_carry_out,
       onebit_alu_8_carry_out, onebit_alu_9_carry_out, onebit_alu_10_carry_out, onebit_alu_11_carry_out,
       onebit_alu_12_carry_out, onebit_alu_13_carry_out, onebit_alu_14_carry_out, onebit_alu_15_carry_out,
       onebit_alu_16_carry_out, or_1_out, or_2_out, or_3_out, SLL, SLT, SLTU, SRA, SRL, xor_1_out;
  wire [1:0] or_5_out;
  wire [15:0] comparator_lessthan_1_less, onebit_alu_16_data_out;

  xor xor_1 (xor_1_out, onebit_alu_1_carry_out, onebit_alu_3_carry_out);
  and and_1 (and_1_out, xor_1_out, nor_1_out);
  or or_1 (or_1_out, and_1_out, and_2_out);
  onebit_ALU onebit_alu_1 (
    .a(A[15]), .b(B[15]), .data_out(onebit_alu_16_data_out[15]), .Cin(onebit_alu_3_carry_out),
    .Carry_Out(onebit_alu_1_carry_out), .ALUop(add_sub[2:0]));
  not not_1 (not_1_out, nor_1_out);
  and and_2 (and_2_out, onebit_alu_1_carry_out, not_1_out);
  or or_2 (or_2_out, or_5_out[0], or_5_out[1]);
  Multiplexer #(.enable("false")) multiplexer_1 (.in0(or_1_out), .in1(1'b0), .out(overflow), .sel(or_2_out));
  nor nor_1 (nor_1_out, add_sub[2], add_sub[1], add_sub[0]);
  onebit_ALU onebit_alu_2 (
    .a(A[13]), .b(B[13]), .data_out(onebit_alu_16_data_out[13]), .Cin(onebit_alu_4_carry_out),
    .Carry_Out(onebit_alu_2_carry_out), .ALUop(add_sub[2:0]));
  onebit_ALU onebit_alu_3 (
    .a(A[14]), .b(B[14]), .data_out(onebit_alu_16_data_out[14]), .Cin(onebit_alu_2_carry_out),
    .Carry_Out(onebit_alu_3_carry_out), .ALUop(add_sub[2:0]));
  onebit_ALU onebit_alu_4 (
    .a(A[12]), .b(B[12]), .data_out(onebit_alu_16_data_out[12]), .Cin(onebit_alu_5_carry_out),
    .Carry_Out(onebit_alu_4_carry_out), .ALUop(add_sub[2:0]));
  onebit_ALU onebit_alu_5 (
    .a(A[11]), .b(B[11]), .data_out(onebit_alu_16_data_out[11]), .Cin(onebit_alu_6_carry_out),
    .Carry_Out(onebit_alu_5_carry_out), .ALUop(add_sub[2:0]));
  onebit_ALU onebit_alu_6 (
    .a(A[10]), .b(B[10]), .data_out(onebit_alu_16_data_out[10]), .Cin(onebit_alu_7_carry_out),
    .Carry_Out(onebit_alu_6_carry_out), .ALUop(add_sub[2:0]));
  onebit_ALU onebit_alu_7 (
    .a(A[9]), .b(B[9]), .data_out(onebit_alu_16_data_out[9]), .Cin(onebit_alu_8_carry_out),
    .Carry_Out(onebit_alu_7_carry_out), .ALUop(add_sub[2:0]));
  onebit_ALU onebit_alu_8 (
    .a(A[8]), .b(B[8]), .data_out(onebit_alu_16_data_out[8]), .Cin(onebit_alu_9_carry_out),
    .Carry_Out(onebit_alu_8_carry_out), .ALUop(add_sub[2:0]));
  onebit_ALU onebit_alu_9 (
    .a(A[7]), .b(B[7]), .data_out(onebit_alu_16_data_out[7]), .Cin(onebit_alu_10_carry_out),
    .Carry_Out(onebit_alu_9_carry_out), .ALUop(add_sub[2:0]));
  Multiplexer #(.select(2), .width(16), .enable("false")) multiplexer_2 (
    .in0(onebit_alu_16_data_out), .in1(\output ), .in2(comparator_lessthan_1_less),
    .in3(comparator_lessthan_1_less), .out(output_2), .sel(or_5_out));
  or or_3 (or_3_out, output_2[15], output_2[14], output_2[13], output_2[12], output_2[11], output_2[10], output_2[9], output_2[8], output_2[7], output_2[6], output_2[5], output_2[4], output_2[3], output_2[2], output_2[1], output_2[0]);
  not not_2 (zero, or_3_out);
  onebit_ALU onebit_alu_10 (
    .a(A[6]), .b(B[6]), .data_out(onebit_alu_16_data_out[6]), .Cin(onebit_alu_11_carry_out),
    .Carry_Out(onebit_alu_10_carry_out), .ALUop(add_sub[2:0]));
  onebit_ALU onebit_alu_11 (
    .a(A[5]), .b(B[5]), .data_out(onebit_alu_16_data_out[5]), .Cin(onebit_alu_12_carry_out),
    .Carry_Out(onebit_alu_11_carry_out), .ALUop(add_sub[2:0]));
  or or_4 (or_5_out[1], SLTU, SLT);
  onebit_ALU onebit_alu_12 (
    .a(A[4]), .b(B[4]), .data_out(onebit_alu_16_data_out[4]), .Cin(onebit_alu_14_carry_out),
    .Carry_Out(onebit_alu_12_carry_out), .ALUop(add_sub[2:0]));
  onebit_ALU onebit_alu_13 (
    .a(A[2]), .b(B[2]), .data_out(onebit_alu_16_data_out[2]), .Cin(onebit_alu_15_carry_out),
    .Carry_Out(onebit_alu_13_carry_out), .ALUop(add_sub[2:0]));
  onebit_ALU onebit_alu_14 (
    .a(A[3]), .b(B[3]), .data_out(onebit_alu_16_data_out[3]), .Cin(onebit_alu_13_carry_out),
    .Carry_Out(onebit_alu_14_carry_out), .ALUop(add_sub[2:0]));
  or or_5 (or_5_out[0], SRA, SLL, SRL);
  onebit_ALU onebit_alu_15 (
    .a(A[1]), .b(B[1]), .data_out(onebit_alu_16_data_out[1]), .Cin(onebit_alu_16_carry_out),
    .Carry_Out(onebit_alu_15_carry_out), .ALUop(add_sub[2:0]));
  onebit_ALU onebit_alu_16 (
    .a(A[0]), .b(B[0]), .data_out(onebit_alu_16_data_out[0]), .Cin(1'b0),
    .Carry_Out(onebit_alu_16_carry_out), .ALUop(add_sub[2:0]));
  comparator_lessthan comparator_lessthan_1 (.LESS(comparator_lessthan_1_less), .A(A), .B(B), .SLTU(SLTU));
  shiftright shiftright_1 (.sign(SRA), .shiftammt(A[2:0]), .\input (B), .\output (\output ), .SLL(SLL));
  not not_3 (not_3_out, add_sub[4]);
  and and_3 (SRL, not_3_out, add_sub[3], not_4_out, not_5_out, add_sub[0]);
  not not_4 (not_4_out, add_sub[2]);
  not not_5 (not_5_out, add_sub[1]);
  not not_6 (not_6_out, add_sub[4]);
  and and_4 (SRA, not_6_out, add_sub[3], not_7_out, add_sub[1], not_8_out);
  not not_7 (not_7_out, add_sub[2]);
  not not_8 (not_8_out, add_sub[0]);
  not not_9 (not_9_out, add_sub[4]);
  and and_5 (SLL, not_9_out, add_sub[3], not_13_out, not_11_out, not_10_out);
  not not_10 (not_10_out, add_sub[0]);
  not not_11 (not_11_out, add_sub[1]);
  not not_12 (not_12_out, add_sub[4]);
  not not_13 (not_13_out, add_sub[2]);
  and and_6 (SLT, not_12_out, add_sub[3], not_15_out, add_sub[1], add_sub[0]);
  and and_7 (SLTU, not_14_out, add_sub[3], add_sub[2], not_17_out, not_16_out);
  not not_14 (not_14_out, add_sub[4]);
  not not_15 (not_15_out, add_sub[2]);
  not not_16 (not_16_out, add_sub[0]);
  not not_17 (not_17_out, add_sub[1]);
endmodule

module D_latch (
  input  in_1,
  input  in_2,
  output out_3,
  output out_4
);

  wire nand_1_out, nand_2_out, nand_3_out, nand_4_out;

  nand nand_1 (nand_1_out, nand_4_out, nand_2_out);
  nand nand_2 (nand_2_out, nand_1_out, in_1);
  nand nand_3 (nand_3_out, nand_2_out, in_1, nand_4_out);
  nand nand_4 (nand_4_out, nand_3_out, in_2);
  nand nand_5 (out_3, nand_2_out, out_4);
  nand nand_6 (out_4, out_3, nand_3_out);
endmodule

module D_Latch_w_R (
  input  Clock,
  input  Data,
  input  Reset,
  output Data_Out,
  output out_5
);

  wire nand_1_out, nand_2_out, nand_3_out, nand_4_out, not_1_out, not_2_out, or_1_out;

  or or_1 (or_1_out, not_2_out, Data);
  not not_1 (not_1_out, Reset);
  nand nand_1 (nand_1_out, nand_4_out, nand_2_out);
  nand nand_2 (nand_2_out, nand_1_out, not_1_out, Clock);
  nand nand_3 (nand_3_out, nand_2_out, Clock, nand_4_out);
  nand nand_4 (nand_4_out, nand_3_out, not_1_out, or_1_out);
  nand nand_5 (Data_Out, nand_2_out, out_5);
  nand nand_6 (out_5, Data_Out, not_1_out, nand_3_out);
  not not_2 (not_2_out, Data_Out);
endmodule

module D_Latch_w_R_and_Set (
  input  Clock,
  input  Data,
  input  A_Reset,
  input  Preset0,
  output Data_Out,
  output out_6
);

  wire nand_1_out, nand_2_out, nand_3_out, nand_4_out, not_1_out, or_1_out;

  not not_1 (not_1_out, A_Reset);
  nand nand_1 (nand_1_out, or_1_out, nand_2_out);
  nand nand_2 (nand_2_out, nand_1_out, not_1_out, Clock);
  nand nand_3 (nand_3_out, nand_2_out, Clock, or_1_out);
  nand nand_4 (nand_4_out, nand_3_out, not_1_out, Data);
  or or_1 (or_1_out, nand_4_out, Preset0);
  nand nand_5 (Data_Out, nand_2_out, out_6);
  nand nand_6 (out_6, Data_Out, not_1_out, nand_3_out);
endmodule

module control (
  input  a,
  input  b,
  input  c,
  input  d,
  output regD,
  output jump,
  output out_7,
  output out_8,
  output memRead,
  output mem2reg,
  output memWrite,
  output regwrite,
  output AluSrc,
  output AluOp1,
  output AluOp2
);

  wire and_1_out, and_2_out, and_3_out, and_4_out, and_7_out, and_8_out, and_9_out, and_10_out, and_12_out,
       and_13_out, and_17_out, and_18_out, and_19_out, and_20_out, and_21_out, not_1_out, not_2_out,
       not_3_out, not_4_out, not_5_out, not_6_out, not_7_out, not_8_out, not_9_out, not_10_out, not_11_out,
       not_12_out, not_13_out, not_14_out, not_15_out, not_16_out, not_17_out, not_18_out, not_19_out,
       not_20_out, not_21_out, not_22_out, not_23_out, not_24_out, not_25_out, not_26_out, not_27_out,
       not_28_out, not_29_out, not_30_out, or_1_out, or_4_out;

  not not_1 (not_1_out, a);
  and and_1 (and_1_out, not_1_out, not_2_out);
  not not_2 (not_2_out, c);
  not not_3 (not_3_out, b);
  and and_2 (and_2_out, not_3_out, not_4_out);
  not not_4 (not_4_out, c);
  not not_5 (not_5_out, a);
  and and_3 (and_3_out, not_5_out, b, d);
  and and_4 (and_4_out, a, c, d);
  not not_6 (not_6_out, b);
  not not_7 (not_7_out, d);
  not not_8 (not_8_out, c);
  not not_9 (not_9_out, d);
  and and_5 (out_7, a, b, d);
  and and_6 (out_8, a, b, c);
  not not_10 (not_10_out, a);
  not not_11 (not_11_out, b);
  not not_12 (not_12_out, d);
  not not_13 (not_13_out, a);
  not not_14 (not_14_out, b);
  not not_15 (not_15_out, d);
  not not_16 (not_16_out, a);
  not not_17 (not_17_out, b);
  and and_7 (and_7_out, d, a);
  not not_18 (not_18_out, c);
  not not_19 (not_19_out, a);
  not not_20 (not_20_out, d);
  or or_1 (or_1_out, not_20_out, b);
  not not_21 (not_21_out, a);
  not not_22 (not_22_out, d);
  not not_23 (not_23_out, a);
  not not_24 (not_24_out, c);
  and and_8 (and_8_out, not_23_out, not_24_out, d);
  not not_25 (not_25_out, c);
  and and_9 (and_9_out, b, not_25_out, d);
  and and_10 (and_10_out, a, b, c);
  not not_26 (not_26_out, a);
  and and_11 (AluOp2, not_26_out, b, not_27_out);
  not not_27 (not_27_out, c);
  or or_2 (regD, and_1_out, and_2_out, and_3_out, and_4_out);
  and and_12 (and_12_out, a, not_6_out, c, not_7_out);
  or or_3 (jump, and_12_out, and_13_out);
  and and_13 (and_13_out, a, b, not_8_out, not_9_out);
  and and_14 (memRead, not_10_out, not_11_out, c, not_12_out);
  and and_15 (mem2reg, not_13_out, not_14_out, c, not_15_out);
  and and_16 (memWrite, not_16_out, not_17_out, c, d);
  or or_4 (or_4_out, and_7_out, not_18_out);
  and and_17 (and_17_out, or_4_out, not_28_out);
  not not_28 (not_28_out, b);
  and and_18 (and_18_out, not_19_out, or_1_out);
  not not_29 (not_29_out, d);
  and and_19 (and_19_out, not_21_out, not_29_out, c);
  and and_20 (and_20_out, not_21_out, b, c, not_22_out);
  and and_21 (and_21_out, not_21_out, d, not_30_out, c);
  not not_30 (not_30_out, b);
  or or_5 (AluOp1, and_8_out, and_9_out, and_10_out);
  or or_6 (regwrite, and_17_out, and_18_out);
  or or_7 (AluSrc, and_19_out, and_20_out, and_21_out);

  // Notes on the sheet:
  //   4
  //   3
  //   2
  //   1
  //   ~c *( a * d + ~b) +  ~d * (c + ~a) 
endmodule

module signExtend (
  input  [5:0] in_1,
  input  in_2,
  output [15:0] out_3
);

  wire and_1_out;

  Transistor transistor_1 (.in(1'b0), .out(out_3[15]), .gate(in_2));
  and and_1 (and_1_out, in_1[5], in_2);
  Transistor #(.\type ("n"), .gate("br")) transistor_2 (.in(and_1_out), .out(out_3[15]), .gate(in_2));

  assign out_3[14:0] = {{9{out_3[15]}}, in_1};
endmodule

module reg_Write_Decode (
  input  in_1,
  input  [2:0] in_2,
  output R0,
  output R1,
  output R2,
  output R3,
  output R4,
  output R5,
  output R6,
  output R7
);

  wire decoder_1_out0, decoder_1_out1, decoder_1_out2, decoder_1_out3, decoder_1_out4, decoder_1_out5,
       decoder_1_out6, decoder_1_out7;

  and and_1 (R0, 1'b0, decoder_1_out0);
  and and_2 (R2, in_1, decoder_1_out2);
  and and_3 (R1, in_1, decoder_1_out1);
  and and_4 (R3, in_1, decoder_1_out3);
  and and_5 (R4, in_1, decoder_1_out4);
  Decoder #(.select(3), .enable("false")) decoder_1 (
    .out0(decoder_1_out0), .out1(decoder_1_out1), .out2(decoder_1_out2), .out3(decoder_1_out3),
    .out4(decoder_1_out4), .out5(decoder_1_out5), .out6(decoder_1_out6), .out7(decoder_1_out7), .sel(in_2));
  and and_6 (R6, in_1, decoder_1_out6);
  and and_7 (R5, in_1, decoder_1_out5);
  and and_8 (R7, in_1, decoder_1_out7);
endmodule

module add_extend_12_16 (
  input  [11:0] in_1,
  output [15:0] out_2
);


  assign out_2 = {4'b0000, in_1};
endmodule

module mem_bit (
  input  Y,
  input  Clock,
  input  Data,
  input  Write,
  input  X,
  input  reset,
  output out_7
);

  wire and_1_out, and_2_out, and_3_out;

  and and_1 (and_1_out, Write, and_2_out);
  and and_2 (and_2_out, Y, X);
  and and_3 (and_3_out, Clock, and_1_out);
  D_Latch_w_R_and_Set d_latch_w_r_and_set_1 (
    .Clock(and_3_out), .Data(Data), .A_Reset(reset), .Preset0(1'b0), .Data_Out(out_7));  // open: out_6
endmodule

module tty (
  input  [31:0] in_1,
  input  [31:0] in_2,
  input  [6:0] in_3,
  input  in_4,
  input  in_5,
  input  in_6
);

  TTY #(.rows(12)) tty_1 (.data(in_3), .clk(in_5), .we(in_6), .clr(in_4));
  // DotMatrix #(.inputtype("select"), .matrixcols(32), .matrixrows(32)) dotmatrix_1: pin names not known; wires that end beside it: in_1, in_2

  // Notes on the sheet:
  //   83 65 77
endmodule

module control_final (
  input  a,
  input  c,
  input  b,
  input  d,
  input  x,
  input  y,
  input  z,
  output out_8,
  output jump,
  output RegD,
  output [1:0] branch,
  output MemRead,
  output MemWrite,
  output Reg2Imm,
  output Jump2Ra,
  output RegWrite,
  output AluSrc,
  output AluOp5,
  output SignExtend,
  output AluOp4,
  output AluOp3,
  output AluOp2,
  output AluOp1
);

  wire and_1_out, and_2_out, and_3_out, and_4_out, and_5_out, and_6_out, and_7_out, and_8_out, and_9_out,
       and_10_out, and_11_out, and_12_out, and_13_out, and_14_out, and_15_out, and_16_out, and_17_out,
       and_18_out, and_19_out, and_20_out, and_21_out, and_22_out, and_23_out, and_24_out, and_25_out,
       and_26_out, and_27_out, and_28_out, and_29_out, and_30_out, and_31_out, and_32_out, and_33_out,
       and_36_out, and_38_out, and_39_out, and_40_out, and_41_out, and_43_out, and_44_out, and_49_out,
       and_50_out, and_51_out, and_52_out, and_53_out, and_54_out, and_55_out, and_56_out, and_57_out,
       and_58_out, and_59_out, and_60_out, and_61_out, and_62_out, and_63_out, and_64_out, and_65_out,
       and_66_out, and_67_out, nor_1_out, not_1_out, not_2_out, not_3_out, not_4_out, not_5_out, not_6_out,
       not_7_out, not_8_out, not_9_out, not_10_out, not_11_out, not_12_out, not_13_out, not_14_out,
       not_15_out, not_16_out, not_17_out, not_18_out, not_19_out, not_20_out, not_21_out, not_22_out,
       not_23_out, not_24_out, not_25_out, not_26_out, not_27_out, not_28_out, not_29_out, not_30_out,
       not_31_out, not_32_out, not_33_out, not_34_out, not_35_out, not_36_out, not_37_out, not_38_out,
       not_39_out, not_40_out, not_41_out, not_42_out, not_43_out, not_44_out, not_45_out, not_46_out,
       not_47_out, not_48_out, not_49_out, not_50_out, not_51_out, not_52_out, not_53_out, not_54_out,
       not_55_out, not_56_out, not_57_out, not_58_out, not_59_out, not_60_out, not_61_out, not_62_out,
       not_63_out, not_64_out, not_65_out, not_66_out, not_67_out, not_68_out, not_69_out, not_70_out,
       not_71_out, not_72_out, not_73_out, not_74_out, not_75_out, not_76_out, not_77_out, not_78_out,
       not_79_out, not_80_out, not_81_out, not_82_out, not_83_out, not_84_out, not_85_out, not_86_out,
       not_87_out, not_88_out, not_89_out, not_90_out, not_91_out, not_92_out, not_93_out, not_94_out,
       not_95_out, not_96_out, not_97_out, not_98_out, not_99_out, not_100_out, not_101_out, not_102_out,
       not_103_out, not_104_out, not_105_out, not_106_out, not_107_out, not_108_out, not_109_out,
       not_110_out, not_111_out, or_1_out, or_2_out, or_3_out, or_4_out, or_5_out, or_6_out, or_7_out,
       or_8_out, or_16_out, or_17_out, or_18_out, or_19_out, or_20_out;

  not not_1 (not_1_out, c);
  not not_2 (not_2_out, d);
  not not_3 (not_3_out, c);
  not not_4 (not_4_out, y);
  not not_5 (not_5_out, d);
  not not_6 (not_6_out, y);
  not not_7 (not_7_out, c);
  not not_8 (not_8_out, d);
  not not_9 (not_9_out, c);
  not not_10 (not_10_out, x);
  not not_11 (not_11_out, c);
  not not_12 (not_12_out, z);
  not not_13 (not_13_out, d);
  not not_14 (not_14_out, x);
  not not_15 (not_15_out, c);
  not not_16 (not_16_out, x);
  not not_17 (not_17_out, y);
  not not_18 (not_18_out, c);
  not not_19 (not_19_out, x);
  not not_20 (not_20_out, z);
  not not_21 (not_21_out, c);
  not not_22 (not_22_out, c);
  and and_1 (and_1_out, not_22_out, not_23_out);
  not not_23 (not_23_out, d);
  not not_24 (not_24_out, c);
  and and_2 (and_2_out, not_24_out, not_25_out);
  not not_25 (not_25_out, x);
  not not_26 (not_26_out, c);
  and and_3 (and_3_out, not_26_out, not_27_out);
  not not_27 (not_27_out, y);
  not not_28 (not_28_out, c);
  and and_4 (and_4_out, not_28_out, not_29_out);
  not not_29 (not_29_out, z);
  not not_30 (not_30_out, d);
  and and_5 (and_5_out, not_30_out, x, not_31_out);
  not not_31 (not_31_out, y);
  and and_6 (and_6_out, c, not_32_out, not_33_out);
  not not_32 (not_32_out, d);
  not not_33 (not_33_out, x);
  and and_7 (and_7_out, c, not_34_out, not_35_out);
  not not_34 (not_34_out, d);
  not not_35 (not_35_out, y);
  not not_36 (not_36_out, c);
  and and_8 (and_8_out, not_36_out, d, not_37_out);
  not not_37 (not_37_out, x);
  not not_38 (not_38_out, c);
  and and_9 (and_9_out, not_38_out, d, not_39_out);
  not not_39 (not_39_out, y);
  not not_40 (not_40_out, c);
  and and_10 (and_10_out, not_40_out, d, not_41_out);
  not not_41 (not_41_out, z);
  not not_42 (not_42_out, c);
  not not_43 (not_43_out, d);
  not not_44 (not_44_out, d);
  not not_45 (not_45_out, y);
  not not_46 (not_46_out, c);
  not not_47 (not_47_out, z);
  not not_48 (not_48_out, c);
  not not_49 (not_49_out, d);
  not not_50 (not_50_out, c);
  not not_51 (not_51_out, x);
  not not_52 (not_52_out, z);
  not not_53 (not_53_out, d);
  not not_54 (not_54_out, x);
  not not_55 (not_55_out, c);
  not not_56 (not_56_out, y);
  not not_57 (not_57_out, c);
  not not_58 (not_58_out, d);
  not not_59 (not_59_out, c);
  not not_60 (not_60_out, y);
  not not_61 (not_61_out, d);
  not not_62 (not_62_out, x);
  not not_63 (not_63_out, d);
  not not_64 (not_64_out, y);
  not not_65 (not_65_out, c);
  not not_66 (not_66_out, y);
  and and_11 (and_11_out, not_1_out, y, not_2_out);
  and and_12 (and_12_out, not_3_out, not_4_out);
  and and_13 (and_13_out, not_5_out, not_6_out);
  and and_14 (and_14_out, not_7_out, not_8_out, x, z);
  and and_15 (and_15_out, not_9_out, d, not_10_out);
  and and_16 (and_16_out, not_11_out, d, not_12_out);
  and and_17 (and_17_out, c, not_13_out, not_14_out);
  and and_18 (and_18_out, not_15_out, d, not_16_out, not_17_out);
  or or_1 (or_1_out, and_18_out, and_19_out);
  and and_19 (and_19_out, not_18_out, d, not_19_out, not_20_out);
  and and_20 (and_20_out, not_21_out, d, x, y, z);
  or or_2 (or_2_out, and_1_out, and_2_out, and_3_out, and_4_out, and_5_out);
  or or_3 (or_3_out, and_6_out, and_7_out);
  or or_4 (or_4_out, and_8_out, and_9_out, and_10_out);
  and and_21 (and_21_out, not_42_out, not_43_out, x);
  or or_5 (or_5_out, and_21_out, and_22_out, and_23_out);
  and and_22 (and_22_out, not_44_out, x, not_45_out);
  and and_23 (and_23_out, not_46_out, x, y, not_47_out);
  and and_24 (and_24_out, not_48_out, not_49_out, y);
  and and_25 (and_25_out, not_50_out, not_51_out, y, not_52_out);
  and and_26 (and_26_out, not_53_out, not_54_out, y);
  and and_27 (and_27_out, not_55_out, d, x, not_56_out, z);
  and and_28 (and_28_out, not_57_out, not_58_out, z);
  and and_29 (and_29_out, not_59_out, not_60_out, z);
  and and_30 (and_30_out, not_61_out, not_62_out, z);
  and and_31 (and_31_out, not_63_out, not_64_out, z);
  and and_32 (and_32_out, not_65_out, d, x, not_66_out);
  nor nor_1 (nor_1_out, a, b);
  or or_6 (or_6_out, and_11_out, and_12_out, and_13_out, and_14_out, and_15_out, and_16_out, and_17_out);
  or or_7 (or_7_out, and_24_out, and_25_out, and_26_out, and_27_out);
  or or_8 (or_8_out, and_28_out, and_29_out, and_30_out, and_31_out, and_32_out);
  and and_33 (and_33_out, nor_1_out, or_6_out);
  and and_34 (Reg2Imm, nor_1_out, or_1_out);
  and and_35 (Jump2Ra, nor_1_out, and_20_out);
  and and_36 (and_36_out, nor_1_out, or_2_out);
  or or_9 (RegWrite, and_36_out, or_16_out);
  and and_37 (AluOp5, nor_1_out, or_3_out);
  and and_38 (and_38_out, or_4_out, nor_1_out);
  or or_10 (AluOp4, and_38_out, or_17_out);
  and and_39 (and_39_out, or_5_out, nor_1_out);
  or or_11 (AluOp3, and_39_out, or_18_out);
  and and_40 (and_40_out, or_7_out, nor_1_out);
  or or_12 (AluOp2, and_40_out, or_19_out);
  and and_41 (and_41_out, or_8_out, nor_1_out);
  or or_13 (AluOp1, and_41_out, or_20_out);
  or or_14 (RegD, and_33_out, and_33_out);
  not not_67 (not_67_out, b);
  not not_68 (not_68_out, c);
  not not_69 (not_69_out, d);
  not not_70 (not_70_out, c);
  not not_71 (not_71_out, d);
  not not_72 (not_72_out, b);
  not not_73 (not_73_out, c);
  not not_74 (not_74_out, b);
  not not_75 (not_75_out, d);
  not not_76 (not_76_out, a);
  not not_77 (not_77_out, b);
  not not_78 (not_78_out, c);
  not not_79 (not_79_out, c);
  not not_80 (not_80_out, a);
  not not_81 (not_81_out, d);
  not not_82 (not_82_out, c);
  not not_83 (not_83_out, a);
  not not_84 (not_84_out, a);
  not not_85 (not_85_out, d);
  not not_86 (not_86_out, a);
  not not_87 (not_87_out, b);
  not not_88 (not_88_out, c);
  not not_89 (not_89_out, d);
  not not_90 (not_90_out, b);
  not not_91 (not_91_out, c);
  not not_92 (not_92_out, b);
  not not_93 (not_93_out, d);
  not not_94 (not_94_out, a);
  not not_95 (not_95_out, b);
  not not_96 (not_96_out, c);
  not not_97 (not_97_out, d);
  not not_98 (not_98_out, a);
  not not_99 (not_99_out, b);
  not not_100 (not_100_out, c);
  not not_101 (not_101_out, d);
  not not_102 (not_102_out, c);
  not not_103 (not_103_out, d);
  not not_104 (not_104_out, d);
  not not_105 (not_105_out, b);
  not not_106 (not_106_out, c);
  not not_107 (not_107_out, d);
  not not_108 (not_108_out, c);
  and and_42 (out_8, a, b, c, d);
  and and_43 (and_43_out, a, not_67_out, c, d);
  and and_44 (and_44_out, a, b, not_68_out, not_69_out);
  and and_45 (branch[0], a, b, not_70_out, d);
  and and_46 (branch[1], a, b, c, not_71_out);
  and and_47 (MemRead, a, not_72_out, not_73_out, d);
  and and_48 (MemWrite, a, not_74_out, c, not_75_out);
  and and_49 (and_49_out, not_76_out, b);
  and and_50 (and_50_out, a, not_77_out, not_78_out);
  and and_51 (and_51_out, a, b, ~c, ~d);  // AND_Gate
  and and_52 (and_52_out, not_79_out, not_80_out, b, not_81_out);
  and and_53 (and_53_out, not_82_out, not_83_out, b, d);
  and and_54 (and_54_out, c, not_84_out, b, not_85_out);
  and and_55 (and_55_out, c, not_86_out, b, d);
  and and_56 (and_56_out, d, a, not_87_out, not_88_out);
  and and_57 (and_57_out, not_89_out, a, not_90_out, not_91_out);
  and and_58 (and_58_out, a, not_92_out, c, not_93_out);
  not not_109 (not_109_out, a);
  not not_110 (not_110_out, c);
  not not_111 (not_111_out, d);
  and and_59 (and_59_out, not_94_out, b, c, d);
  and and_60 (and_60_out, a, not_95_out, not_96_out, not_97_out);
  and and_61 (and_61_out, not_98_out, b, c, d);
  and and_62 (and_62_out, a, not_99_out, not_100_out, not_101_out);
  and and_63 (and_63_out, b, not_102_out, d);
  and and_64 (and_64_out, b, c, not_103_out);
  and and_65 (and_65_out, b, c, not_104_out);
  and and_66 (and_66_out, a, not_105_out, not_106_out, not_107_out);
  and and_67 (and_67_out, a, b, not_108_out, d);
  or or_15 (jump, and_43_out, and_44_out);
  or or_16 (or_16_out, and_49_out, and_51_out, and_50_out);
  and and_68 (SignExtend, b, not_109_out, not_110_out, not_111_out);
  or or_17 (or_17_out, and_59_out, and_60_out);
  or or_18 (or_18_out, and_61_out, and_62_out);
  or or_19 (or_19_out, and_63_out, and_64_out);
  or or_20 (or_20_out, and_65_out, and_66_out, and_67_out);
  or or_21 (AluSrc, and_52_out, and_53_out, and_54_out, and_55_out, and_57_out, and_58_out, and_56_out);

  // Notes on the sheet:
  //   A B C D
endmodule

module debug (
  input  [14:0] in_1,
  output Add,
  output SLL,
  output MUTL,
  output ADDI,
  output Sub,
  output SRL,
  output MULTU,
  output ADDIU,
  output AddU,
  output SRA,
  output DIV,
  output SUBIU,
  output SubU,
  output SLLR,
  output DIVU,
  output SLTI,
  output AND,
  output SRLR,
  output MFHI,
  output SLTIU,
  output OR,
  output STL,
  output MFLO,
  output LHW,
  output NOR,
  output SLTU,
  output SHW,
  output XOR,
  output JR,
  output J,
  output JAL,
  output BEQ,
  output BNE,
  output Syscall
);

  wire and_23_out, and_24_out, not_1_out, not_2_out, not_3_out, not_4_out, not_5_out, not_6_out, not_7_out,
       not_8_out, not_9_out, not_10_out, not_11_out, not_12_out, not_13_out, not_14_out, not_15_out,
       not_16_out, not_17_out, not_18_out, not_19_out, not_20_out, not_21_out, not_22_out, not_23_out,
       not_24_out, not_25_out, not_26_out, not_27_out, not_28_out, not_29_out, not_30_out, not_31_out,
       not_32_out, not_33_out, not_34_out, not_35_out, not_36_out, not_37_out, not_38_out, not_39_out,
       not_40_out, not_41_out, not_42_out, not_43_out, not_44_out, not_45_out, not_46_out, not_47_out,
       not_48_out, not_49_out, not_50_out, not_51_out, not_52_out, not_53_out, not_54_out, not_55_out,
       not_56_out, not_57_out, not_58_out, not_59_out, not_60_out;

  not not_1 (not_1_out, in_1[14]);
  not not_2 (not_2_out, in_1[13]);
  not not_3 (not_3_out, in_1[11]);
  not not_4 (not_4_out, in_1[12]);
  not not_5 (not_5_out, in_1[8]);
  not not_6 (not_6_out, in_1[10]);
  not not_7 (not_7_out, in_1[9]);
  not not_8 (not_8_out, in_1[7]);
  not not_9 (not_9_out, in_1[6]);
  not not_10 (not_10_out, in_1[3]);
  not not_11 (not_11_out, in_1[5]);
  not not_12 (not_12_out, in_1[4]);
  not not_13 (not_13_out, in_1[2]);
  not not_14 (not_14_out, in_1[0]);
  not not_15 (not_15_out, in_1[1]);
  and and_1 (Add, in_1[14], not_2_out, not_4_out, not_3_out, not_7_out, not_6_out, not_5_out, not_8_out, in_1[6], not_11_out, not_12_out, not_10_out, not_13_out, not_15_out, not_14_out);
  and and_2 (Sub, in_1[14], not_2_out, not_4_out, not_3_out, not_7_out, not_6_out, not_5_out, not_8_out, in_1[6], not_11_out, not_12_out, not_10_out, not_13_out, not_15_out, in_1[0]);
  and and_3 (AddU, in_1[14], not_2_out, not_4_out, not_3_out, not_7_out, not_6_out, not_5_out, not_8_out, in_1[6], not_11_out, not_12_out, not_10_out, not_13_out, in_1[1], not_14_out);
  and and_4 (SubU, in_1[14], not_2_out, not_4_out, not_3_out, not_7_out, not_6_out, not_5_out, not_8_out, in_1[6], not_11_out, not_12_out, not_10_out, not_13_out, in_1[1], in_1[0]);
  and and_5 (AND, in_1[14], not_2_out, not_4_out, not_3_out, not_7_out, not_6_out, not_5_out, not_8_out, in_1[6], not_11_out, not_12_out, not_10_out, in_1[2], not_15_out, not_14_out);
  and and_6 (OR, in_1[14], not_2_out, not_4_out, not_3_out, not_7_out, not_6_out, not_5_out, not_8_out, in_1[6], not_11_out, not_12_out, not_10_out, in_1[2], not_15_out, in_1[0]);
  and and_7 (NOR, in_1[14], not_2_out, not_4_out, not_3_out, not_7_out, not_6_out, not_5_out, not_8_out, in_1[6], not_11_out, not_12_out, not_10_out, in_1[2], in_1[1], not_14_out);
  and and_8 (XOR, in_1[14], not_2_out, not_4_out, not_3_out, not_7_out, not_6_out, not_5_out, not_8_out, in_1[6], not_11_out, not_12_out, not_10_out, in_1[2], in_1[1], in_1[0]);
  not not_16 (not_16_out, in_1[14]);
  not not_17 (not_17_out, in_1[13]);
  not not_18 (not_18_out, in_1[11]);
  not not_19 (not_19_out, in_1[9]);
  not not_20 (not_20_out, in_1[12]);
  not not_21 (not_21_out, in_1[7]);
  not not_22 (not_22_out, in_1[10]);
  not not_23 (not_23_out, in_1[8]);
  not not_24 (not_24_out, in_1[6]);
  not not_25 (not_25_out, in_1[5]);
  not not_26 (not_26_out, in_1[2]);
  not not_27 (not_27_out, in_1[3]);
  not not_28 (not_28_out, in_1[4]);
  not not_29 (not_29_out, in_1[0]);
  not not_30 (not_30_out, in_1[1]);
  and and_9 (SLL, in_1[14], in_1[13], not_20_out, not_18_out, not_19_out, not_22_out, not_23_out, not_21_out, in_1[6], not_25_out, not_28_out, in_1[3], not_26_out, not_30_out, not_29_out);
  and and_10 (SRL, in_1[14], in_1[13], not_20_out, not_18_out, not_19_out, not_22_out, not_23_out, not_21_out, in_1[6], not_25_out, not_28_out, in_1[3], not_26_out, not_30_out, in_1[0]);
  and and_11 (SRA, in_1[14], in_1[13], not_20_out, not_18_out, not_19_out, not_22_out, not_23_out, not_21_out, in_1[6], not_25_out, not_28_out, in_1[3], not_26_out, in_1[1], not_29_out);
  and and_12 (SLLR, in_1[14], not_17_out, not_20_out, not_18_out, not_19_out, not_22_out, not_23_out, not_21_out, in_1[6], not_25_out, not_28_out, in_1[3], not_26_out, not_30_out, not_29_out);
  and and_13 (SRLR, in_1[14], not_17_out, not_20_out, not_18_out, not_19_out, not_22_out, not_23_out, not_21_out, in_1[6], not_25_out, not_28_out, in_1[3], not_26_out, not_30_out, in_1[0]);
  and and_14 (STL, in_1[14], not_17_out, not_20_out, not_18_out, not_19_out, not_22_out, not_23_out, not_21_out, in_1[6], not_25_out, not_28_out, in_1[3], not_26_out, in_1[1], in_1[0]);
  and and_15 (SLTU, in_1[14], not_17_out, not_20_out, not_18_out, not_19_out, not_22_out, not_23_out, not_21_out, in_1[6], not_25_out, not_28_out, in_1[3], in_1[2], not_30_out, not_29_out);
  and and_16 (JR, not_16_out, not_17_out, in_1[12], not_18_out, not_19_out, not_22_out, not_23_out, not_21_out, not_24_out, not_25_out, not_28_out, not_27_out, not_26_out, not_30_out, not_29_out);
  not not_31 (not_31_out, in_1[12]);
  not not_32 (not_32_out, in_1[14]);
  not not_33 (not_33_out, in_1[13]);
  not not_34 (not_34_out, in_1[11]);
  not not_35 (not_35_out, in_1[10]);
  not not_36 (not_36_out, in_1[9]);
  not not_37 (not_37_out, in_1[7]);
  not not_38 (not_38_out, in_1[8]);
  not not_39 (not_39_out, in_1[4]);
  not not_40 (not_40_out, in_1[6]);
  not not_41 (not_41_out, in_1[5]);
  not not_42 (not_42_out, in_1[3]);
  not not_43 (not_43_out, in_1[2]);
  not not_44 (not_44_out, in_1[1]);
  not not_45 (not_45_out, in_1[0]);
  and and_17 (MUTL, in_1[14], not_33_out, not_31_out, not_34_out, not_36_out, not_35_out, not_38_out, not_37_out, not_40_out, not_41_out, in_1[4], not_42_out, not_43_out, not_44_out, not_45_out);
  and and_18 (MULTU, in_1[14], not_33_out, not_31_out, not_34_out, not_36_out, not_35_out, not_38_out, not_37_out, not_40_out, not_41_out, in_1[4], not_42_out, not_43_out, not_44_out, in_1[0]);
  and and_19 (DIV, in_1[14], not_33_out, not_31_out, not_34_out, not_36_out, not_35_out, not_38_out, not_37_out, not_40_out, not_41_out, in_1[4], not_42_out, not_43_out, in_1[1], not_45_out);
  and and_20 (DIVU, in_1[14], not_33_out, not_31_out, not_34_out, not_36_out, not_35_out, not_38_out, not_37_out, not_40_out, not_41_out, in_1[4], not_42_out, not_43_out, in_1[1], in_1[0]);
  and and_21 (MFHI, in_1[14], not_33_out, not_31_out, not_34_out, not_36_out, not_35_out, not_38_out, not_37_out, in_1[6], not_41_out, in_1[4], not_42_out, in_1[2], not_44_out, not_45_out);
  and and_22 (MFLO, in_1[14], not_33_out, not_31_out, not_34_out, not_36_out, not_35_out, not_38_out, not_37_out, in_1[6], not_41_out, in_1[4], not_42_out, in_1[2], not_44_out, in_1[0]);
  and and_23 (and_23_out, not_32_out, not_33_out, not_31_out, not_34_out, not_36_out, not_35_out, not_38_out, not_37_out, not_40_out, not_41_out, not_39_out, not_42_out, not_43_out, not_44_out, not_45_out);
  and and_24 (and_24_out, not_32_out, not_33_out, not_31_out, not_34_out, not_36_out, not_35_out, not_38_out, not_37_out, not_40_out, not_41_out, not_39_out, not_42_out, not_43_out, not_44_out, not_45_out);
  not not_46 (not_46_out, in_1[14]);
  not not_47 (not_47_out, in_1[13]);
  not not_48 (not_48_out, in_1[12]);
  not not_49 (not_49_out, in_1[11]);
  not not_50 (not_50_out, in_1[10]);
  not not_51 (not_51_out, in_1[9]);
  not not_52 (not_52_out, in_1[6]);
  not not_53 (not_53_out, in_1[8]);
  not not_54 (not_54_out, in_1[7]);
  not not_55 (not_55_out, in_1[5]);
  not not_56 (not_56_out, in_1[4]);
  not not_57 (not_57_out, in_1[2]);
  not not_58 (not_58_out, in_1[1]);
  not not_59 (not_59_out, in_1[3]);
  not not_60 (not_60_out, in_1[0]);
  and and_25 (ADDI, not_46_out, not_47_out, not_48_out, not_49_out, not_51_out, not_50_out, not_53_out, not_54_out, in_1[6], in_1[5], not_56_out, not_59_out, not_57_out, not_58_out, not_60_out);
  and and_26 (ADDIU, not_46_out, not_47_out, not_48_out, not_49_out, not_51_out, not_50_out, not_53_out, not_54_out, in_1[6], in_1[5], not_56_out, not_59_out, not_57_out, in_1[1], not_60_out);
  and and_27 (SUBIU, not_46_out, not_47_out, not_48_out, not_49_out, not_51_out, not_50_out, not_53_out, not_54_out, in_1[6], in_1[5], not_56_out, not_59_out, not_57_out, in_1[1], in_1[0]);
  and and_28 (SLTI, not_46_out, not_47_out, not_48_out, not_49_out, not_51_out, not_50_out, not_53_out, not_54_out, in_1[6], in_1[5], not_56_out, in_1[3], in_1[2], not_58_out, not_60_out);
  and and_29 (SLTIU, not_46_out, not_47_out, not_48_out, not_49_out, not_51_out, not_50_out, not_53_out, not_54_out, in_1[6], in_1[5], not_56_out, in_1[3], in_1[2], not_58_out, in_1[0]);
  and and_30 (LHW, not_46_out, not_47_out, not_48_out, not_49_out, not_51_out, not_50_out, in_1[8], not_54_out, in_1[6], in_1[5], not_56_out, not_59_out, not_57_out, not_58_out, not_60_out);
  and and_31 (SHW, not_46_out, not_47_out, not_48_out, not_49_out, not_51_out, not_50_out, not_53_out, in_1[7], not_52_out, in_1[5], not_56_out, not_59_out, not_57_out, not_58_out, not_60_out);
  and and_32 (J, not_46_out, not_47_out, not_48_out, in_1[11], not_51_out, not_50_out, not_53_out, not_54_out, not_52_out, not_55_out, not_56_out, not_59_out, not_57_out, not_58_out, not_60_out);
  and and_33 (JAL, not_46_out, not_47_out, not_48_out, in_1[11], not_51_out, not_50_out, not_53_out, not_54_out, in_1[6], not_55_out, not_56_out, not_59_out, not_57_out, not_58_out, not_60_out);
  and and_34 (BEQ, not_46_out, not_47_out, not_48_out, not_49_out, in_1[9], not_50_out, not_53_out, not_54_out, not_52_out, not_55_out, not_56_out, not_59_out, not_57_out, in_1[1], in_1[0]);
  and and_35 (BNE, not_46_out, not_47_out, not_48_out, not_49_out, not_51_out, in_1[10], not_53_out, not_54_out, not_52_out, not_55_out, not_56_out, not_59_out, not_57_out, in_1[1], in_1[0]);
  and and_36 (Syscall, not_46_out, not_47_out, not_48_out, not_49_out, not_51_out, not_50_out, not_53_out, not_54_out, not_52_out, not_55_out, not_56_out, not_59_out, not_57_out, not_58_out, not_60_out);

  // Other names for the same wires on the sheet: A1 = in_1[0]; A2 = in_1[1]; A3 = in_1[2]; A4 = in_1[3]; A5 = in_1[4];
  //   AS = in_1[5]; RW = in_1[6]; MW = in_1[7]; MR = in_1[8]; B1 = in_1[9]; B2 = in_1[10]; J_t = in_1[11];
  //   JR_t = in_1[12]; RI = in_1[13]; RD = in_1[14]
endmodule

module comparator_lessthan (
  input  [15:0] A,
  input  [15:0] B,
  input  SLTU,
  output [15:0] LESS
);

  wire compare_bit_1_o, compare_bit_2_o, compare_bit_3_o, compare_bit_4_o, compare_bit_5_o, compare_bit_6_o,
       compare_bit_7_o, compare_bit_8_o, compare_bit_9_o, compare_bit_10_o, compare_bit_11_o,
       compare_bit_12_o, compare_bit_13_o, compare_bit_14_o, compare_bit_15_o, compare_bit_16_o,
       compare_bit_17_o, or_1_out;

  Multiplexer #(.enable("false")) multiplexer_1 (.in0(or_1_out), .in1(compare_bit_1_o), .out(LESS[0]), .sel(SLTU));
  compare_bit compare_bit_1 (.a(B[15]), .b(A[15]), .c(compare_bit_3_o), .o(compare_bit_1_o));
  compare_bit compare_bit_2 (.a(A[15]), .b(B[15]), .c(1'b0), .o(compare_bit_2_o));
  or or_1 (or_1_out, compare_bit_2_o, compare_bit_3_o);
  compare_bit compare_bit_3 (.a(B[14]), .b(A[14]), .c(compare_bit_4_o), .o(compare_bit_3_o));
  compare_bit compare_bit_4 (.a(B[13]), .b(A[13]), .c(compare_bit_5_o), .o(compare_bit_4_o));
  compare_bit compare_bit_5 (.a(B[12]), .b(A[12]), .c(compare_bit_6_o), .o(compare_bit_5_o));
  compare_bit compare_bit_6 (.a(B[11]), .b(A[11]), .c(compare_bit_8_o), .o(compare_bit_6_o));
  compare_bit compare_bit_7 (.a(B[9]), .b(A[9]), .c(compare_bit_10_o), .o(compare_bit_7_o));
  compare_bit compare_bit_8 (.a(B[10]), .b(A[10]), .c(compare_bit_7_o), .o(compare_bit_8_o));
  compare_bit compare_bit_9 (.a(B[7]), .b(A[7]), .c(compare_bit_11_o), .o(compare_bit_9_o));
  compare_bit compare_bit_10 (.a(B[8]), .b(A[8]), .c(compare_bit_9_o), .o(compare_bit_10_o));
  compare_bit compare_bit_11 (.a(B[6]), .b(A[6]), .c(compare_bit_13_o), .o(compare_bit_11_o));
  compare_bit compare_bit_12 (.a(B[4]), .b(A[4]), .c(compare_bit_14_o), .o(compare_bit_12_o));
  compare_bit compare_bit_13 (.a(B[5]), .b(A[5]), .c(compare_bit_12_o), .o(compare_bit_13_o));
  compare_bit compare_bit_14 (.a(B[3]), .b(A[3]), .c(compare_bit_15_o), .o(compare_bit_14_o));
  compare_bit compare_bit_15 (.a(B[2]), .b(A[2]), .c(compare_bit_16_o), .o(compare_bit_15_o));
  compare_bit compare_bit_16 (.a(B[1]), .b(A[1]), .c(compare_bit_17_o), .o(compare_bit_16_o));
  compare_bit compare_bit_17 (.a(B[0]), .b(A[0]), .c(1'b0), .o(compare_bit_17_o));

  assign LESS[15:1] = {15{1'b0}};
endmodule

module compare_bit (
  input  a,
  input  b,
  input  c,
  output o
);

  wire and_1_out, and_2_out, and_3_out, not_1_out, not_2_out;

  not not_1 (not_1_out, b);
  not not_2 (not_2_out, b);
  and and_1 (and_1_out, not_1_out, c);
  and and_2 (and_2_out, a, not_2_out);
  and and_3 (and_3_out, a, c);
  or or_1 (o, and_1_out, and_2_out, and_3_out);
endmodule

module matrix_32bit (
  input  [4:0] in_1,
  input  [4:0] in_2,
  input  Clock,
  input  Write,
  input  Data,
  input  Reset,
  output [31:0] out_7,
  output [31:0] out_8,
  output [31:0] out_9,
  output [31:0] out_10,
  output [31:0] out_11,
  output [31:0] out_12,
  output [31:0] out_13,
  output [31:0] out_14,
  output [31:0] out_15,
  output [31:0] out_16,
  output [31:0] out_17,
  output [31:0] out_18,
  output [31:0] out_19,
  output [31:0] out_20,
  output [31:0] out_21,
  output [31:0] out_22,
  output [31:0] out_23,
  output [31:0] out_24,
  output [31:0] out_25,
  output [31:0] out_26,
  output [31:0] out_27,
  output [31:0] out_28,
  output [31:0] out_29,
  output [31:0] out_30,
  output [31:0] out_31,
  output [31:0] out_32,
  output [31:0] out_33,
  output [31:0] out_34,
  output [31:0] out_35,
  output [31:0] out_36,
  output [31:0] out_37,
  output [31:0] out_38
);

  wire undriven_10, undriven_11, undriven_12, undriven_13, undriven_14, undriven_15, undriven_16,
       undriven_17, undriven_18, undriven_19, undriven_20, undriven_21, undriven_22, undriven_23,
       undriven_24, undriven_25, undriven_26, undriven_27, undriven_28, undriven_29, undriven_30,
       undriven_31, undriven_32, undriven_33;
  wire [3:0] decoder_1_out0, decoder_1_out4, decoder_1_out8, decoder_1_out12, decoder_1_out16,
       decoder_1_out20, decoder_1_out24, decoder_1_out28, decoder_2_out0, decoder_2_out4, decoder_2_out8,
       decoder_2_out12, decoder_2_out16, decoder_2_out20, decoder_2_out24, decoder_2_out28, n4x4array_65_l,
       n4x4array_65_ll, n4x4array_65_r, n4x4array_65_r_2, n4x4array_66_l, n4x4array_66_ll, n4x4array_66_r,
       n4x4array_66_r_2, n4x4array_67_l, n4x4array_67_ll, n4x4array_67_r, n4x4array_67_r_2, n4x4array_68_l,
       n4x4array_68_ll, n4x4array_68_r, n4x4array_68_r_2, n4x4array_69_l, n4x4array_69_ll, n4x4array_69_r,
       n4x4array_69_r_2, n4x4array_70_l, n4x4array_70_ll, n4x4array_70_r, n4x4array_70_r_2, n4x4array_71_l,
       n4x4array_71_ll, n4x4array_71_r, n4x4array_71_r_2, n4x4array_72_l, n4x4array_72_ll, n4x4array_72_r,
       n4x4array_72_r_2, undriven, undriven_2, undriven_3, undriven_4, undriven_5, undriven_6, undriven_7,
       undriven_8, undriven_9;

  Decoder #(.select(5), .enable("false")) decoder_1 (
    .out0(decoder_1_out0[0]), .out1(decoder_1_out0[1]), .out2(decoder_1_out0[2]), .out3(decoder_1_out0[3]),
    .out4(decoder_1_out4[0]), .out5(decoder_1_out4[1]), .out6(decoder_1_out4[2]), .out7(decoder_1_out4[3]),
    .out8(decoder_1_out8[0]), .out9(decoder_1_out8[1]), .out10(decoder_1_out8[2]), .out11(decoder_1_out8[3]),
    .out12(decoder_1_out12[0]), .out13(decoder_1_out12[1]), .out14(decoder_1_out12[2]),
    .out15(decoder_1_out12[3]), .out16(decoder_1_out16[0]), .out17(decoder_1_out16[1]),
    .out18(decoder_1_out16[2]), .out19(decoder_1_out16[3]), .out20(decoder_1_out20[0]),
    .out21(decoder_1_out20[1]), .out22(decoder_1_out20[2]), .out23(decoder_1_out20[3]),
    .out24(decoder_1_out24[0]), .out25(decoder_1_out24[1]), .out26(decoder_1_out24[2]),
    .out27(decoder_1_out24[3]), .out28(decoder_1_out28[0]), .out29(decoder_1_out28[1]),
    .out30(decoder_1_out28[2]), .out31(decoder_1_out28[3]), .sel(in_1));
  _4x4array u_4x4array_1 (
    .Clock(Clock), .Y(decoder_1_out0), .reset(Reset), .Write(Write), .X(decoder_2_out0), .LL(out_11[31:28]),
    .Data(Data), .L(out_12[31:28]), .R(out_13[31:28]), .R_2(out_14[31:28]));
  _4x4array u_4x4array_2 (
    .Clock(Clock), .Y(decoder_1_out4), .reset(Reset), .Write(Write), .X(decoder_2_out0), .LL(out_11[27:24]),
    .Data(Data), .L(out_12[27:24]), .R(out_13[27:24]), .R_2(out_14[27:24]));
  _4x4array u_4x4array_3 (
    .Clock(Clock), .Y(decoder_1_out8), .reset(Reset), .Write(Write), .X(decoder_2_out0), .LL(out_11[23:20]),
    .Data(Data), .L(out_12[23:20]), .R(out_13[23:20]), .R_2(out_14[23:20]));
  _4x4array u_4x4array_4 (
    .Clock(Clock), .Y(decoder_1_out12), .reset(Reset), .Write(Write), .X(decoder_2_out0), .LL(out_11[19:16]),
    .Data(Data), .L(out_12[19:16]), .R(out_13[19:16]), .R_2(out_14[19:16]));
  _4x4array u_4x4array_5 (
    .Clock(Clock), .Y(decoder_1_out16), .reset(Reset), .Write(Write), .X(decoder_2_out0), .LL(out_11[15:12]),
    .Data(Data), .L(out_12[15:12]), .R(out_13[15:12]), .R_2(out_14[15:12]));
  _4x4array u_4x4array_6 (
    .Clock(Clock), .Y(decoder_1_out20), .reset(Reset), .Write(Write), .X(decoder_2_out0), .LL(out_11[11:8]),
    .Data(Data), .L(out_12[11:8]), .R(out_13[11:8]), .R_2(out_14[11:8]));
  _4x4array u_4x4array_7 (
    .Clock(Clock), .Y(decoder_1_out24), .reset(Reset), .Write(Write), .X(decoder_2_out0), .LL(out_11[7:4]),
    .Data(Data), .L(out_12[7:4]), .R(out_13[7:4]), .R_2(out_14[7:4]));
  _4x4array u_4x4array_8 (
    .Clock(Clock), .Y(decoder_1_out28), .reset(Reset), .Write(Write), .X(decoder_2_out0), .LL(out_11[3:0]),
    .Data(Data), .L(out_12[3:0]), .R(out_13[3:0]), .R_2(out_14[3:0]));
  _4x4array u_4x4array_9 (
    .Clock(Clock), .Y(decoder_1_out0), .reset(Reset), .Write(Write), .X(decoder_2_out4), .LL(out_7[31:28]),
    .Data(Data), .L(out_8[31:28]), .R(out_9[31:28]), .R_2(out_10[31:28]));
  _4x4array u_4x4array_10 (
    .Clock(Clock), .Y(decoder_1_out4), .reset(Reset), .Write(Write), .X(decoder_2_out4), .LL(out_7[27:24]),
    .Data(Data), .L(out_8[27:24]), .R(out_9[27:24]), .R_2(out_10[27:24]));
  _4x4array u_4x4array_11 (
    .Clock(Clock), .Y(decoder_1_out8), .reset(Reset), .Write(Write), .X(decoder_2_out4), .LL(out_7[23:20]),
    .Data(Data), .L(out_8[23:20]), .R(out_9[23:20]), .R_2(out_10[23:20]));
  _4x4array u_4x4array_12 (
    .Clock(Clock), .Y(decoder_1_out12), .reset(Reset), .Write(Write), .X(decoder_2_out4), .LL(out_7[19:16]),
    .Data(Data), .L(out_8[19:16]), .R(out_9[19:16]), .R_2(out_10[19:16]));
  _4x4array u_4x4array_13 (
    .Clock(Clock), .Y(decoder_1_out16), .reset(Reset), .Write(Write), .X(decoder_2_out4), .LL(out_7[15:12]),
    .Data(Data), .L(out_8[15:12]), .R(out_9[15:12]), .R_2(out_10[15:12]));
  _4x4array u_4x4array_14 (
    .Clock(Clock), .Y(decoder_1_out20), .reset(Reset), .Write(Write), .X(decoder_2_out4), .LL(out_7[11:8]),
    .Data(Data), .L(out_8[11:8]), .R(out_9[11:8]), .R_2(out_10[11:8]));
  _4x4array u_4x4array_15 (
    .Clock(Clock), .Y(decoder_1_out24), .reset(Reset), .Write(Write), .X(decoder_2_out4), .LL(out_7[7:4]),
    .Data(Data), .L(out_8[7:4]), .R(out_9[7:4]), .R_2(out_10[7:4]));
  _4x4array u_4x4array_16 (
    .Clock(Clock), .Y(decoder_1_out28), .reset(Reset), .Write(Write), .X(decoder_2_out4), .LL(out_7[3:0]),
    .Data(Data), .L(out_8[3:0]), .R(out_9[3:0]), .R_2(out_10[3:0]));
  _4x4array u_4x4array_17 (
    .Clock(Clock), .Y(decoder_1_out0), .reset(Reset), .Write(Write), .X(decoder_2_out8), .LL(out_15[31:28]),
    .Data(Data), .L(out_16[31:28]), .R(out_17[31:28]), .R_2(out_18[31:28]));
  _4x4array u_4x4array_18 (
    .Clock(Clock), .Y(decoder_1_out4), .reset(Reset), .Write(Write), .X(decoder_2_out8), .LL(out_15[27:24]),
    .Data(Data), .L(out_16[27:24]), .R(out_17[27:24]), .R_2(out_18[27:24]));
  _4x4array u_4x4array_19 (
    .Clock(Clock), .Y(decoder_1_out8), .reset(Reset), .Write(Write), .X(decoder_2_out8), .LL(out_15[23:20]),
    .Data(Data), .L(out_16[23:20]), .R(out_17[23:20]), .R_2(out_18[23:20]));
  _4x4array u_4x4array_20 (
    .Clock(Clock), .Y(decoder_1_out12), .reset(Reset), .Write(Write), .X(decoder_2_out8), .LL(out_15[19:16]),
    .Data(Data), .L(out_16[19:16]), .R(out_17[19:16]), .R_2(out_18[19:16]));
  _4x4array u_4x4array_21 (
    .Clock(Clock), .Y(decoder_1_out16), .reset(Reset), .Write(Write), .X(decoder_2_out8), .LL(out_15[15:12]),
    .Data(Data), .L(out_16[15:12]), .R(out_17[15:12]), .R_2(out_18[15:12]));
  _4x4array u_4x4array_22 (
    .Clock(Clock), .Y(decoder_1_out20), .reset(Reset), .Write(Write), .X(decoder_2_out8), .LL(out_15[11:8]),
    .Data(Data), .L(out_16[11:8]), .R(out_17[11:8]), .R_2(out_18[11:8]));
  _4x4array u_4x4array_23 (
    .Clock(Clock), .Y(decoder_1_out24), .reset(Reset), .Write(Write), .X(decoder_2_out8), .LL(out_15[7:4]),
    .Data(Data), .L(out_16[7:4]), .R(out_17[7:4]), .R_2(out_18[7:4]));
  _4x4array u_4x4array_24 (
    .Clock(Clock), .Y(decoder_1_out28), .reset(Reset), .Write(Write), .X(decoder_2_out8), .LL(out_15[3:0]),
    .Data(Data), .L(out_16[3:0]), .R(out_17[3:0]), .R_2(out_18[3:0]));
  Decoder #(.select(5), .enable("false")) decoder_2 (
    .out0(decoder_2_out0[0]), .out1(decoder_2_out0[1]), .out2(decoder_2_out0[2]), .out3(decoder_2_out0[3]),
    .out4(decoder_2_out4[0]), .out5(decoder_2_out4[1]), .out6(decoder_2_out4[2]), .out7(decoder_2_out4[3]),
    .out8(decoder_2_out8[0]), .out9(decoder_2_out8[1]), .out10(decoder_2_out8[2]), .out11(decoder_2_out8[3]),
    .out12(decoder_2_out12[0]), .out13(decoder_2_out12[1]), .out14(decoder_2_out12[2]),
    .out15(decoder_2_out12[3]), .out16(decoder_2_out16[0]), .out17(decoder_2_out16[1]),
    .out18(decoder_2_out16[2]), .out19(decoder_2_out16[3]), .out20(decoder_2_out20[0]),
    .out21(decoder_2_out20[1]), .out22(decoder_2_out20[2]), .out23(decoder_2_out20[3]),
    .out24(decoder_2_out24[0]), .out25(decoder_2_out24[1]), .out26(decoder_2_out24[2]),
    .out27(decoder_2_out24[3]), .out28(decoder_2_out28[0]), .out29(decoder_2_out28[1]),
    .out30(decoder_2_out28[2]), .out31(decoder_2_out28[3]), .sel(in_2));
  _4x4array u_4x4array_25 (
    .Clock(Clock), .Y(decoder_1_out0), .reset(Reset), .Write(Write), .X(decoder_2_out12), .LL(out_19[31:28]),
    .Data(Data), .L(out_20[31:28]), .R(out_21[31:28]), .R_2(out_22[31:28]));
  _4x4array u_4x4array_26 (
    .Clock(Clock), .Y(decoder_1_out4), .reset(Reset), .Write(Write), .X(decoder_2_out12), .LL(out_19[27:24]),
    .Data(Data), .L(out_20[27:24]), .R(out_21[27:24]), .R_2(out_22[27:24]));
  _4x4array u_4x4array_27 (
    .Clock(Clock), .Y(decoder_1_out8), .reset(Reset), .Write(Write), .X(decoder_2_out12), .LL(out_19[23:20]),
    .Data(Data), .L(out_20[23:20]), .R(out_21[23:20]), .R_2(out_22[23:20]));
  _4x4array u_4x4array_28 (
    .Clock(Clock), .Y(decoder_1_out12), .reset(Reset), .Write(Write), .X(decoder_2_out12),
    .LL(out_19[19:16]), .Data(Data), .L(out_20[19:16]), .R(out_21[19:16]), .R_2(out_22[19:16]));
  _4x4array u_4x4array_29 (
    .Clock(Clock), .Y(decoder_1_out16), .reset(Reset), .Write(Write), .X(decoder_2_out12),
    .LL(out_19[15:12]), .Data(Data), .L(out_20[15:12]), .R(out_21[15:12]), .R_2(out_22[15:12]));
  _4x4array u_4x4array_30 (
    .Clock(Clock), .Y(decoder_1_out20), .reset(Reset), .Write(Write), .X(decoder_2_out12), .LL(out_19[11:8]),
    .Data(Data), .L(out_20[11:8]), .R(out_21[11:8]), .R_2(out_22[11:8]));
  _4x4array u_4x4array_31 (
    .Clock(Clock), .Y(decoder_1_out24), .reset(Reset), .Write(Write), .X(decoder_2_out12), .LL(out_19[7:4]),
    .Data(Data), .L(out_20[7:4]), .R(out_21[7:4]), .R_2(out_22[7:4]));
  _4x4array u_4x4array_32 (
    .Clock(Clock), .Y(decoder_1_out28), .reset(Reset), .Write(Write), .X(decoder_2_out12), .LL(out_19[3:0]),
    .Data(Data), .L(out_20[3:0]), .R(out_21[3:0]), .R_2(out_22[3:0]));
  _4x4array u_4x4array_33 (
    .Clock(Clock), .Y(decoder_1_out0), .reset(Reset), .Write(Write), .X(decoder_2_out16), .LL(out_23[31:28]),
    .Data(Data), .L(out_24[31:28]), .R(out_25[31:28]), .R_2(out_26[31:28]));
  _4x4array u_4x4array_34 (
    .Clock(Clock), .Y(decoder_1_out4), .reset(Reset), .Write(Write), .X(decoder_2_out16), .LL(out_23[27:24]),
    .Data(Data), .L(out_24[27:24]), .R(out_25[27:24]), .R_2(out_26[27:24]));
  _4x4array u_4x4array_35 (
    .Clock(Clock), .Y(decoder_1_out8), .reset(Reset), .Write(Write), .X(decoder_2_out16), .LL(out_23[23:20]),
    .Data(Data), .L(out_24[23:20]), .R(out_25[23:20]), .R_2(out_26[23:20]));
  _4x4array u_4x4array_36 (
    .Clock(Clock), .Y(decoder_1_out12), .reset(Reset), .Write(Write), .X(decoder_2_out16),
    .LL(out_23[19:16]), .Data(Data), .L(out_24[19:16]), .R(out_25[19:16]), .R_2(out_26[19:16]));
  _4x4array u_4x4array_37 (
    .Clock(Clock), .Y(decoder_1_out16), .reset(Reset), .Write(Write), .X(decoder_2_out16),
    .LL(out_23[15:12]), .Data(Data), .L(out_24[15:12]), .R(out_25[15:12]), .R_2(out_26[15:12]));
  _4x4array u_4x4array_38 (
    .Clock(Clock), .Y(decoder_1_out20), .reset(Reset), .Write(Write), .X(decoder_2_out16), .LL(out_23[11:8]),
    .Data(Data), .L(out_24[11:8]), .R(out_25[11:8]), .R_2(out_26[11:8]));
  _4x4array u_4x4array_39 (
    .Clock(Clock), .Y(decoder_1_out24), .reset(Reset), .Write(Write), .X(decoder_2_out16), .LL(out_23[7:4]),
    .Data(Data), .L(out_24[7:4]), .R(out_25[7:4]), .R_2(out_26[7:4]));
  _4x4array u_4x4array_40 (
    .Clock(Clock), .Y(decoder_1_out28), .reset(Reset), .Write(Write), .X(decoder_2_out16), .LL(out_23[3:0]),
    .Data(Data), .L(out_24[3:0]), .R(out_25[3:0]), .R_2(out_26[3:0]));
  _4x4array u_4x4array_41 (
    .Clock(Clock), .Y(decoder_1_out0), .reset(Reset), .Write(Write), .X(decoder_2_out20), .LL(out_27[31:28]),
    .Data(Data), .L(out_28[31:28]), .R(out_29[31:28]), .R_2(out_30[31:28]));
  _4x4array u_4x4array_42 (
    .Clock(Clock), .Y(decoder_1_out4), .reset(Reset), .Write(Write), .X(decoder_2_out20), .LL(out_27[27:24]),
    .Data(Data), .L(out_28[27:24]), .R(out_29[27:24]), .R_2(out_30[27:24]));
  _4x4array u_4x4array_43 (
    .Clock(Clock), .Y(decoder_1_out8), .reset(Reset), .Write(Write), .X(decoder_2_out20), .LL(out_27[23:20]),
    .Data(Data), .L(out_28[23:20]), .R(out_29[23:20]), .R_2(out_30[23:20]));
  _4x4array u_4x4array_44 (
    .Clock(Clock), .Y(decoder_1_out12), .reset(Reset), .Write(Write), .X(decoder_2_out20),
    .LL(out_27[19:16]), .Data(Data), .L(out_28[19:16]), .R(out_29[19:16]), .R_2(out_30[19:16]));
  _4x4array u_4x4array_45 (
    .Clock(Clock), .Y(decoder_1_out16), .reset(Reset), .Write(Write), .X(decoder_2_out20),
    .LL(out_27[15:12]), .Data(Data), .L(out_28[15:12]), .R(out_29[15:12]), .R_2(out_30[15:12]));
  _4x4array u_4x4array_46 (
    .Clock(Clock), .Y(decoder_1_out20), .reset(Reset), .Write(Write), .X(decoder_2_out20), .LL(out_27[11:8]),
    .Data(Data), .L(out_28[11:8]), .R(out_29[11:8]), .R_2(out_30[11:8]));
  _4x4array u_4x4array_47 (
    .Clock(Clock), .Y(decoder_1_out24), .reset(Reset), .Write(Write), .X(decoder_2_out20), .LL(out_27[7:4]),
    .Data(Data), .L(out_28[7:4]), .R(out_29[7:4]), .R_2(out_30[7:4]));
  _4x4array u_4x4array_48 (
    .Clock(Clock), .Y(decoder_1_out28), .reset(Reset), .Write(Write), .X(decoder_2_out20), .LL(out_27[3:0]),
    .Data(Data), .L(out_28[3:0]), .R(out_29[3:0]), .R_2(out_30[3:0]));
  _4x4array u_4x4array_49 (
    .Clock(Clock), .Y(decoder_1_out0), .reset(Reset), .Write(Write), .X(decoder_2_out24), .LL(out_31[31:28]),
    .Data(Data), .L(out_32[31:28]), .R(out_33[31:28]), .R_2(out_34[31:28]));
  _4x4array u_4x4array_50 (
    .Clock(Clock), .Y(decoder_1_out4), .reset(Reset), .Write(Write), .X(decoder_2_out24), .LL(out_31[27:24]),
    .Data(Data), .L(out_32[27:24]), .R(out_33[27:24]), .R_2(out_34[27:24]));
  _4x4array u_4x4array_51 (
    .Clock(Clock), .Y(decoder_1_out8), .reset(Reset), .Write(Write), .X(decoder_2_out24), .LL(out_31[23:20]),
    .Data(Data), .L(out_32[23:20]), .R(out_33[23:20]), .R_2(out_34[23:20]));
  _4x4array u_4x4array_52 (
    .Clock(Clock), .Y(decoder_1_out12), .reset(Reset), .Write(Write), .X(decoder_2_out24),
    .LL(out_31[19:16]), .Data(Data), .L(out_32[19:16]), .R(out_33[19:16]), .R_2(out_34[19:16]));
  _4x4array u_4x4array_53 (
    .Clock(Clock), .Y(decoder_1_out16), .reset(Reset), .Write(Write), .X(decoder_2_out24),
    .LL(out_31[15:12]), .Data(Data), .L(out_32[15:12]), .R(out_33[15:12]), .R_2(out_34[15:12]));
  _4x4array u_4x4array_54 (
    .Clock(Clock), .Y(decoder_1_out20), .reset(Reset), .Write(Write), .X(decoder_2_out24), .LL(out_31[11:8]),
    .Data(Data), .L(out_32[11:8]), .R(out_33[11:8]), .R_2(out_34[11:8]));
  _4x4array u_4x4array_55 (
    .Clock(Clock), .Y(decoder_1_out24), .reset(Reset), .Write(Write), .X(decoder_2_out24), .LL(out_31[7:4]),
    .Data(Data), .L(out_32[7:4]), .R(out_33[7:4]), .R_2(out_34[7:4]));
  _4x4array u_4x4array_56 (
    .Clock(Clock), .Y(decoder_1_out28), .reset(Reset), .Write(Write), .X(decoder_2_out24), .LL(out_31[3:0]),
    .Data(Data), .L(out_32[3:0]), .R(out_33[3:0]), .R_2(out_34[3:0]));
  _4x4array u_4x4array_57 (
    .Clock(Clock), .Y(decoder_1_out0), .reset(Reset), .Write(Write), .X(decoder_2_out28), .LL(out_35[31:28]),
    .Data(Data), .L(out_36[31:28]), .R(out_37[31:28]), .R_2(out_38[31:28]));
  _4x4array u_4x4array_58 (
    .Clock(Clock), .Y(decoder_1_out4), .reset(Reset), .Write(Write), .X(decoder_2_out28), .LL(out_35[27:24]),
    .Data(Data), .L(out_36[27:24]), .R(out_37[27:24]), .R_2(out_38[27:24]));
  _4x4array u_4x4array_59 (
    .Clock(Clock), .Y(decoder_1_out8), .reset(Reset), .Write(Write), .X(decoder_2_out28), .LL(out_35[23:20]),
    .Data(Data), .L(out_36[23:20]), .R(out_37[23:20]), .R_2(out_38[23:20]));
  _4x4array u_4x4array_60 (
    .Clock(Clock), .Y(decoder_1_out12), .reset(Reset), .Write(Write), .X(decoder_2_out28),
    .LL(out_35[19:16]), .Data(Data), .L(out_36[19:16]), .R(out_37[19:16]), .R_2(out_38[19:16]));
  _4x4array u_4x4array_61 (
    .Clock(Clock), .Y(decoder_1_out16), .reset(Reset), .Write(Write), .X(decoder_2_out28),
    .LL(out_35[15:12]), .Data(Data), .L(out_36[15:12]), .R(out_37[15:12]), .R_2(out_38[15:12]));
  _4x4array u_4x4array_62 (
    .Clock(Clock), .Y(decoder_1_out20), .reset(Reset), .Write(Write), .X(decoder_2_out28), .LL(out_35[11:8]),
    .Data(Data), .L(out_36[11:8]), .R(out_37[11:8]), .R_2(out_38[11:8]));
  _4x4array u_4x4array_63 (
    .Clock(Clock), .Y(decoder_1_out24), .reset(Reset), .Write(Write), .X(decoder_2_out28), .LL(out_35[7:4]),
    .Data(Data), .L(out_36[7:4]), .R(out_37[7:4]), .R_2(out_38[7:4]));
  _4x4array u_4x4array_64 (
    .Clock(Clock), .Y(decoder_1_out28), .reset(Reset), .Write(Write), .X(decoder_2_out28), .LL(out_35[3:0]),
    .Data(Data), .L(out_36[3:0]), .R(out_37[3:0]), .R_2(out_38[3:0]));
  _4x4array u_4x4array_65 (
    .Y(undriven), .reset(undriven_10), .Write(undriven_19), .X(undriven_9), .LL(n4x4array_65_ll),
    .Data(undriven_18), .L(n4x4array_65_l), .R(n4x4array_65_r), .R_2(n4x4array_65_r_2));  // open: Clock
  _4x4array u_4x4array_66 (
    .Y(undriven_2), .reset(undriven_11), .Write(undriven_21), .X(undriven_9), .LL(n4x4array_66_ll),
    .Data(undriven_20), .L(n4x4array_66_l), .R(n4x4array_66_r), .R_2(n4x4array_66_r_2));  // open: Clock
  _4x4array u_4x4array_67 (
    .Y(undriven_3), .reset(undriven_12), .Write(undriven_23), .X(undriven_9), .LL(n4x4array_67_ll),
    .Data(undriven_22), .L(n4x4array_67_l), .R(n4x4array_67_r), .R_2(n4x4array_67_r_2));  // open: Clock
  _4x4array u_4x4array_68 (
    .Y(undriven_4), .reset(undriven_13), .Write(undriven_25), .X(undriven_9), .LL(n4x4array_68_ll),
    .Data(undriven_24), .L(n4x4array_68_l), .R(n4x4array_68_r), .R_2(n4x4array_68_r_2));  // open: Clock
  _4x4array u_4x4array_69 (
    .Y(undriven_5), .reset(undriven_14), .Write(undriven_27), .X(undriven_9), .LL(n4x4array_69_ll),
    .Data(undriven_26), .L(n4x4array_69_l), .R(n4x4array_69_r), .R_2(n4x4array_69_r_2));  // open: Clock
  _4x4array u_4x4array_70 (
    .Y(undriven_6), .reset(undriven_15), .Write(undriven_29), .X(undriven_9), .LL(n4x4array_70_ll),
    .Data(undriven_28), .L(n4x4array_70_l), .R(n4x4array_70_r), .R_2(n4x4array_70_r_2));  // open: Clock
  _4x4array u_4x4array_71 (
    .Y(undriven_7), .reset(undriven_16), .Write(undriven_31), .X(undriven_9), .LL(n4x4array_71_ll),
    .Data(undriven_30), .L(n4x4array_71_l), .R(n4x4array_71_r), .R_2(n4x4array_71_r_2));  // open: Clock
  _4x4array u_4x4array_72 (
    .Y(undriven_8), .reset(undriven_17), .Write(undriven_33), .X(undriven_9), .LL(n4x4array_72_ll),
    .Data(undriven_32), .L(n4x4array_72_l), .R(n4x4array_72_r), .R_2(n4x4array_72_r_2));  // open: Clock

  // Other names for the same wires on the sheet: _4_1[31:0] = out_19; _4_2[31:0] = out_20; _4_3[31:0] = out_21;
  //   _4_4[31:0] = out_22; _5_1[31:0] = out_23; _5_2[31:0] = out_24; _5_3[31:0] = out_25; _5_4[31:0] = out_26
endmodule

module _4x4array (
  input  Write,
  input  reset,
  input  [3:0] X,
  input  Clock,
  input  Data,
  input  [3:0] Y,
  output [3:0] LL,
  output [3:0] L,
  output [3:0] R,
  output [3:0] R_2
);

  wire and_1_out, and_2_out, and_3_out, and_4_out, and_5_out, and_6_out, and_7_out, and_8_out, and_9_out,
       and_10_out, and_11_out, and_12_out, and_13_out, and_14_out, and_15_out, and_16_out, and_17_out,
       and_18_out, and_19_out, and_20_out, and_21_out, and_22_out, and_23_out, and_24_out, and_25_out,
       and_26_out, and_27_out, and_28_out, and_29_out, and_30_out, and_31_out, and_32_out, and_33_out,
       and_34_out, and_35_out, and_36_out, and_37_out, register_17_q, transistor_1_out, undriven, undriven_2,
       undriven_3, undriven_4, undriven_5, undriven_6, undriven_7, undriven_8;

  and and_1 (and_1_out, Y[0], X[0]);
  and and_2 (and_2_out, and_1_out, Write);
  and and_3 (and_3_out, Y[1], X[0]);
  and and_4 (and_4_out, and_3_out, Write);
  and and_5 (and_5_out, Y[2], X[0]);
  and and_6 (and_6_out, and_5_out, Write);
  and and_7 (and_7_out, Y[3], X[0]);
  and and_8 (and_8_out, and_7_out, Write);
  LED led_1 (.in(LL[3]));
  Register #(.width(1)) register_1 (.D(Data), .en(and_2_out), .Q(LL[3]), .clk(Clock), .clr(reset));
  LED led_2 (.in(LL[2]));
  Register #(.width(1)) register_2 (.D(Data), .en(and_4_out), .Q(LL[2]), .clk(Clock), .clr(reset));
  LED led_3 (.in(LL[1]));
  Register #(.width(1)) register_3 (.D(Data), .en(and_6_out), .Q(LL[1]), .clk(Clock), .clr(reset));
  LED led_4 (.in(LL[0]));
  Register #(.width(1)) register_4 (.D(Data), .en(and_8_out), .Q(LL[0]), .clk(Clock), .clr(reset));
  and and_9 (and_9_out, Y[0], X[1]);
  and and_10 (and_10_out, and_9_out, Write);
  and and_11 (and_11_out, Y[1], X[1]);
  and and_12 (and_12_out, and_11_out, Write);
  and and_13 (and_13_out, Y[2], X[1]);
  and and_14 (and_14_out, and_13_out, Write);
  and and_15 (and_15_out, Y[3], X[1]);
  and and_16 (and_16_out, and_15_out, Write);
  Register #(.width(1)) register_5 (.D(Data), .en(and_10_out), .Q(L[3]), .clk(Clock), .clr(reset));
  LED led_5 (.in(L[3]));
  Register #(.width(1)) register_6 (.D(Data), .en(and_12_out), .Q(L[2]), .clk(Clock), .clr(reset));
  LED led_6 (.in(L[2]));
  Register #(.width(1)) register_7 (.D(Data), .en(and_14_out), .Q(L[1]), .clk(Clock), .clr(reset));
  LED led_7 (.in(L[1]));
  LED led_8 (.in(L[0]));
  Register #(.width(1)) register_8 (.D(Data), .en(and_16_out), .Q(L[0]), .clk(Clock), .clr(reset));
  and and_17 (and_17_out, Y[0], X[2]);
  and and_18 (and_18_out, Y[1], X[2]);
  and and_19 (and_19_out, Y[2], X[2]);
  and and_20 (and_20_out, Y[3], X[2]);
  LED led_9 (.in(R[3]));
  Register #(.width(1)) register_9 (.D(Data), .en(and_21_out), .Q(R[3]), .clk(Clock), .clr(reset));
  and and_21 (and_21_out, and_17_out, Write);
  Register #(.width(1)) register_10 (.D(Data), .en(and_22_out), .Q(R[2]), .clk(Clock), .clr(reset));
  LED led_10 (.in(R[2]));
  and and_22 (and_22_out, and_18_out, Write);
  Register #(.width(1)) register_11 (.D(Data), .en(and_23_out), .Q(R[1]), .clk(Clock), .clr(reset));
  LED led_11 (.in(R[1]));
  and and_23 (and_23_out, and_19_out, Write);
  LED led_12 (.in(R[0]));
  Register #(.width(1)) register_12 (.D(Data), .en(and_24_out), .Q(R[0]), .clk(Clock), .clr(reset));
  and and_24 (and_24_out, and_20_out, Write);
  and and_25 (and_25_out, Y[0], X[3]);
  and and_26 (and_26_out, and_25_out, Write);
  and and_27 (and_27_out, Y[1], X[3]);
  and and_28 (and_28_out, and_27_out, Write);
  and and_29 (and_29_out, Y[2], X[3]);
  and and_30 (and_30_out, and_29_out, Write);
  and and_31 (and_31_out, Y[3], X[3]);
  and and_32 (and_32_out, and_31_out, Write);
  LED led_13 (.in(R_2[3]));
  Register #(.width(1)) register_13 (.D(Data), .en(and_26_out), .Q(R_2[3]), .clk(Clock), .clr(reset));
  LED led_14 (.in(R_2[2]));
  Register #(.width(1)) register_14 (.D(Data), .en(and_28_out), .Q(R_2[2]), .clk(Clock), .clr(reset));
  LED led_15 (.in(R_2[1]));
  Register #(.width(1)) register_15 (.D(Data), .en(and_30_out), .Q(R_2[1]), .clk(Clock), .clr(reset));
  LED led_16 (.in(R_2[0]));
  Register #(.width(1)) register_16 (.D(Data), .en(and_32_out), .Q(R_2[0]), .clk(Clock), .clr(reset));
  and and_33 (and_33_out, undriven_3, undriven_2);
  and and_34 (and_34_out, and_33_out, undriven);
  and and_35 (and_35_out, and_33_out, register_17_q);
  Register #(.width(1)) register_17 (.D(undriven_6), .Q(register_17_q), .clk(and_36_out));  // open: en, clr
  and and_36 (and_36_out, and_34_out, undriven_5);
  Transistor #(.\type ("n")) transistor_1 (.in(undriven_8), .out(transistor_1_out), .gate(and_37_out));
  and and_37 (and_37_out, undriven_4, undriven_7);
endmodule

module test (
  input  A,
  input  c,
  input  add_sub,
  input  b,
  input  in_5,
  input  in_6,
  input  in_7,
  input  in_8,
  input  in_9,
  input  in_10,
  input  in_11,
  input  in_12,
  input  in_13,
  input  in_14,
  input  in_15,
  output c_out,
  output c_out_2,
  output Data_Out,
  output out_19,
  output Data_Out_2,
  output out_21,
  output Data_Out_3,
  output out_23
);

  wire and_1_out, and_3_out, and_4_out, and_5_out, and_6_out, and_7_out, and_8_out, and_9_out, and_10_out,
       button_1_out, button_2_out, button_3_out, button_4_out, button_5_out, button_6_out, button_7_out,
       nand_1_out, nand_2_out, nand_5_out, nand_6_out, nand_7_out, nand_8_out, nand_11_out, nand_12_out,
       nand_13_out, nand_14_out, not_1_out, not_2_out, not_3_out, not_4_out, not_5_out, not_6_out, not_7_out,
       not_8_out, not_9_out, not_10_out, not_11_out, not_12_out, not_13_out, not_14_out, not_15_out,
       not_16_out, not_17_out, not_18_out, not_19_out, not_20_out, or_1_out, register_2_q, register_3_q,
       register_4_q, register_5_q, register_6_q, register_7_q, register_8_q, transistor_1_out, undriven,
       undriven_2, undriven_3, undriven_4, xor_1_out, xor_2_out, xor_3_out, xor_4_out, xor_5_out, xor_6_out,
       xor_7_out, xor_8_out, xor_9_out, xxx;

  not not_1 (not_1_out, not_2_out);
  not not_2 (not_2_out, not_3_out);
  not not_3 (not_3_out, in_8);
  not not_4 (not_4_out, not_5_out);
  not not_5 (not_5_out, in_10);
  not not_6 (not_6_out, undriven);
  Transistor #(.gate("br")) transistor_1 (.in(not_1_out), .out(transistor_1_out), .gate(button_1_out));
  Transistor #(.\type ("n"), .gate("br")) transistor_2 (.in(button_1_out), .out(transistor_1_out), .gate(button_1_out));
  Button button_1 (.out(button_1_out));
  xor xor_1 (xor_1_out, in_10, not_4_out);
  not not_7 (not_7_out, not_8_out);
  not not_8 (not_8_out, not_6_out);
  and and_1 (and_1_out, in_8, transistor_1_out);
  and and_2 (xxx, undriven, not_7_out);
  Register #(.width(1)) register_1 (.D(xxx), .clk(xxx));  // open: en, Q, clr
  LED led_1 (.in(xxx));
  nand nand_1 (nand_1_out, and_1_out, undriven_2);
  nand nand_2 (nand_2_out, nand_1_out, undriven_2);
  or or_1 (or_1_out, out_19, in_6);
  nand nand_3 (Data_Out_2, nand_1_out, out_21);
  nand nand_4 (out_21, Data_Out_2, nand_2_out);
  nand nand_5 (nand_5_out, or_1_out, xxx);
  nand nand_6 (nand_6_out, nand_5_out, xxx);
  Register #(.width(1), .trigger("high")) register_2 (
    .D(xxx), .Q(register_2_q), .clk(xxx), .clr(button_2_out));  // open: en
  LED led_2 (.in(register_2_q));
  Button button_2 (.out(button_2_out));
  not not_9 (not_9_out, in_15);
  not not_10 (not_10_out, undriven_3);
  not not_11 (not_11_out, not_10_out);
  nand nand_7 (nand_7_out, in_14, not_9_out);
  nand nand_8 (nand_8_out, nand_7_out, not_9_out);
  not not_12 (not_12_out, not_9_out);
  nand nand_9 (Data_Out, nand_5_out, out_19);
  nand nand_10 (out_19, Data_Out, nand_6_out);
  and and_3 (and_3_out, ~undriven_3, not_13_out);  // AND_Gate
  not not_13 (not_13_out, not_11_out);
  Register #(.width(1)) register_3 (.Q(register_3_q), .clk(xxx));  // open: D, en, clr
  not not_14 (not_14_out, and_3_out);
  Button button_3 (.out(button_3_out));
  Register #(.width(1)) register_4 (
    .D(undriven_4), .Q(register_4_q), .clk(undriven_4), .clr(button_4_out));  // open: en
  LED led_3 (.in(register_4_q));
  Button button_4 (.out(button_4_out));
  nand nand_11 (nand_11_out, nand_7_out, nand_12_out);
  nand nand_12 (nand_12_out, nand_11_out, nand_8_out);
  Register #(.width(1)) register_5 (
    .D(not_14_out), .Q(register_5_q), .clk(not_14_out), .clr(button_3_out));  // open: en
  LED led_4 (.in(register_5_q));
  nand nand_13 (nand_13_out, nand_11_out, not_12_out);
  nand nand_14 (nand_14_out, nand_13_out, not_12_out);
  nand nand_15 (Data_Out_3, nand_13_out, out_23);
  nand nand_16 (out_23, Data_Out_3, nand_14_out);
  xor xor_2 (xor_2_out, A, register_3_q);
  xor xor_3 (xor_3_out, A, add_sub);
  xor xor_4 (xor_4_out, b, in_5);
  xor xor_5 (xor_5_out, b, add_sub);
  and and_4 (and_4_out, register_3_q, xor_3_out);
  xor xor_6 (xor_6_out, xor_2_out, add_sub);
  and and_5 (and_5_out, in_5, xor_5_out);
  xor xor_7 (xor_7_out, xor_2_out, c);
  and and_6 (and_6_out, xor_6_out, c);
  xor xor_8 (xor_8_out, xor_4_out, c_out);
  xor xor_9 (xor_9_out, xor_4_out, add_sub);
  and and_7 (and_7_out, xor_9_out, c_out);
  or or_2 (c_out, and_4_out, and_6_out);
  or or_3 (c_out_2, and_5_out, and_7_out);
  not not_15 (not_15_out, in_7);
  not not_16 (not_16_out, in_9);
  not not_17 (not_17_out, in_13);
  and and_8 (and_8_out, in_7, not_18_out);
  not not_18 (not_18_out, in_7);
  not not_19 (not_19_out, in_7);
  and and_9 (and_9_out, not_19_out, not_20_out);
  not not_20 (not_20_out, not_15_out);
  and and_10 (and_10_out, in_9, in_11, not_16_out, not_17_out);
  LED led_5 (.in(register_6_q));
  Register #(.width(1)) register_6 (.D(and_8_out), .Q(register_6_q), .clk(and_8_out), .clr(button_5_out));  // open: en
  Button button_5 (.out(button_5_out));
  Register #(.width(1)) register_7 (.D(and_9_out), .Q(register_7_q), .clk(and_9_out), .clr(button_6_out));  // open: en
  LED led_6 (.in(register_7_q));
  Button button_6 (.out(button_6_out));
  Register #(.width(1)) register_8 (
    .D(and_10_out), .Q(register_8_q), .clk(and_10_out), .clr(button_7_out));  // open: en
  Button button_7 (.out(button_7_out));
  LED led_7 (.in(register_8_q));

  // Notes on the sheet:
  //   b
endmodule
